// Logisim project 8BitCPU.circ as structural Verilog: 32 circuits, main circuit 8-Bit Processor
module _8_Bit_Processor (
  input  Reset,
  input  Reset_RAM,
  input  Program,
  output out_4
);

  wire and_1_out, clock_1_out, instruction_decoder_1_ai, instruction_decoder_1_alu_sel_1,
       instruction_decoder_1_alu_sel_2, instruction_decoder_1_alu_sel_3, instruction_decoder_1_ao,
       instruction_decoder_1_bi, instruction_decoder_1_bo, instruction_decoder_1_ce,
       instruction_decoder_1_ci, instruction_decoder_1_co, instruction_decoder_1_eo,
       instruction_decoder_1_fi, instruction_decoder_1_hlt, instruction_decoder_1_ii,
       instruction_decoder_1_ir, instruction_decoder_1_jp, instruction_decoder_1_mi,
       instruction_decoder_1_oi, instruction_decoder_1_rr, instruction_decoder_1_rw,
       instruction_decoder_1_s1, instruction_decoder_1_s2, instruction_decoder_1_s3,
       instruction_decoder_1_s4, instruction_decoder_1_s5, instruction_decoder_1_s6,
       instruction_decoder_1_s7, instruction_decoder_1_s8, n4_bit_register_1_q0, n4_bit_register_1_q1,
       n4_bit_register_1_q2, n4_bit_register_1_q3, n4_bit_register_1_s0, n4_bit_register_1_s1,
       n4_bit_register_1_s2, n4_bit_register_1_s3, n8_bit_7_segment_decoder_1_a1,
       n8_bit_7_segment_decoder_1_a2, n8_bit_7_segment_decoder_1_a3, n8_bit_7_segment_decoder_1_b1,
       n8_bit_7_segment_decoder_1_b2, n8_bit_7_segment_decoder_1_b3, n8_bit_7_segment_decoder_1_c1,
       n8_bit_7_segment_decoder_1_c2, n8_bit_7_segment_decoder_1_c3, n8_bit_7_segment_decoder_1_d1,
       n8_bit_7_segment_decoder_1_d2, n8_bit_7_segment_decoder_1_d3, n8_bit_7_segment_decoder_1_e1,
       n8_bit_7_segment_decoder_1_e2, n8_bit_7_segment_decoder_1_e3, n8_bit_7_segment_decoder_1_f1,
       n8_bit_7_segment_decoder_1_f2, n8_bit_7_segment_decoder_1_f3, n8_bit_7_segment_decoder_1_g1,
       n8_bit_7_segment_decoder_1_g2, n8_bit_7_segment_decoder_1_g3, n8_bit_alu_1_carry,
       n8_bit_alu_1_negative, n8_bit_alu_1_overflow, n8_bit_alu_1_s0, n8_bit_alu_1_s1_2, n8_bit_alu_1_s2_2,
       n8_bit_alu_1_s3_2, n8_bit_alu_1_s4, n8_bit_alu_1_s5, n8_bit_alu_1_s6, n8_bit_alu_1_s7,
       n8_bit_alu_1_zero, n8_bit_counter_1_d8, n8_bit_counter_1_s1, n8_bit_counter_1_s2, n8_bit_counter_1_s3,
       n8_bit_counter_1_s4, n8_bit_counter_1_s5, n8_bit_counter_1_s6, n8_bit_counter_1_s7,
       n8_bit_register_1_q0, n8_bit_register_1_q1, n8_bit_register_1_q2, n8_bit_register_1_q3,
       n8_bit_register_1_q4, n8_bit_register_1_q5, n8_bit_register_1_q6, n8_bit_register_1_q7,
       n8_bit_register_1_s0, n8_bit_register_1_s1, n8_bit_register_1_s2, n8_bit_register_1_s3,
       n8_bit_register_1_s4, n8_bit_register_1_s5, n8_bit_register_1_s6, n8_bit_register_1_s7,
       n8_bit_register_2_q0, n8_bit_register_2_q1, n8_bit_register_2_q2, n8_bit_register_2_q3,
       n8_bit_register_2_q4, n8_bit_register_2_s0, n8_bit_register_2_s1, n8_bit_register_2_s2,
       n8_bit_register_2_s3, n8_bit_register_2_s4, n8_bit_register_2_s5, n8_bit_register_2_s6,
       n8_bit_register_2_s7, n8_bit_register_3_s0, n8_bit_register_3_s1, n8_bit_register_3_s2,
       n8_bit_register_3_s3, n8_bit_register_3_s4, n8_bit_register_3_s5, n8_bit_register_3_s6,
       n8_bit_register_3_s7, n8_bit_register_4_q0, n8_bit_register_4_q1, n8_bit_register_4_q2,
       n8_bit_register_4_q3, n8_bit_register_4_q4, n8_bit_register_4_q5, n8_bit_register_4_q6,
       n8_bit_register_4_q7, n8_bit_register_5_s0, n8_bit_register_5_s1, n8_bit_register_5_s2,
       n8_bit_register_5_s3, n8_bit_register_5_s4, n8_bit_register_5_s5, n8_bit_register_5_s6,
       n8_bit_register_5_s7, or_1_out, or_2_out, program_loader_1_address_write, program_loader_1_data_write;
  wire [3:0] n8_bit_register_4_s0, n8_bit_register_4_s4, n256_byte_sram_1_s1, n256_byte_sram_1_s5;
  wire [7:0] program_loader_1_rom_address, rom_1_data;

  _8_Bit_Register u_8_bit_register_1 (
    .Clock(clock_1_out), .Load(instruction_decoder_1_ai), .Reset(Reset), .Enable(instruction_decoder_1_ao),
    .A0(n8_bit_register_1_q0), .A1(n8_bit_register_1_q1), .A2(n8_bit_register_1_q2),
    .A3(n8_bit_register_1_q3), .A4(n8_bit_register_1_q4), .A5(n8_bit_register_1_q5),
    .A6(n8_bit_register_1_q6), .A8(n8_bit_register_1_q7), .Q0(n8_bit_register_1_q0),
    .Q1(n8_bit_register_1_q1), .Q2(n8_bit_register_1_q2), .Q3(n8_bit_register_1_q3),
    .Q4(n8_bit_register_1_q4), .Q5(n8_bit_register_1_q5), .Q6(n8_bit_register_1_q6),
    .Q7(n8_bit_register_1_q7), .S7(n8_bit_register_1_s7), .S6(n8_bit_register_1_s6),
    .S5(n8_bit_register_1_s5), .S4(n8_bit_register_1_s4), .S3(n8_bit_register_1_s3),
    .S2(n8_bit_register_1_s2), .S1(n8_bit_register_1_s1), .S0(n8_bit_register_1_s0));
  DotMatrix #(.matrixcols(8), .matrixrows(1), .dotshape("circle")) dotmatrix_1 (
    .col0(n8_bit_register_1_s7), .col1(n8_bit_register_1_s6), .col2(n8_bit_register_1_s5),
    .col3(n8_bit_register_1_s4), .col4(n8_bit_register_1_s3), .col5(n8_bit_register_1_s2),
    .col6(n8_bit_register_1_s1), .col7(n8_bit_register_1_s0));
  DotMatrix #(.matrixcols(8), .matrixrows(1), .dotshape("circle")) dotmatrix_2 (
    .col0(instruction_decoder_1_s8), .col1(instruction_decoder_1_s7), .col2(instruction_decoder_1_s6),
    .col3(instruction_decoder_1_s5), .col4(instruction_decoder_1_s4), .col5(instruction_decoder_1_s3),
    .col6(instruction_decoder_1_s2), .col7(instruction_decoder_1_s1));
  LED led_1 (.in(instruction_decoder_1_ir));
  Instruction_Decoder instruction_decoder_1 (
    .NF(n4_bit_register_1_q2), .VF(n4_bit_register_1_q1), .ZF(n4_bit_register_1_q3),
    .CF(n4_bit_register_1_q0), .OP_0(n8_bit_register_2_q0), .OP_1(n8_bit_register_2_q1),
    .OP_2(n8_bit_register_2_q2), .OP_3(n8_bit_register_2_q3), .OP_4(n8_bit_register_2_q4), .Reset(Reset),
    .Clock(and_1_out), .FI(instruction_decoder_1_fi), .HLT(instruction_decoder_1_hlt),
    .AI(instruction_decoder_1_ai), .AO(instruction_decoder_1_ao),
    .ALU_SEL_3(instruction_decoder_1_alu_sel_3), .ALU_SEL_2(instruction_decoder_1_alu_sel_2),
    .ALU_SEL_1(instruction_decoder_1_alu_sel_1), .EO(instruction_decoder_1_eo),
    .CI(instruction_decoder_1_ci), .BI(instruction_decoder_1_bi), .BO(instruction_decoder_1_bo),
    .MI(instruction_decoder_1_mi), .RW(instruction_decoder_1_rw), .RR(instruction_decoder_1_rr),
    .II(instruction_decoder_1_ii), .IR(instruction_decoder_1_ir), .CE(instruction_decoder_1_ce),
    .CO(instruction_decoder_1_co), .JP(instruction_decoder_1_jp), .OI(instruction_decoder_1_oi),
    .S8(instruction_decoder_1_s8), .S7(instruction_decoder_1_s7), .S6(instruction_decoder_1_s6),
    .S5(instruction_decoder_1_s5), .S4(instruction_decoder_1_s4), .S3(instruction_decoder_1_s3),
    .S2(instruction_decoder_1_s2), .S1(instruction_decoder_1_s1), .PM(Program));  // open: out_13, out_14
  _4_Bit_Register u_4_bit_register_1 (
    .A0(n8_bit_alu_1_carry), .A1(n8_bit_alu_1_overflow), .A2(n8_bit_alu_1_negative), .A3(n8_bit_alu_1_zero),
    .Clock(clock_1_out), .Load(instruction_decoder_1_fi), .Reset(Reset), .S3(n4_bit_register_1_s3),
    .S2(n4_bit_register_1_s2), .S1(n4_bit_register_1_s1), .S0(n4_bit_register_1_s0), .Enable(1'b1),
    .Q0(n4_bit_register_1_q0), .Q1(n4_bit_register_1_q1), .Q2(n4_bit_register_1_q2), .Q3(n4_bit_register_1_q3));
  DotMatrix #(.matrixcols(8), .matrixrows(1), .dotshape("circle")) dotmatrix_3 (
    .col0(n8_bit_alu_1_s7), .col1(n8_bit_alu_1_s6), .col2(n8_bit_alu_1_s5), .col3(n8_bit_alu_1_s4),
    .col4(n8_bit_alu_1_s3_2), .col5(n8_bit_alu_1_s2_2), .col6(n8_bit_alu_1_s1_2), .col7(n8_bit_alu_1_s0));
  _8_Bit_ALU u_8_bit_alu_1 (
    .Alu_En(instruction_decoder_1_eo), .A0(n8_bit_register_1_s0), .A1(n8_bit_register_1_s1),
    .A2(n8_bit_register_1_s2), .A3(n8_bit_register_1_s3), .A4(n8_bit_register_1_s4),
    .A5(n8_bit_register_1_s5), .A6(n8_bit_register_1_s6), .A7(n8_bit_register_1_s7),
    .B0(n8_bit_register_3_s0), .Ci(instruction_decoder_1_ci), .B1(n8_bit_register_3_s1),
    .B2(n8_bit_register_3_s2), .B3(n8_bit_register_3_s3), .B4(n8_bit_register_3_s4),
    .B5(n8_bit_register_3_s5), .B6(n8_bit_register_3_s6), .B7(n8_bit_register_3_s7),
    .Q0(n8_bit_register_1_q0), .Q1(n8_bit_register_1_q1), .Q3(n8_bit_register_1_q3),
    .Q4(n8_bit_register_1_q4), .Q5(n8_bit_register_1_q5), .Q6(n8_bit_register_1_q6),
    .Q7(n8_bit_register_1_q7), .Carry(n8_bit_alu_1_carry), .Overflow(n8_bit_alu_1_overflow),
    .Negative(n8_bit_alu_1_negative), .Zero(n8_bit_alu_1_zero), .S3(instruction_decoder_1_alu_sel_1),
    .S2(instruction_decoder_1_alu_sel_2), .S1(instruction_decoder_1_alu_sel_3), .S7(n8_bit_alu_1_s7),
    .S6(n8_bit_alu_1_s6), .S5(n8_bit_alu_1_s5), .S4(n8_bit_alu_1_s4), .S3_2(n8_bit_alu_1_s3_2),
    .S2_2(n8_bit_alu_1_s2_2), .S1_2(n8_bit_alu_1_s1_2), .S0(n8_bit_alu_1_s0), .Q2(n8_bit_register_1_q2));
  DotMatrix #(.matrixcols(4), .matrixrows(1), .dotshape("circle")) dotmatrix_4 (
    .col0(n4_bit_register_1_s3), .col1(n4_bit_register_1_s2), .col2(n4_bit_register_1_s1),
    .col3(n4_bit_register_1_s0));
  DotMatrix #(.matrixcols(8), .matrixrows(1), .dotshape("circle")) dotmatrix_5 (
    .col0(n8_bit_register_2_s0), .col1(n8_bit_register_2_s1), .col2(n8_bit_register_2_s2),
    .col3(n8_bit_register_2_s3), .col4(n8_bit_register_2_s4), .col5(n8_bit_register_2_s5),
    .col6(n8_bit_register_2_s6), .col7(n8_bit_register_2_s7));
  _8_Bit_Register u_8_bit_register_2 (
    .Clock(and_1_out), .Load(instruction_decoder_1_ii), .Reset(Reset), .Enable(1'b1),
    .A0(n8_bit_register_1_q0), .A1(n8_bit_register_1_q1), .A2(n8_bit_register_1_q2),
    .A3(n8_bit_register_1_q3), .A4(n8_bit_register_1_q4), .A5(n8_bit_register_1_q5),
    .A6(n8_bit_register_1_q6), .A8(n8_bit_register_1_q7), .Q0(n8_bit_register_2_q0),
    .Q1(n8_bit_register_2_q1), .Q2(n8_bit_register_2_q2), .Q3(n8_bit_register_2_q3),
    .Q4(n8_bit_register_2_q4), .S7(n8_bit_register_2_s7), .S6(n8_bit_register_2_s6),
    .S5(n8_bit_register_2_s5), .S4(n8_bit_register_2_s4), .S3(n8_bit_register_2_s3),
    .S2(n8_bit_register_2_s2), .S1(n8_bit_register_2_s1), .S0(n8_bit_register_2_s0));  // open: Q5, Q6, Q7
  _8_Bit_Register u_8_bit_register_3 (
    .Clock(clock_1_out), .Load(instruction_decoder_1_bi), .Reset(Reset), .Enable(instruction_decoder_1_bo),
    .A0(n8_bit_register_1_q0), .A1(n8_bit_register_1_q1), .A2(n8_bit_register_1_q2),
    .A3(n8_bit_register_1_q3), .A4(n8_bit_register_1_q4), .A5(n8_bit_register_1_q5),
    .A6(n8_bit_register_1_q6), .A8(n8_bit_register_1_q7), .Q0(n8_bit_register_1_q0),
    .Q1(n8_bit_register_1_q1), .Q2(n8_bit_register_1_q2), .Q3(n8_bit_register_1_q3),
    .Q4(n8_bit_register_1_q4), .Q5(n8_bit_register_1_q5), .Q6(n8_bit_register_1_q6),
    .Q7(n8_bit_register_1_q7), .S7(n8_bit_register_3_s7), .S6(n8_bit_register_3_s6),
    .S5(n8_bit_register_3_s5), .S4(n8_bit_register_3_s4), .S3(n8_bit_register_3_s3),
    .S2(n8_bit_register_3_s2), .S1(n8_bit_register_3_s1), .S0(n8_bit_register_3_s0));
  DotMatrix #(.matrixcols(8), .matrixrows(1), .dotshape("circle")) dotmatrix_6 (
    .col0(n8_bit_register_3_s7), .col1(n8_bit_register_3_s6), .col2(n8_bit_register_3_s5),
    .col3(n8_bit_register_3_s4), .col4(n8_bit_register_3_s3), .col5(n8_bit_register_3_s2),
    .col6(n8_bit_register_3_s1), .col7(n8_bit_register_3_s0));
  DotMatrix #(.matrixcols(8), .matrixrows(1), .dotshape("circle")) dotmatrix_7 (
    .col0(n8_bit_counter_1_d8), .col1(n8_bit_counter_1_s7), .col2(n8_bit_counter_1_s6),
    .col3(n8_bit_counter_1_s5), .col4(n8_bit_counter_1_s4), .col5(n8_bit_counter_1_s3),
    .col6(n8_bit_counter_1_s2), .col7(n8_bit_counter_1_s1));
  _8_Bit_Register u_8_bit_register_4 (
    .Clock(clock_1_out), .Load(or_1_out), .Reset(Reset), .Enable(1'b1), .A0(n8_bit_register_1_q0),
    .A1(n8_bit_register_1_q1), .A2(n8_bit_register_1_q2), .A3(n8_bit_register_1_q3),
    .A4(n8_bit_register_1_q4), .A5(n8_bit_register_1_q5), .A6(n8_bit_register_1_q6),
    .A8(n8_bit_register_1_q7), .Q0(n8_bit_register_4_q0), .Q1(n8_bit_register_4_q1),
    .Q2(n8_bit_register_4_q2), .Q3(n8_bit_register_4_q3), .Q4(n8_bit_register_4_q4),
    .Q5(n8_bit_register_4_q5), .Q6(n8_bit_register_4_q6), .Q7(n8_bit_register_4_q7),
    .S7(n8_bit_register_4_s4[3]), .S6(n8_bit_register_4_s4[2]), .S5(n8_bit_register_4_s4[1]),
    .S4(n8_bit_register_4_s4[0]), .S3(n8_bit_register_4_s0[3]), .S2(n8_bit_register_4_s0[2]),
    .S1(n8_bit_register_4_s0[1]), .S0(n8_bit_register_4_s0[0]));
  DotMatrix #(.matrixcols(8), .matrixrows(1), .dotshape("circle")) dotmatrix_8 (
    .col0(n8_bit_register_4_s4[3]), .col1(n8_bit_register_4_s4[2]), .col2(n8_bit_register_4_s4[1]),
    .col3(n8_bit_register_4_s4[0]), .col4(n8_bit_register_4_s0[3]), .col5(n8_bit_register_4_s0[2]),
    .col6(n8_bit_register_4_s0[1]), .col7(n8_bit_register_4_s0[0]));
  Hex_Digit_Display hex_digit_display_1 (.value(n8_bit_register_4_s4));  // open: dp
  _8_Bit_Counter u_8_bit_counter_1 (
    .Enable_Out(instruction_decoder_1_co), .Enable(instruction_decoder_1_ce), .Reset(Reset),
    .Write(instruction_decoder_1_jp), .Clock(and_1_out), .Q8(n8_bit_register_1_q7),
    .Q7(n8_bit_register_1_q6), .Q6(n8_bit_register_1_q5), .Q5(n8_bit_register_1_q4),
    .Q4(n8_bit_register_1_q3), .Q3(n8_bit_register_1_q2), .Q2(n8_bit_register_1_q1),
    .Q1(n8_bit_register_1_q0), .D8(n8_bit_counter_1_d8), .S7(n8_bit_counter_1_s7), .S6(n8_bit_counter_1_s6),
    .S5(n8_bit_counter_1_s5), .S4(n8_bit_counter_1_s4), .S3(n8_bit_counter_1_s3), .S2(n8_bit_counter_1_s2),
    .S1(n8_bit_counter_1_s1), .A8(n8_bit_register_1_q7), .A7(n8_bit_register_1_q6),
    .A6(n8_bit_register_1_q5), .A5(n8_bit_register_1_q4), .A4(n8_bit_register_1_q3),
    .A3(n8_bit_register_1_q2), .A2(n8_bit_register_1_q1), .A1(n8_bit_register_1_q0));
  or or_1 (or_1_out, instruction_decoder_1_mi, program_loader_1_address_write);
  Hex_Digit_Display hex_digit_display_2 (.value(n8_bit_register_4_s0));  // open: dp
  Hex_Digit_Display hex_digit_display_3 (.value(n256_byte_sram_1_s1));  // open: dp
  Hex_Digit_Display hex_digit_display_4 (.value(n256_byte_sram_1_s5));  // open: dp
  DotMatrix #(.matrixcols(8), .matrixrows(1), .dotshape("circle")) dotmatrix_9 (
    .col0(n256_byte_sram_1_s5[3]), .col1(n256_byte_sram_1_s5[2]), .col2(n256_byte_sram_1_s5[1]),
    .col3(n256_byte_sram_1_s5[0]), .col4(n256_byte_sram_1_s1[3]), .col5(n256_byte_sram_1_s1[2]),
    .col6(n256_byte_sram_1_s1[1]), .col7(n256_byte_sram_1_s1[0]));
  _256_Byte_SRAM u_256_byte_sram_1 (
    .Read(instruction_decoder_1_rr), .Write(or_2_out), .Clear(Reset_RAM), .Clock(and_1_out),
    .A1_2(n8_bit_register_4_q0), .A2_2(n8_bit_register_4_q1), .A3_2(n8_bit_register_4_q2),
    .A4_2(n8_bit_register_4_q3), .A5_2(n8_bit_register_4_q4), .A6_2(n8_bit_register_4_q5),
    .A7_2(n8_bit_register_4_q6), .A8_2(n8_bit_register_4_q7), .S8(n256_byte_sram_1_s5[3]),
    .S7(n256_byte_sram_1_s5[2]), .S6(n256_byte_sram_1_s5[1]), .S5(n256_byte_sram_1_s5[0]),
    .S4(n256_byte_sram_1_s1[3]), .S3(n256_byte_sram_1_s1[2]), .S2(n256_byte_sram_1_s1[1]),
    .S1(n256_byte_sram_1_s1[0]), .Q8(n8_bit_register_1_q7), .Q7(n8_bit_register_1_q6),
    .Q6(n8_bit_register_1_q5), .Q5(n8_bit_register_1_q4), .Q4(n8_bit_register_1_q3),
    .Q3(n8_bit_register_1_q2), .Q2(n8_bit_register_1_q1), .Q1(n8_bit_register_1_q0),
    .A8(n8_bit_register_1_q7), .A7(n8_bit_register_1_q6), .A6(n8_bit_register_1_q5),
    .A5(n8_bit_register_1_q4), .A4(n8_bit_register_1_q3), .A3(n8_bit_register_1_q2),
    .A2(n8_bit_register_1_q1), .A1(n8_bit_register_1_q0));
  _8_Bit_Register u_8_bit_register_5 (
    .Clock(and_1_out), .Load(instruction_decoder_1_oi), .Reset(Reset), .Enable(1'b1),
    .A0(n8_bit_register_1_q0), .A1(n8_bit_register_1_q1), .A2(n8_bit_register_1_q2),
    .A3(n8_bit_register_1_q3), .A4(n8_bit_register_1_q4), .A5(n8_bit_register_1_q5),
    .A6(n8_bit_register_1_q6), .A8(n8_bit_register_1_q7), .S7(n8_bit_register_5_s7),
    .S6(n8_bit_register_5_s6), .S5(n8_bit_register_5_s5), .S4(n8_bit_register_5_s4),
    .S3(n8_bit_register_5_s3), .S2(n8_bit_register_5_s2), .S1(n8_bit_register_5_s1), .S0(n8_bit_register_5_s0));  // open: Q0, Q1, Q2, Q3, Q4, Q5, Q6, Q7
  _7_Segment_Display u_7_segment_display_1 (
    .g(n8_bit_7_segment_decoder_1_g3), .f(n8_bit_7_segment_decoder_1_f3), .a(n8_bit_7_segment_decoder_1_a3),
    .b(n8_bit_7_segment_decoder_1_b3), .e(n8_bit_7_segment_decoder_1_e3), .d(n8_bit_7_segment_decoder_1_d3),
    .c(n8_bit_7_segment_decoder_1_c3));  // open: dp
  _7_Segment_Display u_7_segment_display_2 (
    .g(n8_bit_7_segment_decoder_1_g2), .f(n8_bit_7_segment_decoder_1_f2), .a(n8_bit_7_segment_decoder_1_a2),
    .b(n8_bit_7_segment_decoder_1_b2), .e(n8_bit_7_segment_decoder_1_e2), .d(n8_bit_7_segment_decoder_1_d2),
    .c(n8_bit_7_segment_decoder_1_c2));  // open: dp
  _8_Bit_7_segment_decoder u_8_bit_7_segment_decoder_1 (
    .in_1(n8_bit_register_5_s0), .in_2(n8_bit_register_5_s1), .in_3(n8_bit_register_5_s2),
    .in_4(n8_bit_register_5_s3), .in_5(n8_bit_register_5_s4), .in_6(n8_bit_register_5_s5),
    .in_7(n8_bit_register_5_s6), .in_8(n8_bit_register_5_s7), .A1(n8_bit_7_segment_decoder_1_a1),
    .B1(n8_bit_7_segment_decoder_1_b1), .C1(n8_bit_7_segment_decoder_1_c1),
    .D1(n8_bit_7_segment_decoder_1_d1), .E1(n8_bit_7_segment_decoder_1_e1),
    .F1(n8_bit_7_segment_decoder_1_f1), .G1(n8_bit_7_segment_decoder_1_g1),
    .A2(n8_bit_7_segment_decoder_1_a2), .B2(n8_bit_7_segment_decoder_1_b2),
    .C2(n8_bit_7_segment_decoder_1_c2), .D2(n8_bit_7_segment_decoder_1_d2),
    .E2(n8_bit_7_segment_decoder_1_e2), .F2(n8_bit_7_segment_decoder_1_f2),
    .G2(n8_bit_7_segment_decoder_1_g2), .A3(n8_bit_7_segment_decoder_1_a3),
    .B3(n8_bit_7_segment_decoder_1_b3), .C3(n8_bit_7_segment_decoder_1_c3),
    .D3(n8_bit_7_segment_decoder_1_d3), .E3(n8_bit_7_segment_decoder_1_e3),
    .F3(n8_bit_7_segment_decoder_1_f3), .G3(n8_bit_7_segment_decoder_1_g3));
  _7_Segment_Display u_7_segment_display_3 (
    .g(n8_bit_7_segment_decoder_1_g1), .f(n8_bit_7_segment_decoder_1_f1), .a(n8_bit_7_segment_decoder_1_a1),
    .b(n8_bit_7_segment_decoder_1_b1), .e(n8_bit_7_segment_decoder_1_e1), .d(n8_bit_7_segment_decoder_1_d1),
    .c(n8_bit_7_segment_decoder_1_c1));  // open: dp
  or or_2 (or_2_out, instruction_decoder_1_rw, program_loader_1_data_write);
  DotMatrix #(.inputtype("row"), .matrixcols(1), .matrixrows(8), .dotshape("circle")) dotmatrix_10 (
    .row0(n8_bit_register_1_q0), .row1(n8_bit_register_1_q1), .row2(n8_bit_register_1_q2),
    .row3(n8_bit_register_1_q3), .row4(n8_bit_register_1_q4), .row5(n8_bit_register_1_q5),
    .row6(n8_bit_register_1_q6), .row7(n8_bit_register_1_q7));
  Program_Loader program_loader_1 (
    .Q1(n8_bit_register_1_q0), .Q2(n8_bit_register_1_q1), .Q3(n8_bit_register_1_q2),
    .Q4(n8_bit_register_1_q3), .Q5(n8_bit_register_1_q4), .Q6(n8_bit_register_1_q5),
    .Q7(n8_bit_register_1_q6), .Q8(n8_bit_register_1_q7), .Programming(out_4),
    .Address_Write(program_loader_1_address_write), .Data_Write(program_loader_1_data_write),
    .Enable(Program), .Reset(Reset), .ROM_Address(program_loader_1_rom_address), .ROM_Data(rom_1_data),
    .Clock(and_1_out));
  ROM rom_1 (.addr(program_loader_1_rom_address), .data(rom_1_data));  // open: sel
  Clock clock_1 (.out(clock_1_out));
  and and_1 (and_1_out, ~Reset, clock_1_out, ~instruction_decoder_1_hlt);  // AND_Gate

  // Notes on the sheet:
  //   A
  //   Register
  //   Flag
  //   Register
  //   Instruction
  //   Register
  //   B
  //   Register
  //   PC
  //   Register
  //   Memory
  //   Register
  //   RAM
  //   Out
  //   Register
  //   contents of rom_1 (hex, n*v repeats v):
  //   2 ff
endmodule

module Half_Adder (
  input  A,
  input  B,
  output Sum,
  output Carry_Out
);

  xor xor_1 (Sum, A, B);
  and and_1 (Carry_Out, A, B);
endmodule

module Full_Adder (
  input  A,
  input  B,
  input  Carry_In,
  output Sum,
  output Carry_Out
);

  wire half_adder_1_carry_out, half_adder_1_sum, half_adder_2_carry_out;

  Half_Adder half_adder_1 (.A(A), .B(B), .Sum(half_adder_1_sum), .Carry_Out(half_adder_1_carry_out));
  Half_Adder half_adder_2 (.A(half_adder_1_sum), .B(Carry_In), .Sum(Sum), .Carry_Out(half_adder_2_carry_out));
  or or_1 (Carry_Out, half_adder_1_carry_out, half_adder_2_carry_out);
endmodule

module _8_Bit_Adder (
  input  A7,
  input  A6,
  input  A5,
  input  A4,
  input  A3,
  input  A2,
  input  A1,
  input  A0,
  input  B7,
  input  B6,
  input  B5,
  input  B4,
  input  B3,
  input  B2,
  input  B1,
  input  B0,
  input  Carry_In,
  output Carry_Out,
  output Overflow,
  output Q7,
  output Q6,
  output Q5,
  output Q4,
  output Q3,
  output Q2,
  output Q1,
  output Q0
);

  wire full_adder_2_carry_out, full_adder_3_carry_out, full_adder_4_carry_out, full_adder_5_carry_out,
       full_adder_6_carry_out, full_adder_7_carry_out, full_adder_8_carry_out;

  xor xor_1 (Overflow, Carry_Out, full_adder_2_carry_out);
  Full_Adder full_adder_1 (.Carry_Out(Carry_Out), .Sum(Q7), .A(A7), .B(B7), .Carry_In(full_adder_2_carry_out));
  Full_Adder full_adder_2 (
    .Carry_Out(full_adder_2_carry_out), .Sum(Q6), .A(A6), .B(B6), .Carry_In(full_adder_3_carry_out));
  Full_Adder full_adder_3 (
    .Carry_Out(full_adder_3_carry_out), .Sum(Q5), .A(A5), .B(B5), .Carry_In(full_adder_4_carry_out));
  Full_Adder full_adder_4 (
    .Carry_Out(full_adder_4_carry_out), .Sum(Q4), .A(A4), .B(B4), .Carry_In(full_adder_5_carry_out));
  Full_Adder full_adder_5 (
    .Carry_Out(full_adder_5_carry_out), .Sum(Q3), .A(A3), .B(B3), .Carry_In(full_adder_6_carry_out));
  Full_Adder full_adder_6 (
    .Carry_Out(full_adder_6_carry_out), .Sum(Q2), .A(A2), .B(B2), .Carry_In(full_adder_7_carry_out));
  Full_Adder full_adder_7 (
    .Carry_Out(full_adder_7_carry_out), .Sum(Q1), .A(A1), .B(B1), .Carry_In(full_adder_8_carry_out));
  Full_Adder full_adder_8 (.Carry_Out(full_adder_8_carry_out), .Sum(Q0), .A(A0), .B(B0), .Carry_In(Carry_In));
endmodule

module _8_Bit_Add_Sub (
  input  B7,
  input  B6,
  input  B5,
  input  B4,
  input  B3,
  input  B2,
  input  B1,
  input  B0,
  input  Add_Sub,
  input  A7,
  input  A6,
  input  A5,
  input  A4,
  input  A3,
  input  A2,
  input  A1,
  input  A0,
  output Carry_Out,
  output Overflow,
  output Q7,
  output Q6,
  output Q5,
  output Q4,
  output Q3,
  output Q2,
  output Q1,
  output Q0
);

  wire full_adder_2_carry_out, full_adder_3_carry_out, full_adder_4_carry_out, full_adder_5_carry_out,
       full_adder_6_carry_out, full_adder_7_carry_out, full_adder_8_carry_out, xor_2_out, xor_3_out,
       xor_4_out, xor_5_out, xor_6_out, xor_7_out, xor_8_out, xor_9_out;

  xor xor_1 (Overflow, Carry_Out, full_adder_2_carry_out);
  xor xor_2 (xor_2_out, B7, Add_Sub);
  Full_Adder full_adder_1 (.Carry_Out(Carry_Out), .Sum(Q7), .A(A7), .B(xor_2_out), .Carry_In(full_adder_2_carry_out));
  xor xor_3 (xor_3_out, B6, Add_Sub);
  Full_Adder full_adder_2 (
    .Carry_Out(full_adder_2_carry_out), .Sum(Q6), .A(A6), .B(xor_3_out), .Carry_In(full_adder_3_carry_out));
  xor xor_4 (xor_4_out, B5, Add_Sub);
  Full_Adder full_adder_3 (
    .Carry_Out(full_adder_3_carry_out), .Sum(Q5), .A(A5), .B(xor_4_out), .Carry_In(full_adder_4_carry_out));
  xor xor_5 (xor_5_out, B4, Add_Sub);
  Full_Adder full_adder_4 (
    .Carry_Out(full_adder_4_carry_out), .Sum(Q4), .A(A4), .B(xor_5_out), .Carry_In(full_adder_5_carry_out));
  xor xor_6 (xor_6_out, B3, Add_Sub);
  Full_Adder full_adder_5 (
    .Carry_Out(full_adder_5_carry_out), .Sum(Q3), .A(A3), .B(xor_6_out), .Carry_In(full_adder_6_carry_out));
  xor xor_7 (xor_7_out, B2, Add_Sub);
  Full_Adder full_adder_6 (
    .Carry_Out(full_adder_6_carry_out), .Sum(Q2), .A(A2), .B(xor_7_out), .Carry_In(full_adder_8_carry_out));
  xor xor_8 (xor_8_out, B1, Add_Sub);
  xor xor_9 (xor_9_out, B0, Add_Sub);
  Full_Adder full_adder_7 (.Carry_Out(full_adder_7_carry_out), .Sum(Q0), .A(A0), .B(xor_9_out), .Carry_In(Add_Sub));
  Full_Adder full_adder_8 (
    .Carry_Out(full_adder_8_carry_out), .Sum(Q1), .A(A1), .B(xor_8_out), .Carry_In(full_adder_7_carry_out));
endmodule

module D_Latch (
  input  Enable,
  input  A,
  output Q,
  output nQ
);

  wire and_1_out, and_2_out, not_1_out;

  not not_1 (not_1_out, A);
  and and_1 (and_1_out, not_1_out, Enable);
  and and_2 (and_2_out, Enable, A);
  nor nor_1 (Q, and_1_out, nQ);
  nor nor_2 (nQ, Q, and_2_out);
endmodule

module D_Flip_Flop (
  input  Set,
  input  Clock,
  input  Data,
  input  Reset,
  output Q,
  output nQ
);

  wire nand_1_out, nand_2_out, nand_3_out, nand_4_out, not_1_out, not_2_out;

  not not_1 (not_1_out, Set);
  not not_2 (not_2_out, Reset);
  nand nand_1 (nand_1_out, not_1_out, nand_4_out, nand_2_out);
  nand nand_2 (nand_2_out, nand_1_out, Clock, not_2_out);
  nand nand_3 (nand_3_out, nand_2_out, Clock, nand_4_out);
  nand nand_4 (nand_4_out, nand_3_out, Data, not_2_out);
  nand nand_5 (Q, not_1_out, nand_2_out, nQ);
  nand nand_6 (nQ, Q, nand_3_out, not_2_out);
endmodule

module _1_Bit_Register (
  input  Clock,
  input  Load,
  input  Data,
  input  Set,
  input  Reset,
  output Q,
  output nQ
);

  wire and_1_out, and_2_out, not_1_out, or_1_out;

  not not_1 (not_1_out, Load);
  and and_1 (and_1_out, Q, not_1_out);
  and and_2 (and_2_out, Load, Data);
  or or_1 (or_1_out, and_1_out, and_2_out);
  D_Flip_Flop_part d_ff_1 (.clk(Clock), .D(or_1_out), .Q(Q), .Qn(nQ), .preset(Set), .reset(Reset));  // open: en
endmodule

module _4_Bit_Register (
  input  Clock,
  input  Load,
  input  Reset,
  input  Enable,
  input  A0,
  input  A1,
  input  A2,
  input  A3,
  output S3,
  output S2,
  output S1,
  output S0,
  output Q0,
  output Q1,
  output Q2,
  output Q3
);

  _1_Bit_Register u_1_bit_register_1 (
    .Clock(Clock), .Load(Load), .Data(A0), .Q(S0), .Set(1'b0), .Reset(Reset));  // open: nQ
  _1_Bit_Register u_1_bit_register_2 (
    .Clock(Clock), .Load(Load), .Data(A1), .Q(S1), .Set(1'b0), .Reset(Reset));  // open: nQ
  _1_Bit_Register u_1_bit_register_3 (
    .Clock(Clock), .Load(Load), .Data(A2), .Q(S2), .Set(1'b0), .Reset(Reset));  // open: nQ
  _1_Bit_Register u_1_bit_register_4 (
    .Clock(Clock), .Load(Load), .Data(A3), .Q(S3), .Set(1'b0), .Reset(Reset));  // open: nQ
  assign Q0 = Enable ? S0 : 1'bz;  // Controlled_Buffer controlled_buffer_1
  assign Q1 = Enable ? S1 : 1'bz;  // Controlled_Buffer controlled_buffer_2
  assign Q2 = Enable ? S2 : 1'bz;  // Controlled_Buffer controlled_buffer_3
  assign Q3 = Enable ? S3 : 1'bz;  // Controlled_Buffer controlled_buffer_4
endmodule

module _8_Bit_Register (
  input  Clock,
  input  Load,
  input  Reset,
  input  Enable,
  input  A0,
  input  A1,
  input  A2,
  input  A3,
  input  A4,
  input  A5,
  input  A6,
  input  A8,
  output S7,
  output S6,
  output S5,
  output S4,
  output S3,
  output S2,
  output S1,
  output S0,
  output Q0,
  output Q1,
  output Q2,
  output Q3,
  output Q4,
  output Q5,
  output Q6,
  output Q7
);

  _1_Bit_Register u_1_bit_register_1 (
    .Clock(Clock), .Load(Load), .Data(A0), .Q(S0), .Set(1'b0), .Reset(Reset));  // open: nQ
  _1_Bit_Register u_1_bit_register_2 (
    .Clock(Clock), .Load(Load), .Data(A1), .Q(S1), .Set(1'b0), .Reset(Reset));  // open: nQ
  _1_Bit_Register u_1_bit_register_3 (
    .Clock(Clock), .Load(Load), .Data(A2), .Q(S2), .Set(1'b0), .Reset(Reset));  // open: nQ
  _1_Bit_Register u_1_bit_register_4 (
    .Clock(Clock), .Load(Load), .Data(A3), .Q(S3), .Set(1'b0), .Reset(Reset));  // open: nQ
  _1_Bit_Register u_1_bit_register_5 (
    .Clock(Clock), .Load(Load), .Data(A4), .Q(S4), .Set(1'b0), .Reset(Reset));  // open: nQ
  _1_Bit_Register u_1_bit_register_6 (
    .Clock(Clock), .Load(Load), .Data(A5), .Q(S5), .Set(1'b0), .Reset(Reset));  // open: nQ
  _1_Bit_Register u_1_bit_register_7 (
    .Clock(Clock), .Load(Load), .Data(A6), .Q(S6), .Set(1'b0), .Reset(Reset));  // open: nQ
  _1_Bit_Register u_1_bit_register_8 (
    .Clock(Clock), .Load(Load), .Data(A8), .Q(S7), .Set(1'b0), .Reset(Reset));  // open: nQ
  assign Q0 = Enable ? S0 : 1'bz;  // Controlled_Buffer controlled_buffer_1
  assign Q1 = Enable ? S1 : 1'bz;  // Controlled_Buffer controlled_buffer_2
  assign Q2 = Enable ? S2 : 1'bz;  // Controlled_Buffer controlled_buffer_3
  assign Q3 = Enable ? S3 : 1'bz;  // Controlled_Buffer controlled_buffer_4
  assign Q4 = Enable ? S4 : 1'bz;  // Controlled_Buffer controlled_buffer_5
  assign Q5 = Enable ? S5 : 1'bz;  // Controlled_Buffer controlled_buffer_6
  assign Q6 = Enable ? S6 : 1'bz;  // Controlled_Buffer controlled_buffer_7
  assign Q7 = Enable ? S7 : 1'bz;  // Controlled_Buffer controlled_buffer_8
endmodule

module _4_bit_binary_decoder (
  input  A3,
  input  A2,
  input  A1,
  input  A0,
  input  Enable,
  output D0,
  output D1,
  output D2,
  output D3,
  output D4,
  output D5,
  output D6,
  output D7,
  output D8,
  output D9,
  output DA,
  output DB,
  output DC,
  output DD,
  output DE,
  output DF
);

  wire and_1_out, and_2_out, and_3_out, and_4_out, and_5_out, and_6_out, and_7_out, and_8_out, and_9_out,
       and_10_out, and_11_out, and_12_out, and_13_out, and_14_out, and_15_out, and_16_out, not_1_out,
       not_2_out, not_3_out, not_4_out;

  and and_1 (and_1_out, A0, A1, A2, A3);
  and and_2 (and_2_out, not_4_out, A1, A2, A3);
  and and_3 (and_3_out, A0, not_2_out, A2, A3);
  and and_4 (and_4_out, not_4_out, not_2_out, A2, A3);
  and and_5 (and_5_out, A0, A1, not_3_out, A3);
  and and_6 (and_6_out, A0, not_2_out, not_3_out, A3);
  and and_7 (and_7_out, not_4_out, A1, not_3_out, A3);
  and and_8 (and_8_out, not_4_out, not_2_out, not_3_out, A3);
  and and_9 (and_9_out, A0, A1, A2, not_1_out);
  and and_10 (and_10_out, not_4_out, A1, A2, not_1_out);
  and and_11 (and_11_out, A0, not_2_out, A2, not_1_out);
  and and_12 (and_12_out, not_4_out, not_2_out, A2, not_1_out);
  and and_13 (and_13_out, A0, A1, not_3_out, not_1_out);
  and and_14 (and_14_out, not_4_out, A1, not_3_out, not_1_out);
  and and_15 (and_15_out, A0, not_2_out, not_3_out, not_1_out);
  not not_1 (not_1_out, A3);
  and and_16 (and_16_out, not_4_out, not_2_out, not_3_out, not_1_out);
  not not_2 (not_2_out, A1);
  not not_3 (not_3_out, A2);
  assign D0 = Enable ? and_16_out : 1'bz;  // Controlled_Buffer controlled_buffer_1
  assign D1 = Enable ? and_15_out : 1'bz;  // Controlled_Buffer controlled_buffer_2
  assign D2 = Enable ? and_14_out : 1'bz;  // Controlled_Buffer controlled_buffer_3
  assign D3 = Enable ? and_13_out : 1'bz;  // Controlled_Buffer controlled_buffer_4
  assign D4 = Enable ? and_12_out : 1'bz;  // Controlled_Buffer controlled_buffer_5
  assign D5 = Enable ? and_11_out : 1'bz;  // Controlled_Buffer controlled_buffer_6
  assign D6 = Enable ? and_10_out : 1'bz;  // Controlled_Buffer controlled_buffer_7
  assign D7 = Enable ? and_9_out : 1'bz;  // Controlled_Buffer controlled_buffer_8
  assign D8 = Enable ? and_8_out : 1'bz;  // Controlled_Buffer controlled_buffer_9
  assign D9 = Enable ? and_6_out : 1'bz;  // Controlled_Buffer controlled_buffer_10
  assign DA = Enable ? and_7_out : 1'bz;  // Controlled_Buffer controlled_buffer_11
  assign DB = Enable ? and_5_out : 1'bz;  // Controlled_Buffer controlled_buffer_12
  assign DC = Enable ? and_4_out : 1'bz;  // Controlled_Buffer controlled_buffer_13
  assign DD = Enable ? and_3_out : 1'bz;  // Controlled_Buffer controlled_buffer_14
  assign DE = Enable ? and_2_out : 1'bz;  // Controlled_Buffer controlled_buffer_15
  assign DF = Enable ? and_1_out : 1'bz;  // Controlled_Buffer controlled_buffer_16
  not not_4 (not_4_out, A0);
endmodule

module _1_Bit_Multiplexer (
  input  A,
  input  Switch,
  input  B,
  output Q
);

  wire and_1_out, and_2_out, not_1_out;

  not not_1 (not_1_out, Switch);
  and and_1 (and_1_out, A, not_1_out);
  and and_2 (and_2_out, Switch, B);
  or or_1 (Q, and_1_out, and_2_out);
endmodule

module _4_Bit_Multiplexer (
  input  Switch,
  input  A0,
  input  B0,
  input  A1,
  input  B1,
  input  A2,
  input  B2,
  input  A3,
  input  B3,
  output Q0,
  output Q1,
  output Q2,
  output Q3
);

  _1_Bit_Multiplexer u_1_bit_multiplexer_1 (.A(A0), .Switch(Switch), .B(B0), .Q(Q0));
  _1_Bit_Multiplexer u_1_bit_multiplexer_2 (.A(A1), .Switch(Switch), .B(B1), .Q(Q1));
  _1_Bit_Multiplexer u_1_bit_multiplexer_3 (.A(A2), .Switch(Switch), .B(B2), .Q(Q2));
  _1_Bit_Multiplexer u_1_bit_multiplexer_4 (.A(A3), .Switch(Switch), .B(B3), .Q(Q3));
endmodule

module _8_Bit_Clear (
  input  A7,
  input  A6,
  input  A5,
  input  A4,
  input  A3,
  input  A2,
  input  A1,
  input  A0,
  input  Enable,
  output Q7,
  output Q6,
  output Q5,
  output Q4,
  output Q3,
  output Q2,
  output Q1,
  output Q0
);

  wire not_1_out;

  not not_1 (not_1_out, Enable);
  and and_1 (Q0, not_1_out, A0);
  and and_2 (Q1, not_1_out, A1);
  and and_3 (Q2, not_1_out, A2);
  and and_4 (Q3, not_1_out, A3);
  and and_5 (Q4, not_1_out, A4);
  and and_6 (Q5, not_1_out, A5);
  and and_7 (Q6, not_1_out, A6);
  and and_8 (Q7, not_1_out, A7);
endmodule

module _8_Bit_Inverter (
  input  A7,
  input  A6,
  input  A5,
  input  A4,
  input  A3,
  input  A2,
  input  A1,
  input  A0,
  input  Enable,
  output Q7,
  output Q6,
  output Q5,
  output Q4,
  output Q3,
  output Q2,
  output Q1,
  output Q0
);

  xor xor_1 (Q0, Enable, A0);
  xor xor_2 (Q1, Enable, A1);
  xor xor_3 (Q2, Enable, A2);
  xor xor_4 (Q3, Enable, A3);
  xor xor_5 (Q4, Enable, A4);
  xor xor_6 (Q5, Enable, A5);
  xor xor_7 (Q6, Enable, A6);
  xor xor_8 (Q7, Enable, A7);
endmodule

module _8_Bit_OR (
  input  B7,
  input  B6,
  input  B5,
  input  B4,
  input  B3,
  input  B2,
  input  B1,
  input  B0,
  input  A7,
  input  A6,
  input  A5,
  input  A4,
  input  A3,
  input  A2,
  input  A1,
  input  A0,
  output Q7,
  output Q6,
  output Q5,
  output Q4,
  output Q3,
  output Q2,
  output Q1,
  output Q0
);

  or or_1 (Q0, A0, B0);
  or or_2 (Q1, A1, B1);
  or or_3 (Q2, A2, B2);
  or or_4 (Q3, A3, B3);
  or or_5 (Q4, A4, B4);
  or or_6 (Q5, A5, B5);
  or or_7 (Q6, A6, B6);
  or or_8 (Q7, A7, B7);
endmodule

module _8_Bit_AND (
  input  B7,
  input  B6,
  input  B5,
  input  B4,
  input  B3,
  input  B2,
  input  B1,
  input  B0,
  input  A7,
  input  A6,
  input  A5,
  input  A4,
  input  A3,
  input  A2,
  input  A1,
  input  A0,
  output Q7,
  output Q6,
  output Q5,
  output Q4,
  output Q3,
  output Q2,
  output Q1,
  output Q0
);

  and and_1 (Q0, A0, B0);
  and and_2 (Q1, A1, B1);
  and and_3 (Q2, A2, B2);
  and and_4 (Q3, A3, B3);
  and and_5 (Q4, A4, B4);
  and and_6 (Q5, A5, B5);
  and and_7 (Q6, A6, B6);
  and and_8 (Q7, A7, B7);
endmodule

module _8_Bit_XOR (
  input  B7,
  input  B6,
  input  B5,
  input  B4,
  input  B3,
  input  B2,
  input  B1,
  input  B0,
  input  A7,
  input  A6,
  input  A5,
  input  A4,
  input  A3,
  input  A2,
  input  A1,
  input  A0,
  output Q7,
  output Q6,
  output Q5,
  output Q4,
  output Q3,
  output Q2,
  output Q1,
  output Q0
);

  xor xor_1 (Q0, A0, B0);
  xor xor_2 (Q1, A1, B1);
  xor xor_3 (Q2, A2, B2);
  xor xor_4 (Q3, A3, B3);
  xor xor_5 (Q4, A4, B4);
  xor xor_6 (Q5, A5, B5);
  xor xor_7 (Q6, A6, B6);
  xor xor_8 (Q7, A7, B7);
endmodule

module _8_Bit_2x1_Multiplexer (
  input  A7,
  input  A6,
  input  A5,
  input  A4,
  input  A3,
  input  A2,
  input  A1,
  input  A0,
  input  B5,
  input  B6,
  input  B5_2,
  input  B4,
  input  B3,
  input  B2,
  input  B1,
  input  B0,
  input  Enable,
  output Q7,
  output Q6,
  output Q5,
  output Q4,
  output Q3,
  output Q2,
  output Q1,
  output Q0
);

  _1_Bit_Multiplexer u_1_bit_multiplexer_1 (.A(A0), .Switch(Enable), .B(B0), .Q(Q0));
  _1_Bit_Multiplexer u_1_bit_multiplexer_2 (.A(A1), .Switch(Enable), .B(B1), .Q(Q1));
  _1_Bit_Multiplexer u_1_bit_multiplexer_3 (.A(A2), .Switch(Enable), .B(B2), .Q(Q2));
  _1_Bit_Multiplexer u_1_bit_multiplexer_4 (.A(A3), .Switch(Enable), .B(B3), .Q(Q3));
  _1_Bit_Multiplexer u_1_bit_multiplexer_5 (.A(A4), .Switch(Enable), .B(B4), .Q(Q4));
  _1_Bit_Multiplexer u_1_bit_multiplexer_6 (.A(A5), .Switch(Enable), .B(B5_2), .Q(Q5));
  _1_Bit_Multiplexer u_1_bit_multiplexer_7 (.A(A6), .Switch(Enable), .B(B6), .Q(Q6));
  _1_Bit_Multiplexer u_1_bit_multiplexer_8 (.A(A7), .Switch(Enable), .B(B5), .Q(Q7));
endmodule

module _8_Bit_2x1_Multiplexer_2 (
  input  A7,
  input  A6,
  input  A5,
  input  A4,
  input  A3,
  input  A2,
  input  A1,
  input  A0,
  input  B7,
  input  B6,
  input  B5,
  input  B4,
  input  B3,
  input  B2,
  input  B1,
  input  B0,
  input  Enable,
  output Q7,
  output Q6,
  output Q5,
  output Q4,
  output Q3,
  output Q2,
  output Q1,
  output Q0
);

  _1_Bit_Multiplexer u_1_bit_multiplexer_1 (.A(A0), .Switch(Enable), .B(B0), .Q(Q0));
  _1_Bit_Multiplexer u_1_bit_multiplexer_2 (.A(A1), .Switch(Enable), .B(B1), .Q(Q1));
  _1_Bit_Multiplexer u_1_bit_multiplexer_3 (.A(A2), .Switch(Enable), .B(B2), .Q(Q2));
  _1_Bit_Multiplexer u_1_bit_multiplexer_4 (.A(A3), .Switch(Enable), .B(B3), .Q(Q3));
  _1_Bit_Multiplexer u_1_bit_multiplexer_5 (.A(A4), .Switch(Enable), .B(B4), .Q(Q4));
  _1_Bit_Multiplexer u_1_bit_multiplexer_6 (.A(A5), .Switch(Enable), .B(B5), .Q(Q5));
  _1_Bit_Multiplexer u_1_bit_multiplexer_7 (.A(A6), .Switch(Enable), .B(B6), .Q(Q6));
  _1_Bit_Multiplexer u_1_bit_multiplexer_8 (.A(A7), .Switch(Enable), .B(B7), .Q(Q7));
endmodule

module _8_Bit_4x1_Multiplexer (
  input  in_1,
  input  in_2,
  input  in_3,
  input  in_4,
  input  in_5,
  input  in_6,
  input  in_7,
  input  in_8,
  input  in_9,
  input  in_10,
  input  in_11,
  input  in_12,
  input  in_13,
  input  in_14,
  input  in_15,
  input  in_16,
  input  in_17,
  input  in_18,
  input  in_19,
  input  in_20,
  input  in_21,
  input  in_22,
  input  in_23,
  input  in_24,
  input  in_25,
  input  in_26,
  input  in_27,
  input  in_28,
  input  in_29,
  input  in_30,
  input  in_31,
  input  in_32,
  input  in_33,
  input  in_34,
  output out_35,
  output out_36,
  output out_37,
  output out_38,
  output out_39,
  output out_40,
  output out_41,
  output out_42
);

  wire n8_bit_2x1_multiplexer_1_q0, n8_bit_2x1_multiplexer_1_q1, n8_bit_2x1_multiplexer_1_q2,
       n8_bit_2x1_multiplexer_1_q3, n8_bit_2x1_multiplexer_1_q4, n8_bit_2x1_multiplexer_1_q5,
       n8_bit_2x1_multiplexer_1_q6, n8_bit_2x1_multiplexer_1_q7, n8_bit_2x1_multiplexer_2_q0,
       n8_bit_2x1_multiplexer_2_q1, n8_bit_2x1_multiplexer_2_q2, n8_bit_2x1_multiplexer_2_q3,
       n8_bit_2x1_multiplexer_2_q4, n8_bit_2x1_multiplexer_2_q5, n8_bit_2x1_multiplexer_2_q6,
       n8_bit_2x1_multiplexer_2_q7;

  _8_Bit_2x1_Multiplexer u_8_bit_2x1_multiplexer_1 (
    .Enable(in_17), .A7(in_1), .A6(in_2), .A5(in_3), .A4(in_4), .A3(in_5), .A2(in_6), .A1(in_7), .A0(in_8),
    .B5(in_9), .B6(in_10), .B5_2(in_11), .B4(in_12), .B3(in_13), .B2(in_14), .B1(in_15), .B0(in_16),
    .Q7(n8_bit_2x1_multiplexer_1_q7), .Q6(n8_bit_2x1_multiplexer_1_q6), .Q5(n8_bit_2x1_multiplexer_1_q5),
    .Q4(n8_bit_2x1_multiplexer_1_q4), .Q3(n8_bit_2x1_multiplexer_1_q3), .Q2(n8_bit_2x1_multiplexer_1_q2),
    .Q1(n8_bit_2x1_multiplexer_1_q1), .Q0(n8_bit_2x1_multiplexer_1_q0));
  _8_Bit_2x1_Multiplexer u_8_bit_2x1_multiplexer_2 (
    .Enable(in_17), .A7(in_18), .A6(in_19), .A5(in_20), .A4(in_21), .A3(in_22), .A2(in_23), .A1(in_24),
    .A0(in_25), .B5(in_26), .B6(in_27), .B5_2(in_28), .B4(in_29), .B3(in_30), .B2(in_31), .B1(in_32),
    .B0(in_33), .Q7(n8_bit_2x1_multiplexer_2_q7), .Q6(n8_bit_2x1_multiplexer_2_q6),
    .Q5(n8_bit_2x1_multiplexer_2_q5), .Q4(n8_bit_2x1_multiplexer_2_q4), .Q3(n8_bit_2x1_multiplexer_2_q3),
    .Q2(n8_bit_2x1_multiplexer_2_q2), .Q1(n8_bit_2x1_multiplexer_2_q1), .Q0(n8_bit_2x1_multiplexer_2_q0));
  _8_Bit_2x1_Multiplexer u_8_bit_2x1_multiplexer_3 (
    .Enable(in_34), .A7(n8_bit_2x1_multiplexer_2_q7), .A6(n8_bit_2x1_multiplexer_2_q6),
    .A5(n8_bit_2x1_multiplexer_2_q5), .A4(n8_bit_2x1_multiplexer_2_q4), .A3(n8_bit_2x1_multiplexer_2_q3),
    .A2(n8_bit_2x1_multiplexer_2_q2), .A1(n8_bit_2x1_multiplexer_2_q1), .A0(n8_bit_2x1_multiplexer_2_q0),
    .B5(n8_bit_2x1_multiplexer_1_q7), .B6(n8_bit_2x1_multiplexer_1_q6), .B5_2(n8_bit_2x1_multiplexer_1_q5),
    .B4(n8_bit_2x1_multiplexer_1_q4), .B3(n8_bit_2x1_multiplexer_1_q3), .B2(n8_bit_2x1_multiplexer_1_q2),
    .B1(n8_bit_2x1_multiplexer_1_q1), .B0(n8_bit_2x1_multiplexer_1_q0), .Q7(out_35), .Q6(out_36),
    .Q5(out_37), .Q4(out_38), .Q3(out_39), .Q2(out_40), .Q1(out_41), .Q0(out_42));
endmodule

module _8_Bit_4x1_Multiplexer_2 (
  input  S0,
  input  S1,
  input  A0,
  input  A1,
  input  A2,
  input  A3,
  input  A4,
  input  A5,
  input  A6,
  input  A7,
  input  B0,
  input  B1,
  input  B2,
  input  B3,
  input  B4,
  input  B5,
  input  B6,
  input  B7,
  input  C0,
  input  C1,
  input  C2,
  input  C3,
  input  C4,
  input  C5,
  input  C6,
  input  C7,
  input  D0,
  input  D1,
  input  D2,
  input  D3,
  input  D4,
  input  D5,
  input  D6,
  input  D7,
  output Q0,
  output Q1,
  output Q2,
  output Q3,
  output Q4,
  output Q5,
  output Q6,
  output Q7
);

  wire n8_bit_2x1_multiplexer_1_q0, n8_bit_2x1_multiplexer_1_q1, n8_bit_2x1_multiplexer_1_q2,
       n8_bit_2x1_multiplexer_1_q3, n8_bit_2x1_multiplexer_1_q4, n8_bit_2x1_multiplexer_1_q5,
       n8_bit_2x1_multiplexer_1_q6, n8_bit_2x1_multiplexer_1_q7, n8_bit_2x1_multiplexer_2_q0,
       n8_bit_2x1_multiplexer_2_q1, n8_bit_2x1_multiplexer_2_q2, n8_bit_2x1_multiplexer_2_q3,
       n8_bit_2x1_multiplexer_2_q4, n8_bit_2x1_multiplexer_2_q5, n8_bit_2x1_multiplexer_2_q6,
       n8_bit_2x1_multiplexer_2_q7;

  _8_Bit_2x1_Multiplexer_2 u_8_bit_2x1_multiplexer_1 (
    .Enable(S0), .A7(A7), .A6(A6), .A5(A5), .A4(A4), .A3(A3), .A2(A2), .A1(A1), .A0(A0), .B7(B7), .B6(B6),
    .B5(B5), .B4(B4), .B3(B3), .B2(B2), .B1(B1), .B0(B0), .Q7(n8_bit_2x1_multiplexer_1_q7),
    .Q6(n8_bit_2x1_multiplexer_1_q6), .Q5(n8_bit_2x1_multiplexer_1_q5), .Q4(n8_bit_2x1_multiplexer_1_q4),
    .Q3(n8_bit_2x1_multiplexer_1_q3), .Q2(n8_bit_2x1_multiplexer_1_q2), .Q1(n8_bit_2x1_multiplexer_1_q1),
    .Q0(n8_bit_2x1_multiplexer_1_q0));
  _8_Bit_2x1_Multiplexer_2 u_8_bit_2x1_multiplexer_2 (
    .Enable(S0), .A7(C7), .A6(C6), .A5(C5), .A4(C4), .A3(C3), .A2(C2), .A1(C1), .A0(C0), .B7(D7), .B6(D6),
    .B5(D5), .B4(D4), .B3(D3), .B2(D2), .B1(D1), .B0(D0), .Q7(n8_bit_2x1_multiplexer_2_q7),
    .Q6(n8_bit_2x1_multiplexer_2_q6), .Q5(n8_bit_2x1_multiplexer_2_q5), .Q4(n8_bit_2x1_multiplexer_2_q4),
    .Q3(n8_bit_2x1_multiplexer_2_q3), .Q2(n8_bit_2x1_multiplexer_2_q2), .Q1(n8_bit_2x1_multiplexer_2_q1),
    .Q0(n8_bit_2x1_multiplexer_2_q0));
  _8_Bit_2x1_Multiplexer_2 u_8_bit_2x1_multiplexer_3 (
    .Enable(S1), .A7(n8_bit_2x1_multiplexer_1_q7), .A6(n8_bit_2x1_multiplexer_1_q6),
    .A5(n8_bit_2x1_multiplexer_1_q5), .A4(n8_bit_2x1_multiplexer_1_q4), .A3(n8_bit_2x1_multiplexer_1_q3),
    .A2(n8_bit_2x1_multiplexer_1_q2), .A1(n8_bit_2x1_multiplexer_1_q1), .A0(n8_bit_2x1_multiplexer_1_q0),
    .B7(n8_bit_2x1_multiplexer_2_q7), .B6(n8_bit_2x1_multiplexer_2_q6), .B5(n8_bit_2x1_multiplexer_2_q5),
    .B4(n8_bit_2x1_multiplexer_2_q4), .B3(n8_bit_2x1_multiplexer_2_q3), .B2(n8_bit_2x1_multiplexer_2_q2),
    .B1(n8_bit_2x1_multiplexer_2_q1), .B0(n8_bit_2x1_multiplexer_2_q0), .Q7(Q7), .Q6(Q6), .Q5(Q5), .Q4(Q4),
    .Q3(Q3), .Q2(Q2), .Q1(Q1), .Q0(Q0));
endmodule

module _8_Bit_ALU (
  input  Alu_En,
  input  S3,
  input  S2,
  input  S1,
  input  A0,
  input  A1,
  input  A2,
  input  A3,
  input  A4,
  input  A5,
  input  A6,
  input  A7,
  input  B0,
  input  Ci,
  input  B1,
  input  B2,
  input  B3,
  input  B4,
  input  B5,
  input  B6,
  input  B7,
  output S7,
  output S6,
  output S5,
  output S4,
  output S3_2,
  output S2_2,
  output S1_2,
  output S0,
  output Q0,
  output Q1,
  output Q2,
  output Q3,
  output Q4,
  output Q5,
  output Q6,
  output Q7,
  output Carry,
  output Overflow,
  output Negative,
  output Zero
);

  wire and_1_out, and_2_out, n8_bit_add_sub_1_carry_out, n8_bit_add_sub_1_overflow, n8_bit_add_sub_1_q0,
       n8_bit_add_sub_1_q1, n8_bit_add_sub_1_q2, n8_bit_add_sub_1_q3, n8_bit_add_sub_1_q4,
       n8_bit_add_sub_1_q5, n8_bit_add_sub_1_q6, n8_bit_add_sub_1_q7, n8_bit_and_1_q0, n8_bit_and_1_q1,
       n8_bit_and_1_q2, n8_bit_and_1_q3, n8_bit_and_1_q4, n8_bit_and_1_q5, n8_bit_and_1_q6, n8_bit_and_1_q7,
       n8_bit_clear_1_q0, n8_bit_clear_1_q1, n8_bit_clear_1_q2, n8_bit_clear_1_q3, n8_bit_clear_1_q4,
       n8_bit_clear_1_q5, n8_bit_clear_1_q6, n8_bit_clear_1_q7, n8_bit_inverter_1_q0, n8_bit_inverter_1_q1,
       n8_bit_inverter_1_q2, n8_bit_inverter_1_q3, n8_bit_inverter_1_q4, n8_bit_inverter_1_q5,
       n8_bit_inverter_1_q6, n8_bit_inverter_1_q7, n8_bit_inverter_2_q0, n8_bit_inverter_2_q1,
       n8_bit_inverter_2_q2, n8_bit_inverter_2_q3, n8_bit_inverter_2_q4, n8_bit_inverter_2_q5,
       n8_bit_inverter_2_q6, n8_bit_inverter_2_q7, n8_bit_or_1_q0, n8_bit_or_1_q1, n8_bit_or_1_q2,
       n8_bit_or_1_q3, n8_bit_or_1_q4, n8_bit_or_1_q5, n8_bit_or_1_q6, n8_bit_or_1_q7, n8_bit_xor_1_q0,
       n8_bit_xor_1_q1, n8_bit_xor_1_q2, n8_bit_xor_1_q3, n8_bit_xor_1_q4, n8_bit_xor_1_q5, n8_bit_xor_1_q6,
       n8_bit_xor_1_q7, nor_1_out, not_1_out, not_2_out, or_1_out;

  not not_1 (not_1_out, S1);
  not not_2 (not_2_out, S2);
  or or_1 (or_1_out, not_2_out, S3);
  and and_1 (and_1_out, not_2_out, S3);
  and and_2 (and_2_out, not_2_out, not_1_out);
  _8_Bit_Clear u_8_bit_clear_1 (
    .Enable(or_1_out), .A7(B7), .A6(B6), .A5(B5), .A4(B4), .A3(B3), .A2(B2), .A1(B1), .A0(B0),
    .Q7(n8_bit_clear_1_q7), .Q6(n8_bit_clear_1_q6), .Q5(n8_bit_clear_1_q5), .Q4(n8_bit_clear_1_q4),
    .Q3(n8_bit_clear_1_q3), .Q2(n8_bit_clear_1_q2), .Q1(n8_bit_clear_1_q1), .Q0(n8_bit_clear_1_q0));
  _8_Bit_Inverter u_8_bit_inverter_1 (
    .A7(A7), .A6(A6), .A5(A5), .A4(A4), .A3(A3), .A2(A2), .A1(A1), .A0(A0), .Q7(n8_bit_inverter_1_q7),
    .Q6(n8_bit_inverter_1_q6), .Q5(n8_bit_inverter_1_q5), .Q4(n8_bit_inverter_1_q4),
    .Q3(n8_bit_inverter_1_q3), .Q2(n8_bit_inverter_1_q2), .Q1(n8_bit_inverter_1_q1),
    .Q0(n8_bit_inverter_1_q0), .Enable(not_2_out));
  _8_Bit_Inverter u_8_bit_inverter_2 (
    .A7(n8_bit_clear_1_q7), .A6(n8_bit_clear_1_q6), .A5(n8_bit_clear_1_q5), .A4(n8_bit_clear_1_q4),
    .A3(n8_bit_clear_1_q3), .A2(n8_bit_clear_1_q2), .A1(n8_bit_clear_1_q1), .A0(n8_bit_clear_1_q0),
    .Q7(n8_bit_inverter_2_q7), .Q6(n8_bit_inverter_2_q6), .Q5(n8_bit_inverter_2_q5),
    .Q4(n8_bit_inverter_2_q4), .Q3(n8_bit_inverter_2_q3), .Q2(n8_bit_inverter_2_q2),
    .Q1(n8_bit_inverter_2_q1), .Q0(n8_bit_inverter_2_q0), .Enable(not_1_out));
  _8_Bit_OR u_8_bit_or_1 (
    .B7(B7), .B6(B6), .B5(B5), .B4(B4), .B3(B3), .B2(B2), .B1(B1), .B0(B0), .A7(A7), .A6(A6), .A5(A5),
    .A4(A4), .A3(A3), .A2(A2), .A1(A1), .A0(A0), .Q7(n8_bit_or_1_q7), .Q6(n8_bit_or_1_q6),
    .Q5(n8_bit_or_1_q5), .Q4(n8_bit_or_1_q4), .Q3(n8_bit_or_1_q3), .Q2(n8_bit_or_1_q2), .Q1(n8_bit_or_1_q1),
    .Q0(n8_bit_or_1_q0));
  _8_Bit_AND u_8_bit_and_1 (
    .B7(B7), .B6(B6), .B5(B5), .B4(B4), .B3(B3), .B2(B2), .B1(B1), .B0(B0), .A7(A7), .A6(A6), .A5(A5),
    .A4(A4), .A3(A3), .A2(A2), .A1(A1), .A0(A0), .Q7(n8_bit_and_1_q7), .Q6(n8_bit_and_1_q6),
    .Q5(n8_bit_and_1_q5), .Q4(n8_bit_and_1_q4), .Q3(n8_bit_and_1_q3), .Q2(n8_bit_and_1_q2),
    .Q1(n8_bit_and_1_q1), .Q0(n8_bit_and_1_q0));
  _8_Bit_XOR u_8_bit_xor_1 (
    .B7(B7), .B6(B6), .B5(B5), .B4(B4), .B3(B3), .B2(B2), .B1(B1), .B0(B0), .A7(A7), .A6(A6), .A5(A5),
    .A4(A4), .A3(A3), .A2(A2), .A1(A1), .A0(A0), .Q7(n8_bit_xor_1_q7), .Q6(n8_bit_xor_1_q6),
    .Q5(n8_bit_xor_1_q5), .Q4(n8_bit_xor_1_q4), .Q3(n8_bit_xor_1_q3), .Q2(n8_bit_xor_1_q2),
    .Q1(n8_bit_xor_1_q1), .Q0(n8_bit_xor_1_q0));
  _8_Bit_Add_Sub u_8_bit_add_sub_1 (
    .Carry_Out(n8_bit_add_sub_1_carry_out), .Add_Sub(Ci), .A7(n8_bit_inverter_1_q7),
    .B7(n8_bit_inverter_2_q7), .A6(n8_bit_inverter_1_q6), .B6(n8_bit_inverter_2_q6),
    .A5(n8_bit_inverter_1_q5), .B5(n8_bit_inverter_2_q5), .A4(n8_bit_inverter_1_q4),
    .B4(n8_bit_inverter_2_q4), .A3(n8_bit_inverter_1_q3), .B3(n8_bit_inverter_2_q3),
    .A2(n8_bit_inverter_1_q2), .B2(n8_bit_inverter_2_q2), .A1(n8_bit_inverter_1_q1),
    .B1(n8_bit_inverter_2_q1), .A0(n8_bit_inverter_1_q0), .B0(n8_bit_inverter_2_q0),
    .Q7(n8_bit_add_sub_1_q7), .Q6(n8_bit_add_sub_1_q6), .Q5(n8_bit_add_sub_1_q5), .Q4(n8_bit_add_sub_1_q4),
    .Q3(n8_bit_add_sub_1_q3), .Q2(n8_bit_add_sub_1_q2), .Q1(n8_bit_add_sub_1_q1), .Q0(n8_bit_add_sub_1_q0),
    .Overflow(n8_bit_add_sub_1_overflow));
  _8_Bit_4x1_Multiplexer_2 u_8_bit_4x1_multiplexer_1 (
    .S0(and_2_out), .S1(and_1_out), .A0(n8_bit_add_sub_1_q0), .A1(n8_bit_add_sub_1_q1),
    .A2(n8_bit_add_sub_1_q2), .A3(n8_bit_add_sub_1_q3), .A4(n8_bit_add_sub_1_q4), .A5(n8_bit_add_sub_1_q5),
    .A6(n8_bit_add_sub_1_q6), .A7(n8_bit_add_sub_1_q7), .B0(n8_bit_or_1_q0), .B1(n8_bit_or_1_q1),
    .B2(n8_bit_or_1_q2), .B3(n8_bit_or_1_q3), .B4(n8_bit_or_1_q4), .B5(n8_bit_or_1_q5), .B6(n8_bit_or_1_q6),
    .B7(n8_bit_or_1_q7), .C0(n8_bit_and_1_q0), .C1(n8_bit_and_1_q1), .C2(n8_bit_and_1_q2),
    .C3(n8_bit_and_1_q3), .C4(n8_bit_and_1_q4), .C5(n8_bit_and_1_q5), .C6(n8_bit_and_1_q6),
    .C7(n8_bit_and_1_q7), .D0(n8_bit_xor_1_q0), .D1(n8_bit_xor_1_q1), .D2(n8_bit_xor_1_q2),
    .D3(n8_bit_xor_1_q3), .D4(n8_bit_xor_1_q4), .D5(n8_bit_xor_1_q5), .D6(n8_bit_xor_1_q6),
    .D7(n8_bit_xor_1_q7), .Q0(S0), .Q1(S1_2), .Q2(S2_2), .Q3(S3_2), .Q4(S4), .Q5(S5), .Q6(S6), .Q7(S7));
  nor nor_1 (nor_1_out, n8_bit_add_sub_1_q7, n8_bit_add_sub_1_q6, n8_bit_add_sub_1_q5, n8_bit_add_sub_1_q4, n8_bit_add_sub_1_q3, n8_bit_add_sub_1_q2, n8_bit_add_sub_1_q1, n8_bit_add_sub_1_q0);
  and and_3 (Carry, n8_bit_add_sub_1_carry_out, Alu_En);
  and and_4 (Overflow, n8_bit_add_sub_1_overflow, Alu_En);
  and and_5 (Negative, n8_bit_add_sub_1_q7, Alu_En);
  and and_6 (Zero, nor_1_out, Alu_En);
  assign Q0 = Alu_En ? S0 : 1'bz;  // Controlled_Buffer controlled_buffer_1
  assign Q1 = Alu_En ? S1_2 : 1'bz;  // Controlled_Buffer controlled_buffer_2
  assign Q2 = Alu_En ? S2_2 : 1'bz;  // Controlled_Buffer controlled_buffer_3
  assign Q3 = Alu_En ? S3_2 : 1'bz;  // Controlled_Buffer controlled_buffer_4
  assign Q4 = Alu_En ? S4 : 1'bz;  // Controlled_Buffer controlled_buffer_5
  assign Q5 = Alu_En ? S5 : 1'bz;  // Controlled_Buffer controlled_buffer_6
  assign Q6 = Alu_En ? S6 : 1'bz;  // Controlled_Buffer controlled_buffer_7
  assign Q7 = Alu_En ? S7 : 1'bz;  // Controlled_Buffer controlled_buffer_8

  // Notes on the sheet:
  //   000 A OR B
  //   001 NOT A
  //   010 A + NOT B + Ci
  //   011 A + B + Ci
  //   100 A XOR B
  //   101 A AND B
  //   110 A - 1 + Ci
endmodule

module _4_Bit_Decoder___7_Segment (
  input  D,
  input  C,
  input  B,
  input  A,
  output a_2,
  output b_2,
  output c_2,
  output d_2,
  output e,
  output f,
  output g
);

  wire nand_1_out, nand_2_out, nand_3_out, nand_4_out, nand_5_out, nand_6_out, nand_7_out, nand_8_out,
       nand_9_out, nand_10_out, nand_11_out, nand_12_out, nand_13_out, nand_14_out, nand_15_out, nand_16_out,
       nand_17_out, nand_18_out, nand_19_out, nand_20_out, nand_21_out, nand_22_out, nand_23_out,
       nand_24_out, nand_25_out, nand_26_out, nand_27_out, nand_28_out, nand_29_out, nand_30_out,
       nand_31_out, nand_32_out, nand_33_out, nand_34_out, nand_35_out, nand_36_out, nand_37_out,
       nand_38_out, nand_39_out, nand_40_out, nand_41_out, nand_42_out, nand_43_out, nand_44_out,
       nand_45_out, nand_46_out, nand_47_out, nand_48_out, nand_49_out, nand_50_out, nand_51_out,
       nand_52_out, nand_53_out, nand_54_out, nand_55_out, nand_56_out, nand_57_out, nand_58_out,
       nand_59_out, nand_60_out, nand_61_out, nand_62_out, nand_63_out, nand_64_out, nand_65_out,
       nand_66_out, nand_67_out, nand_68_out, nand_69_out, nand_70_out, nand_71_out, nand_72_out,
       nand_73_out, nand_74_out, nand_75_out, nand_76_out, nand_77_out, nand_78_out, nand_79_out,
       nand_80_out, nand_81_out, nand_82_out, nand_83_out, nand_84_out, nand_85_out, nand_86_out,
       nand_87_out, nand_88_out, nand_89_out, nand_90_out, nand_91_out, nand_92_out, nand_93_out,
       nand_94_out, nand_95_out, nand_96_out, nand_97_out, nand_98_out, nand_99_out, nand_100_out,
       nand_101_out, nand_102_out, nand_103_out, nand_104_out, nand_106_out, nand_107_out, nand_108_out,
       nand_109_out, nand_110_out, nand_111_out, nand_112_out, nand_113_out, nand_114_out, nand_115_out,
       nand_116_out, nand_117_out, nand_118_out, nand_119_out, nand_120_out, nand_121_out, nand_122_out,
       nand_123_out, nand_124_out, nand_125_out, nand_126_out, nand_127_out, nand_128_out, nand_129_out,
       nand_130_out, nand_131_out, nand_132_out, nand_133_out, nand_134_out, nand_136_out, nand_137_out,
       nand_138_out, nand_139_out, nand_141_out, nand_142_out, nand_143_out, nand_144_out, nand_145_out,
       nand_146_out, nand_147_out, nand_148_out;

  nand nand_1 (nand_1_out, C, C);
  nand nand_2 (nand_2_out, D, D);
  nand nand_3 (nand_3_out, B, B);
  nand nand_4 (nand_4_out, D, D);
  nand nand_5 (nand_5_out, B, B);
  nand nand_6 (nand_6_out, D, D);
  nand nand_7 (nand_7_out, D, D);
  nand nand_8 (nand_8_out, C, C);
  nand nand_9 (nand_9_out, C, C);
  nand nand_10 (nand_10_out, C, C);
  nand nand_11 (nand_11_out, A, A);
  nand nand_12 (nand_12_out, A, A);
  nand nand_13 (nand_13_out, D, D);
  nand nand_14 (nand_14_out, C, C);
  nand nand_15 (nand_15_out, A, A);
  nand nand_16 (nand_16_out, D, D);
  nand nand_17 (nand_17_out, D, nand_1_out);
  nand nand_18 (nand_18_out, nand_2_out, nand_3_out);
  nand nand_19 (nand_19_out, nand_4_out, nand_5_out);
  nand nand_20 (nand_20_out, nand_6_out, A);
  nand nand_21 (nand_21_out, nand_7_out, nand_8_out);
  nand nand_22 (nand_22_out, nand_9_out, B);
  nand nand_23 (nand_23_out, nand_10_out, nand_11_out);
  nand nand_24 (nand_24_out, B, nand_12_out);
  nand nand_25 (nand_25_out, D, B);
  nand nand_26 (nand_26_out, D, C);
  nand nand_27 (nand_27_out, nand_13_out, C);
  nand nand_28 (nand_28_out, nand_14_out, B);
  nand nand_29 (nand_29_out, B, nand_15_out);
  nand nand_30 (nand_30_out, nand_16_out, C);
  nand nand_31 (nand_31_out, C, C);
  nand nand_32 (nand_32_out, A, A);
  nand nand_33 (nand_33_out, D, D);
  nand nand_34 (nand_34_out, D, D);
  nand nand_35 (nand_35_out, nand_17_out, nand_17_out);
  nand nand_36 (nand_36_out, B, B);
  nand nand_37 (nand_37_out, D, D);
  nand nand_38 (nand_38_out, C, C);
  nand nand_39 (nand_39_out, nand_18_out, nand_18_out);
  nand nand_40 (nand_40_out, A, A);
  nand nand_41 (nand_41_out, D, D);
  nand nand_42 (nand_42_out, B, B);
  nand nand_43 (nand_43_out, nand_19_out, nand_20_out);
  nand nand_44 (nand_44_out, B, B);
  nand nand_45 (nand_45_out, D, D);
  nand nand_46 (nand_46_out, C, C);
  nand nand_47 (nand_47_out, nand_21_out, nand_21_out);
  nand nand_48 (nand_48_out, A, A);
  nand nand_49 (nand_49_out, nand_22_out, nand_22_out);
  nand nand_50 (nand_50_out, B, B);
  nand nand_51 (nand_51_out, B, B);
  nand nand_52 (nand_52_out, nand_23_out, nand_24_out);
  nand nand_53 (nand_53_out, nand_25_out, nand_26_out);
  nand nand_54 (nand_54_out, B, B);
  nand nand_55 (nand_55_out, A, A);
  nand nand_56 (nand_56_out, nand_27_out, nand_27_out);
  nand nand_57 (nand_57_out, B, B);
  nand nand_58 (nand_58_out, nand_28_out, nand_29_out);
  nand nand_59 (nand_59_out, nand_30_out, nand_30_out);
  nand nand_60 (nand_60_out, B, B);
  nand nand_61 (nand_61_out, C, C);
  nand nand_62 (nand_62_out, nand_31_out, nand_32_out);
  nand nand_63 (nand_63_out, nand_33_out, B);
  nand nand_64 (nand_64_out, nand_34_out, C);
  nand nand_65 (nand_65_out, C, B);
  nand nand_66 (nand_66_out, nand_35_out, nand_36_out);
  nand nand_67 (nand_67_out, nand_37_out, nand_38_out);
  nand nand_68 (nand_68_out, nand_39_out, nand_40_out);
  nand nand_69 (nand_69_out, nand_41_out, B);
  nand nand_70 (nand_70_out, D, nand_42_out);
  nand nand_71 (nand_71_out, nand_43_out, nand_43_out);
  nand nand_72 (nand_72_out, nand_44_out, A);
  nand nand_73 (nand_73_out, nand_45_out, C);
  nand nand_74 (nand_74_out, D, nand_46_out);
  nand nand_75 (nand_75_out, nand_47_out, nand_48_out);
  nand nand_76 (nand_76_out, nand_49_out, A);
  nand nand_77 (nand_77_out, C, nand_50_out);
  nand nand_78 (nand_78_out, C, B);
  nand nand_79 (nand_79_out, D, nand_51_out);
  nand nand_80 (nand_80_out, nand_52_out, nand_52_out);
  nand nand_81 (nand_81_out, nand_53_out, nand_53_out);
  nand nand_82 (nand_82_out, nand_54_out, nand_55_out);
  nand nand_83 (nand_83_out, nand_56_out, nand_57_out);
  nand nand_84 (nand_84_out, nand_58_out, nand_58_out);
  nand nand_85 (nand_85_out, nand_59_out, nand_60_out);
  nand nand_86 (nand_86_out, D, nand_61_out);
  nand nand_87 (nand_87_out, D, A);
  nand nand_88 (nand_88_out, nand_62_out, nand_63_out);
  nand nand_89 (nand_89_out, nand_64_out, nand_64_out);
  nand nand_90 (nand_90_out, nand_65_out, nand_66_out);
  nand nand_91 (nand_91_out, A, A);
  nand nand_92 (nand_92_out, nand_67_out, nand_68_out);
  nand nand_93 (nand_93_out, C, C);
  nand nand_94 (nand_94_out, A, A);
  nand nand_95 (nand_95_out, nand_69_out, nand_69_out);
  nand nand_96 (nand_96_out, nand_70_out, nand_70_out);
  nand nand_97 (nand_97_out, nand_71_out, nand_72_out);
  nand nand_98 (nand_98_out, nand_73_out, nand_74_out);
  nand nand_99 (nand_99_out, nand_75_out, nand_76_out);
  nand nand_100 (nand_100_out, nand_77_out, nand_77_out);
  nand nand_101 (nand_101_out, nand_78_out, nand_78_out);
  nand nand_102 (nand_102_out, A, A);
  nand nand_103 (nand_103_out, nand_79_out, nand_79_out);
  nand nand_104 (nand_104_out, A, A);
  nand nand_105 (e, nand_80_out, nand_81_out);
  nand nand_106 (nand_106_out, nand_82_out, nand_83_out);
  nand nand_107 (nand_107_out, A, A);
  nand nand_108 (nand_108_out, C, C);
  nand nand_109 (nand_109_out, nand_84_out, nand_85_out);
  nand nand_110 (nand_110_out, nand_86_out, nand_87_out);
  nand nand_111 (nand_111_out, nand_88_out, nand_88_out);
  nand nand_112 (nand_112_out, nand_89_out, A);
  nand nand_113 (nand_113_out, nand_90_out, nand_90_out);
  nand nand_114 (nand_114_out, D, nand_91_out);
  nand nand_115 (nand_115_out, nand_92_out, nand_92_out);
  nand nand_116 (nand_116_out, nand_93_out, nand_94_out);
  nand nand_117 (nand_117_out, nand_95_out, A);
  nand nand_118 (nand_118_out, nand_96_out, A);
  nand nand_119 (nand_119_out, nand_97_out, nand_97_out);
  nand nand_120 (nand_120_out, nand_98_out, nand_98_out);
  nand nand_121 (nand_121_out, nand_99_out, nand_99_out);
  nand nand_122 (nand_122_out, nand_100_out, A);
  nand nand_123 (nand_123_out, nand_101_out, nand_102_out);
  nand nand_124 (nand_124_out, nand_103_out, nand_104_out);
  nand nand_125 (nand_125_out, nand_106_out, nand_106_out);
  nand nand_126 (nand_126_out, C, nand_107_out);
  nand nand_127 (nand_127_out, D, nand_108_out);
  nand nand_128 (nand_128_out, D, B);
  nand nand_129 (nand_129_out, nand_109_out, nand_109_out);
  nand nand_130 (nand_130_out, nand_110_out, nand_110_out);
  nand nand_131 (nand_131_out, nand_111_out, nand_112_out);
  nand nand_132 (nand_132_out, nand_113_out, nand_114_out);
  nand nand_133 (nand_133_out, nand_115_out, nand_116_out);
  nand nand_134 (nand_134_out, nand_117_out, nand_118_out);
  nand nand_135 (c_2, nand_119_out, nand_120_out);
  nand nand_136 (nand_136_out, nand_121_out, nand_122_out);
  nand nand_137 (nand_137_out, nand_123_out, nand_124_out);
  nand nand_138 (nand_138_out, nand_125_out, nand_126_out);
  nand nand_139 (nand_139_out, nand_127_out, nand_128_out);
  nand nand_140 (g, nand_129_out, nand_130_out);
  nand nand_141 (nand_141_out, nand_131_out, nand_131_out);
  nand nand_142 (nand_142_out, nand_132_out, nand_132_out);
  nand nand_143 (nand_143_out, nand_133_out, nand_133_out);
  nand nand_144 (nand_144_out, nand_134_out, nand_134_out);
  nand nand_145 (nand_145_out, nand_136_out, nand_136_out);
  nand nand_146 (nand_146_out, nand_137_out, nand_137_out);
  nand nand_147 (nand_147_out, nand_138_out, nand_138_out);
  nand nand_148 (nand_148_out, nand_139_out, nand_139_out);
  nand nand_149 (a_2, nand_141_out, nand_142_out);
  nand nand_150 (b_2, nand_143_out, nand_144_out);
  nand nand_151 (d_2, nand_145_out, nand_146_out);
  nand nand_152 (f, nand_147_out, nand_148_out);
endmodule

module _8_Bit_7_segment_decoder (
  input  in_1,
  input  in_2,
  input  in_3,
  input  in_4,
  input  in_5,
  input  in_6,
  input  in_7,
  input  in_8,
  output A1,
  output B1,
  output C1,
  output D1,
  output E1,
  output F1,
  output G1,
  output A2,
  output B2,
  output C2,
  output D2,
  output E2,
  output F2,
  output G2,
  output A3,
  output B3,
  output C3,
  output D3,
  output E3,
  output F3,
  output G3
);

  ROM #(.dataWidth(21)) rom_1 (
    .addr({in_8, in_7, in_6, in_5, in_4, in_3, in_2, in_1}),
    .data({G3, F3, E3, D3, C3, B3, A3, G2, F2, E2, D2, C2, B2, A2, G1, F1, E1, D1, C1, B1, A1}));  // open: sel

  // Notes on the sheet:
  //   contents of rom_1 (hex, n*v repeats v):
  //   3f 6 5b 4f 66 6d 7d 7 7f 6f 33f 306 35b 34f 366 36d 37d 307 37f 36f 2dbf 2d86 2ddb 2dcf 2de6 2ded
  //   2dfd 2d87 2dff 2def 27bf 2786 27db 27cf 27e6 27ed 27fd 2787 27ff 27ef 333f 3306 335b 334f 3366 336d
  //   337d 3307 337f 336f 36bf 3686 36db 36cf 36e6 36ed 36fd 3687 36ff 36ef 3ebf 3e86 3edb 3ecf 3ee6 3eed
  //   3efd 3e87 3eff 3eef 3bf 386 3db 3cf 3e6 3ed 3fd 387 3ff 3ef 3fbf 3f86 3fdb 3fcf 3fe6 3fed 3ffd 3f87
  //   3fff 3fef 37bf 3786 37db 37cf 37e6 37ed 37fd 3787 37ff 37ef 19fbf 19f86 19fdb 19fcf 19fe6 19fed
  //   19ffd 19f87 19fff 19fef 1833f 18306 1835b 1834f 18366 1836d 1837d 18307 1837f 1836f 1adbf 1ad86
  //   1addb 1adcf 1ade6 1aded 1adfd 1ad87 1adff 1adef 1a7bf 1a786 1a7db 1a7cf 1a7e6 1a7ed 1a7fd 1a787
  //   1a7ff 1a7ef 1b33f 1b306 1b35b 1b34f 1b366 1b36d 1b37d 1b307 1b37f 1b36f 1b6bf 1b686 1b6db 1b6cf
  //   1b6e6 1b6ed 1b6fd 1b687 1b6ff 1b6ef 1bebf 1be86 1bedb 1becf 1bee6 1beed 1befd 1be87 1beff 1beef
  //   183bf 18386 183db 183cf 183e6 183ed 183fd 18387 183ff 183ef 1bfbf 1bf86 1bfdb 1bfcf 1bfe6 1bfed
  //   1bffd 1bf87 1bfff 1bfef 1b7bf 1b786 1b7db 1b7cf 1b7e6 1b7ed 1b7fd 1b787 1b7ff 1b7ef 16dfbf 16df86
  //   16dfdb 16dfcf 16dfe6 16dfed 16dffd 16df87 16dfff 16dfef 16c33f 16c306 16c35b 16c34f 16c366 16c36d
  //   16c37d 16c307 16c37f 16c36f 16edbf 16ed86 16eddb 16edcf 16ede6 16eded 16edfd 16ed87 16edff 16edef
  //   16e7bf 16e786 16e7db 16e7cf 16e7e6 16e7ed 16e7fd 16e787 16e7ff 16e7ef 16f33f 16f306 16f35b 16f34f
  //   16f366 16f36d 16f37d 16f307 16f37f 16f36f 16f6bf 16f686 16f6db 16f6cf 16f6e6 16f6ed
endmodule

module _8_Bit_Reverser (
  input  A8,
  input  A7,
  input  A6,
  input  A5,
  input  A4,
  input  A3,
  input  A2,
  input  A1,
  output Q8,
  output Q7,
  output Q6,
  output Q5,
  output Q4,
  output Q3,
  output Q2,
  output Q1
);


  assign Q1 = A8;
  assign Q2 = A7;
  assign Q3 = A6;
  assign Q4 = A5;
  assign Q5 = A4;
  assign Q6 = A3;
  assign Q7 = A2;
  assign Q8 = A1;
endmodule

module _8_Bit_Counter (
  input  Enable_Out,
  input  Enable,
  input  Reset,
  input  Write,
  input  Clock,
  input  A8,
  input  A7,
  input  A6,
  input  A5,
  input  A4,
  input  A3,
  input  A2,
  input  A1,
  output Q8,
  output Q7,
  output Q6,
  output Q5,
  output Q4,
  output Q3,
  output Q2,
  output Q1,
  output D8,
  output S7,
  output S6,
  output S5,
  output S4,
  output S3,
  output S2,
  output S1
);

  wire and_1_out, and_2_out, and_3_out, and_4_out, and_5_out, and_6_out, and_7_out, and_8_out, and_9_out,
       and_10_out, and_11_out, and_12_out, and_13_out, and_14_out, and_15_out, and_16_out, j_k_ff_2_qn,
       j_k_ff_3_qn, j_k_ff_4_qn, j_k_ff_5_qn, j_k_ff_6_qn, j_k_ff_7_qn, j_k_ff_8_qn, or_1_out, or_2_out,
       or_3_out, or_4_out, or_5_out, or_6_out, or_7_out, or_8_out;

  assign Q8 = Enable_Out ? D8 : 1'bz;  // Controlled_Buffer controlled_buffer_1
  J_K_Flip_Flop j_k_ff_1 (
    .J(Enable), .clk(j_k_ff_2_qn), .K(Enable), .Q(D8), .preset(and_2_out), .reset(or_1_out));  // open: Qn, en
  or or_1 (or_1_out, Reset, and_1_out);
  and and_1 (and_1_out, Write, ~A8, Clock);  // AND_Gate
  and and_2 (and_2_out, Write, A8, Clock);
  assign Q6 = Enable_Out ? S6 : 1'bz;  // Controlled_Buffer controlled_buffer_2
  assign Q4 = Enable_Out ? S4 : 1'bz;  // Controlled_Buffer controlled_buffer_3
  assign Q5 = Enable_Out ? S5 : 1'bz;  // Controlled_Buffer controlled_buffer_4
  assign Q7 = Enable_Out ? S7 : 1'bz;  // Controlled_Buffer controlled_buffer_5
  J_K_Flip_Flop j_k_ff_2 (
    .J(Enable), .clk(j_k_ff_3_qn), .K(Enable), .Q(S7), .Qn(j_k_ff_2_qn), .preset(and_4_out), .reset(or_2_out));  // open: en
  or or_2 (or_2_out, Reset, and_3_out);
  and and_3 (and_3_out, Write, ~A7, Clock);  // AND_Gate
  and and_4 (and_4_out, Write, A7, Clock);
  assign Q2 = Enable_Out ? S2 : 1'bz;  // Controlled_Buffer controlled_buffer_6
  assign Q1 = Enable_Out ? S1 : 1'bz;  // Controlled_Buffer controlled_buffer_7
  assign Q3 = Enable_Out ? S3 : 1'bz;  // Controlled_Buffer controlled_buffer_8
  J_K_Flip_Flop j_k_ff_3 (
    .J(Enable), .clk(j_k_ff_4_qn), .K(Enable), .Q(S6), .Qn(j_k_ff_3_qn), .preset(and_6_out), .reset(or_3_out));  // open: en
  or or_3 (or_3_out, Reset, and_5_out);
  and and_5 (and_5_out, Write, ~A6, Clock);  // AND_Gate
  and and_6 (and_6_out, Write, A6, Clock);
  J_K_Flip_Flop j_k_ff_4 (
    .J(Enable), .clk(j_k_ff_5_qn), .K(Enable), .Q(S5), .Qn(j_k_ff_4_qn), .preset(and_8_out), .reset(or_4_out));  // open: en
  or or_4 (or_4_out, Reset, and_7_out);
  and and_7 (and_7_out, Write, ~A5, Clock);  // AND_Gate
  and and_8 (and_8_out, Write, A5, Clock);
  J_K_Flip_Flop j_k_ff_5 (
    .J(Enable), .clk(j_k_ff_6_qn), .K(Enable), .Q(S4), .Qn(j_k_ff_5_qn), .preset(and_9_out), .reset(or_5_out));  // open: en
  or or_5 (or_5_out, Reset, and_10_out);
  and and_9 (and_9_out, Write, A4, Clock);
  and and_10 (and_10_out, Write, ~A4, Clock);  // AND_Gate
  J_K_Flip_Flop j_k_ff_6 (
    .J(Enable), .clk(j_k_ff_7_qn), .K(Enable), .Q(S3), .Qn(j_k_ff_6_qn), .preset(and_11_out), .reset(or_6_out));  // open: en
  or or_6 (or_6_out, Reset, and_12_out);
  and and_11 (and_11_out, Write, A3, Clock);
  and and_12 (and_12_out, Write, ~A3, Clock);  // AND_Gate
  J_K_Flip_Flop j_k_ff_7 (
    .J(Enable), .clk(j_k_ff_8_qn), .K(Enable), .Q(S2), .Qn(j_k_ff_7_qn), .preset(and_13_out), .reset(or_7_out));  // open: en
  or or_7 (or_7_out, Reset, and_14_out);
  and and_13 (and_13_out, Write, A2, Clock);
  and and_14 (and_14_out, Write, ~A2, Clock);  // AND_Gate
  J_K_Flip_Flop j_k_ff_8 (
    .J(Enable), .clk(Clock), .K(Enable), .Q(S1), .Qn(j_k_ff_8_qn), .preset(and_15_out), .reset(or_8_out));  // open: en
  or or_8 (or_8_out, Reset, and_16_out);
  and and_15 (and_15_out, Write, A1, Clock);
  and and_16 (and_16_out, Write, ~A1, Clock);  // AND_Gate
endmodule

module _16_Byte_SRAM (
  input  A8,
  input  A7,
  input  A6,
  input  A5,
  input  A4,
  input  A3,
  input  A2,
  input  A1,
  input  Read,
  input  Write,
  input  Clear,
  input  Clock,
  input  A1_2,
  input  A2_2,
  input  A3_2,
  input  A4_2,
  output S8,
  output S7,
  output S6,
  output S5,
  output S4,
  output S3,
  output S2,
  output S1,
  output Q8,
  output Q7,
  output Q6,
  output Q5,
  output Q4,
  output Q3,
  output Q2,
  output Q1
);

  wire and_1_out, and_2_out, and_3_out, and_4_out, and_5_out, and_6_out, and_7_out, and_8_out, and_9_out,
       and_10_out, and_11_out, and_12_out, and_13_out, and_14_out, and_15_out, and_16_out,
       controlled_buffer_9_out, controlled_buffer_10_out, controlled_buffer_11_out, controlled_buffer_12_out,
       controlled_buffer_13_out, controlled_buffer_14_out, controlled_buffer_15_out,
       controlled_buffer_16_out, n4_bit_binary_decoder_1_d0, n4_bit_binary_decoder_1_d1,
       n4_bit_binary_decoder_1_d2, n4_bit_binary_decoder_1_d3, n4_bit_binary_decoder_1_d4,
       n4_bit_binary_decoder_1_d5, n4_bit_binary_decoder_1_d6, n4_bit_binary_decoder_1_d7,
       n4_bit_binary_decoder_1_d8, n4_bit_binary_decoder_1_d9, n4_bit_binary_decoder_1_da,
       n4_bit_binary_decoder_1_db, n4_bit_binary_decoder_1_dc, n4_bit_binary_decoder_1_dd,
       n4_bit_binary_decoder_1_de, n4_bit_binary_decoder_1_df, n8_bit_register_1_s0, n8_bit_register_1_s1,
       n8_bit_register_1_s2, n8_bit_register_1_s3, n8_bit_register_1_s4, n8_bit_register_1_s5,
       n8_bit_register_1_s6, n8_bit_register_1_s7, n8_bit_register_2_s0, n8_bit_register_2_s1,
       n8_bit_register_2_s2, n8_bit_register_2_s3, n8_bit_register_2_s4, n8_bit_register_2_s5,
       n8_bit_register_2_s6, n8_bit_register_2_s7, n8_bit_register_3_s0, n8_bit_register_3_s1,
       n8_bit_register_3_s2, n8_bit_register_3_s3, n8_bit_register_3_s4, n8_bit_register_3_s5,
       n8_bit_register_3_s6, n8_bit_register_3_s7, n8_bit_register_4_s0, n8_bit_register_4_s1,
       n8_bit_register_4_s2, n8_bit_register_4_s3, n8_bit_register_4_s4, n8_bit_register_4_s5,
       n8_bit_register_4_s6, n8_bit_register_4_s7, n8_bit_register_5_s0, n8_bit_register_5_s1,
       n8_bit_register_5_s2, n8_bit_register_5_s3, n8_bit_register_5_s4, n8_bit_register_5_s5,
       n8_bit_register_5_s6, n8_bit_register_5_s7, n8_bit_register_6_s0, n8_bit_register_6_s1,
       n8_bit_register_6_s2, n8_bit_register_6_s3, n8_bit_register_6_s4, n8_bit_register_6_s5,
       n8_bit_register_6_s6, n8_bit_register_6_s7, n8_bit_register_7_s0, n8_bit_register_7_s1,
       n8_bit_register_7_s2, n8_bit_register_7_s3, n8_bit_register_7_s4, n8_bit_register_7_s5,
       n8_bit_register_7_s6, n8_bit_register_7_s7, n8_bit_register_8_s0, n8_bit_register_8_s1,
       n8_bit_register_8_s2, n8_bit_register_8_s3, n8_bit_register_8_s4, n8_bit_register_8_s5,
       n8_bit_register_8_s6, n8_bit_register_8_s7, n8_bit_register_9_s0, n8_bit_register_9_s1,
       n8_bit_register_9_s2, n8_bit_register_9_s3, n8_bit_register_9_s4, n8_bit_register_9_s5,
       n8_bit_register_9_s6, n8_bit_register_9_s7, n8_bit_register_10_s0, n8_bit_register_10_s1,
       n8_bit_register_10_s2, n8_bit_register_10_s3, n8_bit_register_10_s4, n8_bit_register_10_s5,
       n8_bit_register_10_s6, n8_bit_register_10_s7, n8_bit_register_11_s0, n8_bit_register_11_s1,
       n8_bit_register_11_s2, n8_bit_register_11_s3, n8_bit_register_11_s4, n8_bit_register_11_s5,
       n8_bit_register_11_s6, n8_bit_register_11_s7, n8_bit_register_12_s0, n8_bit_register_12_s1,
       n8_bit_register_12_s2, n8_bit_register_12_s3, n8_bit_register_12_s4, n8_bit_register_12_s5,
       n8_bit_register_12_s6, n8_bit_register_12_s7, n8_bit_register_13_s0, n8_bit_register_13_s1,
       n8_bit_register_13_s2, n8_bit_register_13_s3, n8_bit_register_13_s4, n8_bit_register_13_s5,
       n8_bit_register_13_s6, n8_bit_register_13_s7, n8_bit_register_14_s0, n8_bit_register_14_s1,
       n8_bit_register_14_s2, n8_bit_register_14_s3, n8_bit_register_14_s4, n8_bit_register_14_s5,
       n8_bit_register_14_s6, n8_bit_register_14_s7, n8_bit_register_15_s0, n8_bit_register_15_s1,
       n8_bit_register_15_s2, n8_bit_register_15_s3, n8_bit_register_15_s4, n8_bit_register_15_s5,
       n8_bit_register_15_s6, n8_bit_register_15_s7, n8_bit_register_16_s0, n8_bit_register_16_s1,
       n8_bit_register_16_s2, n8_bit_register_16_s3, n8_bit_register_16_s4, n8_bit_register_16_s5,
       n8_bit_register_16_s6, n8_bit_register_16_s7;

  _4_bit_binary_decoder u_4_bit_binary_decoder_1 (
    .D0(n4_bit_binary_decoder_1_d0), .D1(n4_bit_binary_decoder_1_d1), .D2(n4_bit_binary_decoder_1_d2),
    .D3(n4_bit_binary_decoder_1_d3), .D4(n4_bit_binary_decoder_1_d4), .D5(n4_bit_binary_decoder_1_d5),
    .D6(n4_bit_binary_decoder_1_d6), .D7(n4_bit_binary_decoder_1_d7), .D8(n4_bit_binary_decoder_1_d8),
    .D9(n4_bit_binary_decoder_1_d9), .DA(n4_bit_binary_decoder_1_da), .DB(n4_bit_binary_decoder_1_db),
    .DC(n4_bit_binary_decoder_1_dc), .DD(n4_bit_binary_decoder_1_dd), .DE(n4_bit_binary_decoder_1_de),
    .DF(n4_bit_binary_decoder_1_df), .Enable(1'b1), .A0(A1_2), .A1(A2_2), .A2(A3_2), .A3(A4_2));
  DotMatrix #(.inputtype("row"), .matrixcols(1), .matrixrows(8), .dotshape("circle")) dotmatrix_1 (
    .row0(n8_bit_register_1_s7), .row1(n8_bit_register_1_s6), .row2(n8_bit_register_1_s5),
    .row3(n8_bit_register_1_s4), .row4(n8_bit_register_1_s3), .row5(n8_bit_register_1_s2),
    .row6(n8_bit_register_1_s1), .row7(n8_bit_register_1_s0));
  DotMatrix #(.inputtype("row"), .matrixcols(1), .matrixrows(8), .dotshape("circle")) dotmatrix_2 (
    .row0(n8_bit_register_2_s7), .row1(n8_bit_register_2_s6), .row2(n8_bit_register_2_s5),
    .row3(n8_bit_register_2_s4), .row4(n8_bit_register_2_s3), .row5(n8_bit_register_2_s2),
    .row6(n8_bit_register_2_s1), .row7(n8_bit_register_2_s0));
  DotMatrix #(.inputtype("row"), .matrixcols(1), .matrixrows(8), .dotshape("circle")) dotmatrix_3 (
    .row0(n8_bit_register_3_s7), .row1(n8_bit_register_3_s6), .row2(n8_bit_register_3_s5),
    .row3(n8_bit_register_3_s4), .row4(n8_bit_register_3_s3), .row5(n8_bit_register_3_s2),
    .row6(n8_bit_register_3_s1), .row7(n8_bit_register_3_s0));
  DotMatrix #(.inputtype("row"), .matrixcols(1), .matrixrows(8), .dotshape("circle")) dotmatrix_4 (
    .row0(n8_bit_register_4_s7), .row1(n8_bit_register_4_s6), .row2(n8_bit_register_4_s5),
    .row3(n8_bit_register_4_s4), .row4(n8_bit_register_4_s3), .row5(n8_bit_register_4_s2),
    .row6(n8_bit_register_4_s1), .row7(n8_bit_register_4_s0));
  DotMatrix #(.inputtype("row"), .matrixcols(1), .matrixrows(8), .dotshape("circle")) dotmatrix_5 (
    .row0(n8_bit_register_5_s7), .row1(n8_bit_register_5_s6), .row2(n8_bit_register_5_s5),
    .row3(n8_bit_register_5_s4), .row4(n8_bit_register_5_s3), .row5(n8_bit_register_5_s2),
    .row6(n8_bit_register_5_s1), .row7(n8_bit_register_5_s0));
  DotMatrix #(.inputtype("row"), .matrixcols(1), .matrixrows(8), .dotshape("circle")) dotmatrix_6 (
    .row0(n8_bit_register_6_s7), .row1(n8_bit_register_6_s6), .row2(n8_bit_register_6_s5),
    .row3(n8_bit_register_6_s4), .row4(n8_bit_register_6_s3), .row5(n8_bit_register_6_s2),
    .row6(n8_bit_register_6_s1), .row7(n8_bit_register_6_s0));
  DotMatrix #(.inputtype("row"), .matrixcols(1), .matrixrows(8), .dotshape("circle")) dotmatrix_7 (
    .row0(n8_bit_register_7_s7), .row1(n8_bit_register_7_s6), .row2(n8_bit_register_7_s5),
    .row3(n8_bit_register_7_s4), .row4(n8_bit_register_7_s3), .row5(n8_bit_register_7_s2),
    .row6(n8_bit_register_7_s1), .row7(n8_bit_register_7_s0));
  DotMatrix #(.inputtype("row"), .matrixcols(1), .matrixrows(8), .dotshape("circle")) dotmatrix_8 (
    .row0(n8_bit_register_8_s7), .row1(n8_bit_register_8_s6), .row2(n8_bit_register_8_s5),
    .row3(n8_bit_register_8_s4), .row4(n8_bit_register_8_s3), .row5(n8_bit_register_8_s2),
    .row6(n8_bit_register_8_s1), .row7(n8_bit_register_8_s0));
  assign Q8 = Read ? S8 : 1'bz;  // Controlled_Buffer controlled_buffer_1
  _8_Bit_Register u_8_bit_register_1 (
    .Clock(Clock), .Load(and_1_out), .Reset(Clear), .Enable(n4_bit_binary_decoder_1_df),
    .A0(controlled_buffer_16_out), .A1(controlled_buffer_15_out), .A2(controlled_buffer_13_out),
    .A3(controlled_buffer_14_out), .A4(controlled_buffer_11_out), .A5(controlled_buffer_12_out),
    .A6(controlled_buffer_9_out), .A8(controlled_buffer_10_out), .Q0(S1), .Q1(S2), .Q2(S3), .Q3(S4), .Q4(S5),
    .Q5(S6), .Q6(S7), .Q7(S8), .S7(n8_bit_register_1_s7), .S6(n8_bit_register_1_s6),
    .S5(n8_bit_register_1_s5), .S4(n8_bit_register_1_s4), .S3(n8_bit_register_1_s3),
    .S2(n8_bit_register_1_s2), .S1(n8_bit_register_1_s1), .S0(n8_bit_register_1_s0));
  _8_Bit_Register u_8_bit_register_2 (
    .Clock(Clock), .Load(and_2_out), .Reset(Clear), .Enable(n4_bit_binary_decoder_1_de),
    .A0(controlled_buffer_16_out), .A1(controlled_buffer_15_out), .A2(controlled_buffer_13_out),
    .A3(controlled_buffer_14_out), .A4(controlled_buffer_11_out), .A5(controlled_buffer_12_out),
    .A6(controlled_buffer_9_out), .A8(controlled_buffer_10_out), .Q0(S1), .Q1(S2), .Q2(S3), .Q3(S4), .Q4(S5),
    .Q5(S6), .Q6(S7), .Q7(S8), .S7(n8_bit_register_2_s7), .S6(n8_bit_register_2_s6),
    .S5(n8_bit_register_2_s5), .S4(n8_bit_register_2_s4), .S3(n8_bit_register_2_s3),
    .S2(n8_bit_register_2_s2), .S1(n8_bit_register_2_s1), .S0(n8_bit_register_2_s0));
  _8_Bit_Register u_8_bit_register_3 (
    .Clock(Clock), .Load(and_3_out), .Reset(Clear), .Enable(n4_bit_binary_decoder_1_dd),
    .A0(controlled_buffer_16_out), .A1(controlled_buffer_15_out), .A2(controlled_buffer_13_out),
    .A3(controlled_buffer_14_out), .A4(controlled_buffer_11_out), .A5(controlled_buffer_12_out),
    .A6(controlled_buffer_9_out), .A8(controlled_buffer_10_out), .Q0(S1), .Q1(S2), .Q2(S3), .Q3(S4), .Q4(S5),
    .Q5(S6), .Q6(S7), .Q7(S8), .S7(n8_bit_register_3_s7), .S6(n8_bit_register_3_s6),
    .S5(n8_bit_register_3_s5), .S4(n8_bit_register_3_s4), .S3(n8_bit_register_3_s3),
    .S2(n8_bit_register_3_s2), .S1(n8_bit_register_3_s1), .S0(n8_bit_register_3_s0));
  _8_Bit_Register u_8_bit_register_4 (
    .Clock(Clock), .Load(and_4_out), .Reset(Clear), .Enable(n4_bit_binary_decoder_1_dc),
    .A0(controlled_buffer_16_out), .A1(controlled_buffer_15_out), .A2(controlled_buffer_13_out),
    .A3(controlled_buffer_14_out), .A4(controlled_buffer_11_out), .A5(controlled_buffer_12_out),
    .A6(controlled_buffer_9_out), .A8(controlled_buffer_10_out), .Q0(S1), .Q1(S2), .Q2(S3), .Q3(S4), .Q4(S5),
    .Q5(S6), .Q6(S7), .Q7(S8), .S7(n8_bit_register_4_s7), .S6(n8_bit_register_4_s6),
    .S5(n8_bit_register_4_s5), .S4(n8_bit_register_4_s4), .S3(n8_bit_register_4_s3),
    .S2(n8_bit_register_4_s2), .S1(n8_bit_register_4_s1), .S0(n8_bit_register_4_s0));
  _8_Bit_Register u_8_bit_register_5 (
    .Clock(Clock), .Load(and_5_out), .Reset(Clear), .Enable(n4_bit_binary_decoder_1_db),
    .A0(controlled_buffer_16_out), .A1(controlled_buffer_15_out), .A2(controlled_buffer_13_out),
    .A3(controlled_buffer_14_out), .A4(controlled_buffer_11_out), .A5(controlled_buffer_12_out),
    .A6(controlled_buffer_9_out), .A8(controlled_buffer_10_out), .Q0(S1), .Q1(S2), .Q2(S3), .Q3(S4), .Q4(S5),
    .Q5(S6), .Q6(S7), .Q7(S8), .S7(n8_bit_register_5_s7), .S6(n8_bit_register_5_s6),
    .S5(n8_bit_register_5_s5), .S4(n8_bit_register_5_s4), .S3(n8_bit_register_5_s3),
    .S2(n8_bit_register_5_s2), .S1(n8_bit_register_5_s1), .S0(n8_bit_register_5_s0));
  _8_Bit_Register u_8_bit_register_6 (
    .Clock(Clock), .Load(and_6_out), .Reset(Clear), .Enable(n4_bit_binary_decoder_1_da),
    .A0(controlled_buffer_16_out), .A1(controlled_buffer_15_out), .A2(controlled_buffer_13_out),
    .A3(controlled_buffer_14_out), .A4(controlled_buffer_11_out), .A5(controlled_buffer_12_out),
    .A6(controlled_buffer_9_out), .A8(controlled_buffer_10_out), .Q0(S1), .Q1(S2), .Q2(S3), .Q3(S4), .Q4(S5),
    .Q5(S6), .Q6(S7), .Q7(S8), .S7(n8_bit_register_6_s7), .S6(n8_bit_register_6_s6),
    .S5(n8_bit_register_6_s5), .S4(n8_bit_register_6_s4), .S3(n8_bit_register_6_s3),
    .S2(n8_bit_register_6_s2), .S1(n8_bit_register_6_s1), .S0(n8_bit_register_6_s0));
  _8_Bit_Register u_8_bit_register_7 (
    .Clock(Clock), .Load(and_7_out), .Reset(Clear), .Enable(n4_bit_binary_decoder_1_d9),
    .A0(controlled_buffer_16_out), .A1(controlled_buffer_15_out), .A2(controlled_buffer_13_out),
    .A3(controlled_buffer_14_out), .A4(controlled_buffer_11_out), .A5(controlled_buffer_12_out),
    .A6(controlled_buffer_9_out), .A8(controlled_buffer_10_out), .Q0(S1), .Q1(S2), .Q2(S3), .Q3(S4), .Q4(S5),
    .Q5(S6), .Q6(S7), .Q7(S8), .S7(n8_bit_register_7_s7), .S6(n8_bit_register_7_s6),
    .S5(n8_bit_register_7_s5), .S4(n8_bit_register_7_s4), .S3(n8_bit_register_7_s3),
    .S2(n8_bit_register_7_s2), .S1(n8_bit_register_7_s1), .S0(n8_bit_register_7_s0));
  _8_Bit_Register u_8_bit_register_8 (
    .Clock(Clock), .Load(and_8_out), .Reset(Clear), .Enable(n4_bit_binary_decoder_1_d8),
    .A0(controlled_buffer_16_out), .A1(controlled_buffer_15_out), .A2(controlled_buffer_13_out),
    .A3(controlled_buffer_14_out), .A4(controlled_buffer_11_out), .A5(controlled_buffer_12_out),
    .A6(controlled_buffer_9_out), .A8(controlled_buffer_10_out), .Q0(S1), .Q1(S2), .Q2(S3), .Q3(S4), .Q4(S5),
    .Q5(S6), .Q6(S7), .Q7(S8), .S7(n8_bit_register_8_s7), .S6(n8_bit_register_8_s6),
    .S5(n8_bit_register_8_s5), .S4(n8_bit_register_8_s4), .S3(n8_bit_register_8_s3),
    .S2(n8_bit_register_8_s2), .S1(n8_bit_register_8_s1), .S0(n8_bit_register_8_s0));
  assign Q7 = Read ? S7 : 1'bz;  // Controlled_Buffer controlled_buffer_2
  assign Q6 = Read ? S6 : 1'bz;  // Controlled_Buffer controlled_buffer_3
  assign Q5 = Read ? S5 : 1'bz;  // Controlled_Buffer controlled_buffer_4
  assign Q4 = Read ? S4 : 1'bz;  // Controlled_Buffer controlled_buffer_5
  and and_1 (and_1_out, n4_bit_binary_decoder_1_df, Write);
  and and_2 (and_2_out, n4_bit_binary_decoder_1_de, Write);
  and and_3 (and_3_out, n4_bit_binary_decoder_1_dd, Write);
  and and_4 (and_4_out, n4_bit_binary_decoder_1_dc, Write);
  and and_5 (and_5_out, n4_bit_binary_decoder_1_db, Write);
  and and_6 (and_6_out, n4_bit_binary_decoder_1_da, Write);
  and and_7 (and_7_out, n4_bit_binary_decoder_1_d9, Write);
  and and_8 (and_8_out, n4_bit_binary_decoder_1_d8, Write);
  assign Q2 = Read ? S2 : 1'bz;  // Controlled_Buffer controlled_buffer_6
  assign Q3 = Read ? S3 : 1'bz;  // Controlled_Buffer controlled_buffer_7
  assign Q1 = Read ? S1 : 1'bz;  // Controlled_Buffer controlled_buffer_8
  assign controlled_buffer_9_out = Write ? A7 : 1'bz;  // Controlled_Buffer controlled_buffer_9
  assign controlled_buffer_10_out = Write ? A8 : 1'bz;  // Controlled_Buffer controlled_buffer_10
  assign controlled_buffer_11_out = Write ? A5 : 1'bz;  // Controlled_Buffer controlled_buffer_11
  assign controlled_buffer_12_out = Write ? A6 : 1'bz;  // Controlled_Buffer controlled_buffer_12
  DotMatrix #(.inputtype("row"), .matrixcols(1), .matrixrows(8), .dotshape("circle")) dotmatrix_9 (
    .row0(n8_bit_register_9_s7), .row1(n8_bit_register_9_s6), .row2(n8_bit_register_9_s5),
    .row3(n8_bit_register_9_s4), .row4(n8_bit_register_9_s3), .row5(n8_bit_register_9_s2),
    .row6(n8_bit_register_9_s1), .row7(n8_bit_register_9_s0));
  DotMatrix #(.inputtype("row"), .matrixcols(1), .matrixrows(8), .dotshape("circle")) dotmatrix_10 (
    .row0(n8_bit_register_10_s7), .row1(n8_bit_register_10_s6), .row2(n8_bit_register_10_s5),
    .row3(n8_bit_register_10_s4), .row4(n8_bit_register_10_s3), .row5(n8_bit_register_10_s2),
    .row6(n8_bit_register_10_s1), .row7(n8_bit_register_10_s0));
  DotMatrix #(.inputtype("row"), .matrixcols(1), .matrixrows(8), .dotshape("circle")) dotmatrix_11 (
    .row0(n8_bit_register_11_s7), .row1(n8_bit_register_11_s6), .row2(n8_bit_register_11_s5),
    .row3(n8_bit_register_11_s4), .row4(n8_bit_register_11_s3), .row5(n8_bit_register_11_s2),
    .row6(n8_bit_register_11_s1), .row7(n8_bit_register_11_s0));
  DotMatrix #(.inputtype("row"), .matrixcols(1), .matrixrows(8), .dotshape("circle")) dotmatrix_12 (
    .row0(n8_bit_register_12_s7), .row1(n8_bit_register_12_s6), .row2(n8_bit_register_12_s5),
    .row3(n8_bit_register_12_s4), .row4(n8_bit_register_12_s3), .row5(n8_bit_register_12_s2),
    .row6(n8_bit_register_12_s1), .row7(n8_bit_register_12_s0));
  DotMatrix #(.inputtype("row"), .matrixcols(1), .matrixrows(8), .dotshape("circle")) dotmatrix_13 (
    .row0(n8_bit_register_13_s7), .row1(n8_bit_register_13_s6), .row2(n8_bit_register_13_s5),
    .row3(n8_bit_register_13_s4), .row4(n8_bit_register_13_s3), .row5(n8_bit_register_13_s2),
    .row6(n8_bit_register_13_s1), .row7(n8_bit_register_13_s0));
  DotMatrix #(.inputtype("row"), .matrixcols(1), .matrixrows(8), .dotshape("circle")) dotmatrix_14 (
    .row0(n8_bit_register_14_s7), .row1(n8_bit_register_14_s6), .row2(n8_bit_register_14_s5),
    .row3(n8_bit_register_14_s4), .row4(n8_bit_register_14_s3), .row5(n8_bit_register_14_s2),
    .row6(n8_bit_register_14_s1), .row7(n8_bit_register_14_s0));
  DotMatrix #(.inputtype("row"), .matrixcols(1), .matrixrows(8), .dotshape("circle")) dotmatrix_15 (
    .row0(n8_bit_register_15_s7), .row1(n8_bit_register_15_s6), .row2(n8_bit_register_15_s5),
    .row3(n8_bit_register_15_s4), .row4(n8_bit_register_15_s3), .row5(n8_bit_register_15_s2),
    .row6(n8_bit_register_15_s1), .row7(n8_bit_register_15_s0));
  DotMatrix #(.inputtype("row"), .matrixcols(1), .matrixrows(8), .dotshape("circle")) dotmatrix_16 (
    .row0(n8_bit_register_16_s7), .row1(n8_bit_register_16_s6), .row2(n8_bit_register_16_s5),
    .row3(n8_bit_register_16_s4), .row4(n8_bit_register_16_s3), .row5(n8_bit_register_16_s2),
    .row6(n8_bit_register_16_s1), .row7(n8_bit_register_16_s0));
  assign controlled_buffer_13_out = Write ? A3 : 1'bz;  // Controlled_Buffer controlled_buffer_13
  assign controlled_buffer_14_out = Write ? A4 : 1'bz;  // Controlled_Buffer controlled_buffer_14
  assign controlled_buffer_15_out = Write ? A2 : 1'bz;  // Controlled_Buffer controlled_buffer_15
  assign controlled_buffer_16_out = Write ? A1 : 1'bz;  // Controlled_Buffer controlled_buffer_16
  _8_Bit_Register u_8_bit_register_9 (
    .Clock(Clock), .Load(and_9_out), .Reset(Clear), .Enable(n4_bit_binary_decoder_1_d0),
    .A0(controlled_buffer_16_out), .A1(controlled_buffer_15_out), .A2(controlled_buffer_13_out),
    .A3(controlled_buffer_14_out), .A4(controlled_buffer_11_out), .A5(controlled_buffer_12_out),
    .A6(controlled_buffer_9_out), .A8(controlled_buffer_10_out), .Q0(S1), .Q1(S2), .Q2(S3), .Q3(S4), .Q4(S5),
    .Q5(S6), .Q6(S7), .Q7(S8), .S7(n8_bit_register_9_s7), .S6(n8_bit_register_9_s6),
    .S5(n8_bit_register_9_s5), .S4(n8_bit_register_9_s4), .S3(n8_bit_register_9_s3),
    .S2(n8_bit_register_9_s2), .S1(n8_bit_register_9_s1), .S0(n8_bit_register_9_s0));
  _8_Bit_Register u_8_bit_register_10 (
    .Clock(Clock), .Load(and_10_out), .Reset(Clear), .Enable(n4_bit_binary_decoder_1_d1),
    .A0(controlled_buffer_16_out), .A1(controlled_buffer_15_out), .A2(controlled_buffer_13_out),
    .A3(controlled_buffer_14_out), .A4(controlled_buffer_11_out), .A5(controlled_buffer_12_out),
    .A6(controlled_buffer_9_out), .A8(controlled_buffer_10_out), .Q0(S1), .Q1(S2), .Q2(S3), .Q3(S4), .Q4(S5),
    .Q5(S6), .Q6(S7), .Q7(S8), .S7(n8_bit_register_10_s7), .S6(n8_bit_register_10_s6),
    .S5(n8_bit_register_10_s5), .S4(n8_bit_register_10_s4), .S3(n8_bit_register_10_s3),
    .S2(n8_bit_register_10_s2), .S1(n8_bit_register_10_s1), .S0(n8_bit_register_10_s0));
  _8_Bit_Register u_8_bit_register_11 (
    .Clock(Clock), .Load(and_11_out), .Reset(Clear), .Enable(n4_bit_binary_decoder_1_d2),
    .A0(controlled_buffer_16_out), .A1(controlled_buffer_15_out), .A2(controlled_buffer_13_out),
    .A3(controlled_buffer_14_out), .A4(controlled_buffer_11_out), .A5(controlled_buffer_12_out),
    .A6(controlled_buffer_9_out), .A8(controlled_buffer_10_out), .Q0(S1), .Q1(S2), .Q2(S3), .Q3(S4), .Q4(S5),
    .Q5(S6), .Q6(S7), .Q7(S8), .S7(n8_bit_register_11_s7), .S6(n8_bit_register_11_s6),
    .S5(n8_bit_register_11_s5), .S4(n8_bit_register_11_s4), .S3(n8_bit_register_11_s3),
    .S2(n8_bit_register_11_s2), .S1(n8_bit_register_11_s1), .S0(n8_bit_register_11_s0));
  _8_Bit_Register u_8_bit_register_12 (
    .Clock(Clock), .Load(and_12_out), .Reset(Clear), .Enable(n4_bit_binary_decoder_1_d3),
    .A0(controlled_buffer_16_out), .A1(controlled_buffer_15_out), .A2(controlled_buffer_13_out),
    .A3(controlled_buffer_14_out), .A4(controlled_buffer_11_out), .A5(controlled_buffer_12_out),
    .A6(controlled_buffer_9_out), .A8(controlled_buffer_10_out), .Q0(S1), .Q1(S2), .Q2(S3), .Q3(S4), .Q4(S5),
    .Q5(S6), .Q6(S7), .Q7(S8), .S7(n8_bit_register_12_s7), .S6(n8_bit_register_12_s6),
    .S5(n8_bit_register_12_s5), .S4(n8_bit_register_12_s4), .S3(n8_bit_register_12_s3),
    .S2(n8_bit_register_12_s2), .S1(n8_bit_register_12_s1), .S0(n8_bit_register_12_s0));
  _8_Bit_Register u_8_bit_register_13 (
    .Clock(Clock), .Load(and_13_out), .Reset(Clear), .Enable(n4_bit_binary_decoder_1_d4),
    .A0(controlled_buffer_16_out), .A1(controlled_buffer_15_out), .A2(controlled_buffer_13_out),
    .A3(controlled_buffer_14_out), .A4(controlled_buffer_11_out), .A5(controlled_buffer_12_out),
    .A6(controlled_buffer_9_out), .A8(controlled_buffer_10_out), .Q0(S1), .Q1(S2), .Q2(S3), .Q3(S4), .Q4(S5),
    .Q5(S6), .Q6(S7), .Q7(S8), .S7(n8_bit_register_13_s7), .S6(n8_bit_register_13_s6),
    .S5(n8_bit_register_13_s5), .S4(n8_bit_register_13_s4), .S3(n8_bit_register_13_s3),
    .S2(n8_bit_register_13_s2), .S1(n8_bit_register_13_s1), .S0(n8_bit_register_13_s0));
  _8_Bit_Register u_8_bit_register_14 (
    .Clock(Clock), .Load(and_14_out), .Reset(Clear), .Enable(n4_bit_binary_decoder_1_d5),
    .A0(controlled_buffer_16_out), .A1(controlled_buffer_15_out), .A2(controlled_buffer_13_out),
    .A3(controlled_buffer_14_out), .A4(controlled_buffer_11_out), .A5(controlled_buffer_12_out),
    .A6(controlled_buffer_9_out), .A8(controlled_buffer_10_out), .Q0(S1), .Q1(S2), .Q2(S3), .Q3(S4), .Q4(S5),
    .Q5(S6), .Q6(S7), .Q7(S8), .S7(n8_bit_register_14_s7), .S6(n8_bit_register_14_s6),
    .S5(n8_bit_register_14_s5), .S4(n8_bit_register_14_s4), .S3(n8_bit_register_14_s3),
    .S2(n8_bit_register_14_s2), .S1(n8_bit_register_14_s1), .S0(n8_bit_register_14_s0));
  _8_Bit_Register u_8_bit_register_15 (
    .Clock(Clock), .Load(and_15_out), .Reset(Clear), .Enable(n4_bit_binary_decoder_1_d6),
    .A0(controlled_buffer_16_out), .A1(controlled_buffer_15_out), .A2(controlled_buffer_13_out),
    .A3(controlled_buffer_14_out), .A4(controlled_buffer_11_out), .A5(controlled_buffer_12_out),
    .A6(controlled_buffer_9_out), .A8(controlled_buffer_10_out), .Q0(S1), .Q1(S2), .Q2(S3), .Q3(S4), .Q4(S5),
    .Q5(S6), .Q6(S7), .Q7(S8), .S7(n8_bit_register_15_s7), .S6(n8_bit_register_15_s6),
    .S5(n8_bit_register_15_s5), .S4(n8_bit_register_15_s4), .S3(n8_bit_register_15_s3),
    .S2(n8_bit_register_15_s2), .S1(n8_bit_register_15_s1), .S0(n8_bit_register_15_s0));
  _8_Bit_Register u_8_bit_register_16 (
    .Clock(Clock), .Load(and_16_out), .Reset(Clear), .Enable(n4_bit_binary_decoder_1_d7),
    .A0(controlled_buffer_16_out), .A1(controlled_buffer_15_out), .A2(controlled_buffer_13_out),
    .A3(controlled_buffer_14_out), .A4(controlled_buffer_11_out), .A5(controlled_buffer_12_out),
    .A6(controlled_buffer_9_out), .A8(controlled_buffer_10_out), .Q0(S1), .Q1(S2), .Q2(S3), .Q3(S4), .Q4(S5),
    .Q5(S6), .Q6(S7), .Q7(S8), .S7(n8_bit_register_16_s7), .S6(n8_bit_register_16_s6),
    .S5(n8_bit_register_16_s5), .S4(n8_bit_register_16_s4), .S3(n8_bit_register_16_s3),
    .S2(n8_bit_register_16_s2), .S1(n8_bit_register_16_s1), .S0(n8_bit_register_16_s0));
  and and_9 (and_9_out, Write, n4_bit_binary_decoder_1_d0);
  and and_10 (and_10_out, Write, n4_bit_binary_decoder_1_d1);
  and and_11 (and_11_out, Write, n4_bit_binary_decoder_1_d2);
  and and_12 (and_12_out, Write, n4_bit_binary_decoder_1_d3);
  and and_13 (and_13_out, Write, n4_bit_binary_decoder_1_d4);
  and and_14 (and_14_out, Write, n4_bit_binary_decoder_1_d5);
  and and_15 (and_15_out, Write, n4_bit_binary_decoder_1_d6);
  and and_16 (and_16_out, Write, n4_bit_binary_decoder_1_d7);
endmodule
module _256_Byte_SRAM (
  input  A8,
  input  A7,
  input  A6,
  input  A5,
  input  A4,
  input  A3,
  input  A2,
  input  A1,
  input  Read,
  input  Write,
  input  Clear,
  input  Clock,
  input  A1_2,
  input  A2_2,
  input  A3_2,
  input  A4_2,
  input  A5_2,
  input  A6_2,
  input  A7_2,
  input  A8_2,
  output S8,
  output S7,
  output S6,
  output S5,
  output S4,
  output S3,
  output S2,
  output S1,
  output Q8,
  output Q7,
  output Q6,
  output Q5,
  output Q4,
  output Q3,
  output Q2,
  output Q1
);

  wire and_1_out, and_2_out, and_3_out, and_4_out, and_5_out, and_6_out, and_7_out, and_8_out, and_9_out,
       and_10_out, and_11_out, and_12_out, and_13_out, and_14_out, and_15_out, and_16_out,
       controlled_buffer_9_out, controlled_buffer_10_out, controlled_buffer_11_out, controlled_buffer_12_out,
       controlled_buffer_13_out, controlled_buffer_14_out, controlled_buffer_15_out,
       controlled_buffer_16_out, n4_bit_binary_decoder_1_d0, n4_bit_binary_decoder_1_d1,
       n4_bit_binary_decoder_1_d2, n4_bit_binary_decoder_1_d3, n4_bit_binary_decoder_1_d4,
       n4_bit_binary_decoder_1_d5, n4_bit_binary_decoder_1_d6, n4_bit_binary_decoder_1_d7,
       n4_bit_binary_decoder_1_d8, n4_bit_binary_decoder_1_d9, n4_bit_binary_decoder_1_da,
       n4_bit_binary_decoder_1_db, n4_bit_binary_decoder_1_dc, n4_bit_binary_decoder_1_dd,
       n4_bit_binary_decoder_1_de, n4_bit_binary_decoder_1_df, n16_byte_sram_1_s1, n16_byte_sram_1_s2,
       n16_byte_sram_1_s3, n16_byte_sram_1_s4, n16_byte_sram_1_s5, n16_byte_sram_1_s6, n16_byte_sram_1_s7,
       n16_byte_sram_1_s8, n16_byte_sram_2_s1, n16_byte_sram_2_s2, n16_byte_sram_2_s3, n16_byte_sram_2_s4,
       n16_byte_sram_2_s5, n16_byte_sram_2_s6, n16_byte_sram_2_s7, n16_byte_sram_2_s8, n16_byte_sram_3_s1,
       n16_byte_sram_3_s2, n16_byte_sram_3_s3, n16_byte_sram_3_s4, n16_byte_sram_3_s5, n16_byte_sram_3_s6,
       n16_byte_sram_3_s7, n16_byte_sram_3_s8, n16_byte_sram_4_s1, n16_byte_sram_4_s2, n16_byte_sram_4_s3,
       n16_byte_sram_4_s4, n16_byte_sram_4_s5, n16_byte_sram_4_s6, n16_byte_sram_4_s7, n16_byte_sram_4_s8,
       n16_byte_sram_5_s1, n16_byte_sram_5_s2, n16_byte_sram_5_s3, n16_byte_sram_5_s4, n16_byte_sram_5_s5,
       n16_byte_sram_5_s6, n16_byte_sram_5_s7, n16_byte_sram_5_s8, n16_byte_sram_6_s1, n16_byte_sram_6_s2,
       n16_byte_sram_6_s3, n16_byte_sram_6_s4, n16_byte_sram_6_s5, n16_byte_sram_6_s6, n16_byte_sram_6_s7,
       n16_byte_sram_6_s8, n16_byte_sram_7_s1, n16_byte_sram_7_s2, n16_byte_sram_7_s3, n16_byte_sram_7_s4,
       n16_byte_sram_7_s5, n16_byte_sram_7_s6, n16_byte_sram_7_s7, n16_byte_sram_7_s8, n16_byte_sram_8_s1,
       n16_byte_sram_8_s2, n16_byte_sram_8_s3, n16_byte_sram_8_s4, n16_byte_sram_8_s5, n16_byte_sram_8_s6,
       n16_byte_sram_8_s7, n16_byte_sram_8_s8, n16_byte_sram_9_s1, n16_byte_sram_9_s2, n16_byte_sram_9_s3,
       n16_byte_sram_9_s4, n16_byte_sram_9_s5, n16_byte_sram_9_s6, n16_byte_sram_9_s7, n16_byte_sram_9_s8,
       n16_byte_sram_10_s1, n16_byte_sram_10_s2, n16_byte_sram_10_s3, n16_byte_sram_10_s4,
       n16_byte_sram_10_s5, n16_byte_sram_10_s6, n16_byte_sram_10_s7, n16_byte_sram_10_s8,
       n16_byte_sram_11_s1, n16_byte_sram_11_s2, n16_byte_sram_11_s3, n16_byte_sram_11_s4,
       n16_byte_sram_11_s5, n16_byte_sram_11_s6, n16_byte_sram_11_s7, n16_byte_sram_11_s8,
       n16_byte_sram_12_s1, n16_byte_sram_12_s2, n16_byte_sram_12_s3, n16_byte_sram_12_s4,
       n16_byte_sram_12_s5, n16_byte_sram_12_s6, n16_byte_sram_12_s7, n16_byte_sram_12_s8,
       n16_byte_sram_13_s1, n16_byte_sram_13_s2, n16_byte_sram_13_s3, n16_byte_sram_13_s4,
       n16_byte_sram_13_s5, n16_byte_sram_13_s6, n16_byte_sram_13_s7, n16_byte_sram_13_s8,
       n16_byte_sram_14_s1, n16_byte_sram_14_s2, n16_byte_sram_14_s3, n16_byte_sram_14_s4,
       n16_byte_sram_14_s5, n16_byte_sram_14_s6, n16_byte_sram_14_s7, n16_byte_sram_14_s8,
       n16_byte_sram_15_s1, n16_byte_sram_15_s2, n16_byte_sram_15_s3, n16_byte_sram_15_s4,
       n16_byte_sram_15_s5, n16_byte_sram_15_s6, n16_byte_sram_15_s7, n16_byte_sram_15_s8,
       n16_byte_sram_16_s1, n16_byte_sram_16_s2, n16_byte_sram_16_s3, n16_byte_sram_16_s4,
       n16_byte_sram_16_s5, n16_byte_sram_16_s6, n16_byte_sram_16_s7, n16_byte_sram_16_s8;

  _4_bit_binary_decoder u_4_bit_binary_decoder_1 (
    .D0(n4_bit_binary_decoder_1_d0), .D1(n4_bit_binary_decoder_1_d1), .D2(n4_bit_binary_decoder_1_d2),
    .D3(n4_bit_binary_decoder_1_d3), .D4(n4_bit_binary_decoder_1_d4), .D5(n4_bit_binary_decoder_1_d5),
    .D6(n4_bit_binary_decoder_1_d6), .D7(n4_bit_binary_decoder_1_d7), .D8(n4_bit_binary_decoder_1_d8),
    .D9(n4_bit_binary_decoder_1_d9), .DA(n4_bit_binary_decoder_1_da), .DB(n4_bit_binary_decoder_1_db),
    .DC(n4_bit_binary_decoder_1_dc), .DD(n4_bit_binary_decoder_1_dd), .DE(n4_bit_binary_decoder_1_de),
    .DF(n4_bit_binary_decoder_1_df), .Enable(1'b1), .A0(A5_2), .A1(A6_2), .A2(A7_2), .A3(A8_2));
  and and_1 (and_1_out, n4_bit_binary_decoder_1_d7, Write);
  and and_2 (and_2_out, n4_bit_binary_decoder_1_d6, Write);
  and and_3 (and_3_out, n4_bit_binary_decoder_1_d5, Write);
  and and_4 (and_4_out, n4_bit_binary_decoder_1_d4, Write);
  and and_5 (and_5_out, n4_bit_binary_decoder_1_d3, Write);
  and and_6 (and_6_out, n4_bit_binary_decoder_1_d2, Write);
  and and_7 (and_7_out, n4_bit_binary_decoder_1_d1, Write);
  and and_8 (and_8_out, n4_bit_binary_decoder_1_d0, Write);
  assign Q8 = Read ? S8 : 1'bz;  // Controlled_Buffer controlled_buffer_1
  _16_Byte_SRAM u_16_byte_sram_1 (
    .Read(n4_bit_binary_decoder_1_d7), .Write(and_1_out), .Clear(Clear), .A1_2(A1_2), .A2_2(A2_2),
    .A3_2(A3_2), .A4_2(A4_2), .S8(n16_byte_sram_1_s8), .S7(n16_byte_sram_1_s7), .S6(n16_byte_sram_1_s6),
    .S5(n16_byte_sram_1_s5), .S4(n16_byte_sram_1_s4), .S3(n16_byte_sram_1_s3), .S2(n16_byte_sram_1_s2),
    .S1(n16_byte_sram_1_s1), .Q8(S8), .Q7(S7), .Q6(S6), .Q5(S5), .Q4(S4), .Q3(S3), .Q2(S2), .Q1(S1),
    .A8(controlled_buffer_12_out), .A7(controlled_buffer_11_out), .A6(controlled_buffer_9_out),
    .A5(controlled_buffer_10_out), .A4(controlled_buffer_16_out), .A3(controlled_buffer_15_out),
    .A2(controlled_buffer_13_out), .A1(controlled_buffer_14_out), .Clock(Clock));
  DotMatrix #(.matrixcols(8), .matrixrows(1), .dotshape("circle")) dotmatrix_1 (
    .col0(n16_byte_sram_1_s8), .col1(n16_byte_sram_1_s7), .col2(n16_byte_sram_1_s6),
    .col3(n16_byte_sram_1_s5), .col4(n16_byte_sram_1_s4), .col5(n16_byte_sram_1_s3),
    .col6(n16_byte_sram_1_s2), .col7(n16_byte_sram_1_s1));
  _16_Byte_SRAM u_16_byte_sram_2 (
    .Read(n4_bit_binary_decoder_1_d6), .Write(and_2_out), .Clear(Clear), .A1_2(A1_2), .A2_2(A2_2),
    .A3_2(A3_2), .A4_2(A4_2), .S8(n16_byte_sram_2_s8), .S7(n16_byte_sram_2_s7), .S6(n16_byte_sram_2_s6),
    .S5(n16_byte_sram_2_s5), .S4(n16_byte_sram_2_s4), .S3(n16_byte_sram_2_s3), .S2(n16_byte_sram_2_s2),
    .S1(n16_byte_sram_2_s1), .Q8(S8), .Q7(S7), .Q6(S6), .Q5(S5), .Q4(S4), .Q3(S3), .Q2(S2), .Q1(S1),
    .A8(controlled_buffer_12_out), .A7(controlled_buffer_11_out), .A6(controlled_buffer_9_out),
    .A5(controlled_buffer_10_out), .A4(controlled_buffer_16_out), .A3(controlled_buffer_15_out),
    .A2(controlled_buffer_13_out), .A1(controlled_buffer_14_out), .Clock(Clock));
  DotMatrix #(.matrixcols(8), .matrixrows(1), .dotshape("circle")) dotmatrix_2 (
    .col0(n16_byte_sram_2_s8), .col1(n16_byte_sram_2_s7), .col2(n16_byte_sram_2_s6),
    .col3(n16_byte_sram_2_s5), .col4(n16_byte_sram_2_s4), .col5(n16_byte_sram_2_s3),
    .col6(n16_byte_sram_2_s2), .col7(n16_byte_sram_2_s1));
  _16_Byte_SRAM u_16_byte_sram_3 (
    .Read(n4_bit_binary_decoder_1_d5), .Write(and_3_out), .Clear(Clear), .A1_2(A1_2), .A2_2(A2_2),
    .A3_2(A3_2), .A4_2(A4_2), .S8(n16_byte_sram_3_s8), .S7(n16_byte_sram_3_s7), .S6(n16_byte_sram_3_s6),
    .S5(n16_byte_sram_3_s5), .S4(n16_byte_sram_3_s4), .S3(n16_byte_sram_3_s3), .S2(n16_byte_sram_3_s2),
    .S1(n16_byte_sram_3_s1), .Q8(S8), .Q7(S7), .Q6(S6), .Q5(S5), .Q4(S4), .Q3(S3), .Q2(S2), .Q1(S1),
    .A8(controlled_buffer_12_out), .A7(controlled_buffer_11_out), .A6(controlled_buffer_9_out),
    .A5(controlled_buffer_10_out), .A4(controlled_buffer_16_out), .A3(controlled_buffer_15_out),
    .A2(controlled_buffer_13_out), .A1(controlled_buffer_14_out), .Clock(Clock));
  DotMatrix #(.matrixcols(8), .matrixrows(1), .dotshape("circle")) dotmatrix_3 (
    .col0(n16_byte_sram_3_s8), .col1(n16_byte_sram_3_s7), .col2(n16_byte_sram_3_s6),
    .col3(n16_byte_sram_3_s5), .col4(n16_byte_sram_3_s4), .col5(n16_byte_sram_3_s3),
    .col6(n16_byte_sram_3_s2), .col7(n16_byte_sram_3_s1));
  _16_Byte_SRAM u_16_byte_sram_4 (
    .Read(n4_bit_binary_decoder_1_d4), .Write(and_4_out), .Clear(Clear), .A1_2(A1_2), .A2_2(A2_2),
    .A3_2(A3_2), .A4_2(A4_2), .S8(n16_byte_sram_4_s8), .S7(n16_byte_sram_4_s7), .S6(n16_byte_sram_4_s6),
    .S5(n16_byte_sram_4_s5), .S4(n16_byte_sram_4_s4), .S3(n16_byte_sram_4_s3), .S2(n16_byte_sram_4_s2),
    .S1(n16_byte_sram_4_s1), .Q8(S8), .Q7(S7), .Q6(S6), .Q5(S5), .Q4(S4), .Q3(S3), .Q2(S2), .Q1(S1),
    .A8(controlled_buffer_12_out), .A7(controlled_buffer_11_out), .A6(controlled_buffer_9_out),
    .A5(controlled_buffer_10_out), .A4(controlled_buffer_16_out), .A3(controlled_buffer_15_out),
    .A2(controlled_buffer_13_out), .A1(controlled_buffer_14_out), .Clock(Clock));
  DotMatrix #(.matrixcols(8), .matrixrows(1), .dotshape("circle")) dotmatrix_4 (
    .col0(n16_byte_sram_4_s8), .col1(n16_byte_sram_4_s7), .col2(n16_byte_sram_4_s6),
    .col3(n16_byte_sram_4_s5), .col4(n16_byte_sram_4_s4), .col5(n16_byte_sram_4_s3),
    .col6(n16_byte_sram_4_s2), .col7(n16_byte_sram_4_s1));
  _16_Byte_SRAM u_16_byte_sram_5 (
    .Read(n4_bit_binary_decoder_1_d3), .Write(and_5_out), .Clear(Clear), .A1_2(A1_2), .A2_2(A2_2),
    .A3_2(A3_2), .A4_2(A4_2), .S8(n16_byte_sram_5_s8), .S7(n16_byte_sram_5_s7), .S6(n16_byte_sram_5_s6),
    .S5(n16_byte_sram_5_s5), .S4(n16_byte_sram_5_s4), .S3(n16_byte_sram_5_s3), .S2(n16_byte_sram_5_s2),
    .S1(n16_byte_sram_5_s1), .Q8(S8), .Q7(S7), .Q6(S6), .Q5(S5), .Q4(S4), .Q3(S3), .Q2(S2), .Q1(S1),
    .A8(controlled_buffer_12_out), .A7(controlled_buffer_11_out), .A6(controlled_buffer_9_out),
    .A5(controlled_buffer_10_out), .A4(controlled_buffer_16_out), .A3(controlled_buffer_15_out),
    .A2(controlled_buffer_13_out), .A1(controlled_buffer_14_out), .Clock(Clock));
  DotMatrix #(.matrixcols(8), .matrixrows(1), .dotshape("circle")) dotmatrix_5 (
    .col0(n16_byte_sram_5_s8), .col1(n16_byte_sram_5_s7), .col2(n16_byte_sram_5_s6),
    .col3(n16_byte_sram_5_s5), .col4(n16_byte_sram_5_s4), .col5(n16_byte_sram_5_s3),
    .col6(n16_byte_sram_5_s2), .col7(n16_byte_sram_5_s1));
  _16_Byte_SRAM u_16_byte_sram_6 (
    .Read(n4_bit_binary_decoder_1_d2), .Write(and_6_out), .Clear(Clear), .A1_2(A1_2), .A2_2(A2_2),
    .A3_2(A3_2), .A4_2(A4_2), .S8(n16_byte_sram_6_s8), .S7(n16_byte_sram_6_s7), .S6(n16_byte_sram_6_s6),
    .S5(n16_byte_sram_6_s5), .S4(n16_byte_sram_6_s4), .S3(n16_byte_sram_6_s3), .S2(n16_byte_sram_6_s2),
    .S1(n16_byte_sram_6_s1), .Q8(S8), .Q7(S7), .Q6(S6), .Q5(S5), .Q4(S4), .Q3(S3), .Q2(S2), .Q1(S1),
    .A8(controlled_buffer_12_out), .A7(controlled_buffer_11_out), .A6(controlled_buffer_9_out),
    .A5(controlled_buffer_10_out), .A4(controlled_buffer_16_out), .A3(controlled_buffer_15_out),
    .A2(controlled_buffer_13_out), .A1(controlled_buffer_14_out), .Clock(Clock));
  DotMatrix #(.matrixcols(8), .matrixrows(1), .dotshape("circle")) dotmatrix_6 (
    .col0(n16_byte_sram_6_s8), .col1(n16_byte_sram_6_s7), .col2(n16_byte_sram_6_s6),
    .col3(n16_byte_sram_6_s5), .col4(n16_byte_sram_6_s4), .col5(n16_byte_sram_6_s3),
    .col6(n16_byte_sram_6_s2), .col7(n16_byte_sram_6_s1));
  _16_Byte_SRAM u_16_byte_sram_7 (
    .Read(n4_bit_binary_decoder_1_d1), .Write(and_7_out), .Clear(Clear), .A1_2(A1_2), .A2_2(A2_2),
    .A3_2(A3_2), .A4_2(A4_2), .S8(n16_byte_sram_7_s8), .S7(n16_byte_sram_7_s7), .S6(n16_byte_sram_7_s6),
    .S5(n16_byte_sram_7_s5), .S4(n16_byte_sram_7_s4), .S3(n16_byte_sram_7_s3), .S2(n16_byte_sram_7_s2),
    .S1(n16_byte_sram_7_s1), .Q8(S8), .Q7(S7), .Q6(S6), .Q5(S5), .Q4(S4), .Q3(S3), .Q2(S2), .Q1(S1),
    .A8(controlled_buffer_12_out), .A7(controlled_buffer_11_out), .A6(controlled_buffer_9_out),
    .A5(controlled_buffer_10_out), .A4(controlled_buffer_16_out), .A3(controlled_buffer_15_out),
    .A2(controlled_buffer_13_out), .A1(controlled_buffer_14_out), .Clock(Clock));
  DotMatrix #(.matrixcols(8), .matrixrows(1), .dotshape("circle")) dotmatrix_7 (
    .col0(n16_byte_sram_7_s8), .col1(n16_byte_sram_7_s7), .col2(n16_byte_sram_7_s6),
    .col3(n16_byte_sram_7_s5), .col4(n16_byte_sram_7_s4), .col5(n16_byte_sram_7_s3),
    .col6(n16_byte_sram_7_s2), .col7(n16_byte_sram_7_s1));
  _16_Byte_SRAM u_16_byte_sram_8 (
    .Read(n4_bit_binary_decoder_1_d0), .Write(and_8_out), .Clear(Clear), .A1_2(A1_2), .A2_2(A2_2),
    .A3_2(A3_2), .A4_2(A4_2), .S8(n16_byte_sram_8_s8), .S7(n16_byte_sram_8_s7), .S6(n16_byte_sram_8_s6),
    .S5(n16_byte_sram_8_s5), .S4(n16_byte_sram_8_s4), .S3(n16_byte_sram_8_s3), .S2(n16_byte_sram_8_s2),
    .S1(n16_byte_sram_8_s1), .Q8(S8), .Q7(S7), .Q6(S6), .Q5(S5), .Q4(S4), .Q3(S3), .Q2(S2), .Q1(S1),
    .A8(controlled_buffer_12_out), .A7(controlled_buffer_11_out), .A6(controlled_buffer_9_out),
    .A5(controlled_buffer_10_out), .A4(controlled_buffer_16_out), .A3(controlled_buffer_15_out),
    .A2(controlled_buffer_13_out), .A1(controlled_buffer_14_out), .Clock(Clock));
  DotMatrix #(.matrixcols(8), .matrixrows(1), .dotshape("circle")) dotmatrix_8 (
    .col0(n16_byte_sram_8_s8), .col1(n16_byte_sram_8_s7), .col2(n16_byte_sram_8_s6),
    .col3(n16_byte_sram_8_s5), .col4(n16_byte_sram_8_s4), .col5(n16_byte_sram_8_s3),
    .col6(n16_byte_sram_8_s2), .col7(n16_byte_sram_8_s1));
  assign Q4 = Read ? S4 : 1'bz;  // Controlled_Buffer controlled_buffer_2
  assign Q6 = Read ? S6 : 1'bz;  // Controlled_Buffer controlled_buffer_3
  assign Q5 = Read ? S5 : 1'bz;  // Controlled_Buffer controlled_buffer_4
  assign Q7 = Read ? S7 : 1'bz;  // Controlled_Buffer controlled_buffer_5
  assign Q2 = Read ? S2 : 1'bz;  // Controlled_Buffer controlled_buffer_6
  assign Q1 = Read ? S1 : 1'bz;  // Controlled_Buffer controlled_buffer_7
  assign Q3 = Read ? S3 : 1'bz;  // Controlled_Buffer controlled_buffer_8
  assign controlled_buffer_9_out = Write ? A6 : 1'bz;  // Controlled_Buffer controlled_buffer_9
  assign controlled_buffer_10_out = Write ? A5 : 1'bz;  // Controlled_Buffer controlled_buffer_10
  assign controlled_buffer_11_out = Write ? A7 : 1'bz;  // Controlled_Buffer controlled_buffer_11
  assign controlled_buffer_12_out = Write ? A8 : 1'bz;  // Controlled_Buffer controlled_buffer_12
  assign controlled_buffer_13_out = Write ? A2 : 1'bz;  // Controlled_Buffer controlled_buffer_13
  assign controlled_buffer_14_out = Write ? A1 : 1'bz;  // Controlled_Buffer controlled_buffer_14
  assign controlled_buffer_15_out = Write ? A3 : 1'bz;  // Controlled_Buffer controlled_buffer_15
  assign controlled_buffer_16_out = Write ? A4 : 1'bz;  // Controlled_Buffer controlled_buffer_16
  and and_9 (and_9_out, n4_bit_binary_decoder_1_df, Write);
  and and_10 (and_10_out, n4_bit_binary_decoder_1_de, Write);
  and and_11 (and_11_out, n4_bit_binary_decoder_1_dd, Write);
  and and_12 (and_12_out, n4_bit_binary_decoder_1_dc, Write);
  and and_13 (and_13_out, n4_bit_binary_decoder_1_db, Write);
  and and_14 (and_14_out, n4_bit_binary_decoder_1_da, Write);
  and and_15 (and_15_out, n4_bit_binary_decoder_1_d9, Write);
  and and_16 (and_16_out, n4_bit_binary_decoder_1_d8, Write);
  _16_Byte_SRAM u_16_byte_sram_9 (
    .Read(n4_bit_binary_decoder_1_df), .Write(and_9_out), .Clear(Clear), .A1_2(A1_2), .A2_2(A2_2),
    .A3_2(A3_2), .A4_2(A4_2), .S8(n16_byte_sram_9_s8), .S7(n16_byte_sram_9_s7), .S6(n16_byte_sram_9_s6),
    .S5(n16_byte_sram_9_s5), .S4(n16_byte_sram_9_s4), .S3(n16_byte_sram_9_s3), .S2(n16_byte_sram_9_s2),
    .S1(n16_byte_sram_9_s1), .Q8(S8), .Q7(S7), .Q6(S6), .Q5(S5), .Q4(S4), .Q3(S3), .Q2(S2), .Q1(S1),
    .A8(controlled_buffer_12_out), .A7(controlled_buffer_11_out), .A6(controlled_buffer_9_out),
    .A5(controlled_buffer_10_out), .A4(controlled_buffer_16_out), .A3(controlled_buffer_15_out),
    .A2(controlled_buffer_13_out), .A1(controlled_buffer_14_out), .Clock(Clock));
  DotMatrix #(.matrixcols(8), .matrixrows(1), .dotshape("circle")) dotmatrix_9 (
    .col0(n16_byte_sram_9_s8), .col1(n16_byte_sram_9_s7), .col2(n16_byte_sram_9_s6),
    .col3(n16_byte_sram_9_s5), .col4(n16_byte_sram_9_s4), .col5(n16_byte_sram_9_s3),
    .col6(n16_byte_sram_9_s2), .col7(n16_byte_sram_9_s1));
  _16_Byte_SRAM u_16_byte_sram_10 (
    .Read(n4_bit_binary_decoder_1_de), .Write(and_10_out), .Clear(Clear), .A1_2(A1_2), .A2_2(A2_2),
    .A3_2(A3_2), .A4_2(A4_2), .S8(n16_byte_sram_10_s8), .S7(n16_byte_sram_10_s7), .S6(n16_byte_sram_10_s6),
    .S5(n16_byte_sram_10_s5), .S4(n16_byte_sram_10_s4), .S3(n16_byte_sram_10_s3), .S2(n16_byte_sram_10_s2),
    .S1(n16_byte_sram_10_s1), .Q8(S8), .Q7(S7), .Q6(S6), .Q5(S5), .Q4(S4), .Q3(S3), .Q2(S2), .Q1(S1),
    .A8(controlled_buffer_12_out), .A7(controlled_buffer_11_out), .A6(controlled_buffer_9_out),
    .A5(controlled_buffer_10_out), .A4(controlled_buffer_16_out), .A3(controlled_buffer_15_out),
    .A2(controlled_buffer_13_out), .A1(controlled_buffer_14_out), .Clock(Clock));
  DotMatrix #(.matrixcols(8), .matrixrows(1), .dotshape("circle")) dotmatrix_10 (
    .col0(n16_byte_sram_10_s8), .col1(n16_byte_sram_10_s7), .col2(n16_byte_sram_10_s6),
    .col3(n16_byte_sram_10_s5), .col4(n16_byte_sram_10_s4), .col5(n16_byte_sram_10_s3),
    .col6(n16_byte_sram_10_s2), .col7(n16_byte_sram_10_s1));
  _16_Byte_SRAM u_16_byte_sram_11 (
    .Read(n4_bit_binary_decoder_1_dd), .Write(and_11_out), .Clear(Clear), .A1_2(A1_2), .A2_2(A2_2),
    .A3_2(A3_2), .A4_2(A4_2), .S8(n16_byte_sram_11_s8), .S7(n16_byte_sram_11_s7), .S6(n16_byte_sram_11_s6),
    .S5(n16_byte_sram_11_s5), .S4(n16_byte_sram_11_s4), .S3(n16_byte_sram_11_s3), .S2(n16_byte_sram_11_s2),
    .S1(n16_byte_sram_11_s1), .Q8(S8), .Q7(S7), .Q6(S6), .Q5(S5), .Q4(S4), .Q3(S3), .Q2(S2), .Q1(S1),
    .A8(controlled_buffer_12_out), .A7(controlled_buffer_11_out), .A6(controlled_buffer_9_out),
    .A5(controlled_buffer_10_out), .A4(controlled_buffer_16_out), .A3(controlled_buffer_15_out),
    .A2(controlled_buffer_13_out), .A1(controlled_buffer_14_out), .Clock(Clock));
  DotMatrix #(.matrixcols(8), .matrixrows(1), .dotshape("circle")) dotmatrix_11 (
    .col0(n16_byte_sram_11_s8), .col1(n16_byte_sram_11_s7), .col2(n16_byte_sram_11_s6),
    .col3(n16_byte_sram_11_s5), .col4(n16_byte_sram_11_s4), .col5(n16_byte_sram_11_s3),
    .col6(n16_byte_sram_11_s2), .col7(n16_byte_sram_11_s1));
  _16_Byte_SRAM u_16_byte_sram_12 (
    .Read(n4_bit_binary_decoder_1_dc), .Write(and_12_out), .Clear(Clear), .A1_2(A1_2), .A2_2(A2_2),
    .A3_2(A3_2), .A4_2(A4_2), .S8(n16_byte_sram_12_s8), .S7(n16_byte_sram_12_s7), .S6(n16_byte_sram_12_s6),
    .S5(n16_byte_sram_12_s5), .S4(n16_byte_sram_12_s4), .S3(n16_byte_sram_12_s3), .S2(n16_byte_sram_12_s2),
    .S1(n16_byte_sram_12_s1), .Q8(S8), .Q7(S7), .Q6(S6), .Q5(S5), .Q4(S4), .Q3(S3), .Q2(S2), .Q1(S1),
    .A8(controlled_buffer_12_out), .A7(controlled_buffer_11_out), .A6(controlled_buffer_9_out),
    .A5(controlled_buffer_10_out), .A4(controlled_buffer_16_out), .A3(controlled_buffer_15_out),
    .A2(controlled_buffer_13_out), .A1(controlled_buffer_14_out), .Clock(Clock));
  DotMatrix #(.matrixcols(8), .matrixrows(1), .dotshape("circle")) dotmatrix_12 (
    .col0(n16_byte_sram_12_s8), .col1(n16_byte_sram_12_s7), .col2(n16_byte_sram_12_s6),
    .col3(n16_byte_sram_12_s5), .col4(n16_byte_sram_12_s4), .col5(n16_byte_sram_12_s3),
    .col6(n16_byte_sram_12_s2), .col7(n16_byte_sram_12_s1));
  _16_Byte_SRAM u_16_byte_sram_13 (
    .Read(n4_bit_binary_decoder_1_db), .Write(and_13_out), .Clear(Clear), .A1_2(A1_2), .A2_2(A2_2),
    .A3_2(A3_2), .A4_2(A4_2), .S8(n16_byte_sram_13_s8), .S7(n16_byte_sram_13_s7), .S6(n16_byte_sram_13_s6),
    .S5(n16_byte_sram_13_s5), .S4(n16_byte_sram_13_s4), .S3(n16_byte_sram_13_s3), .S2(n16_byte_sram_13_s2),
    .S1(n16_byte_sram_13_s1), .Q8(S8), .Q7(S7), .Q6(S6), .Q5(S5), .Q4(S4), .Q3(S3), .Q2(S2), .Q1(S1),
    .A8(controlled_buffer_12_out), .A7(controlled_buffer_11_out), .A6(controlled_buffer_9_out),
    .A5(controlled_buffer_10_out), .A4(controlled_buffer_16_out), .A3(controlled_buffer_15_out),
    .A2(controlled_buffer_13_out), .A1(controlled_buffer_14_out), .Clock(Clock));
  DotMatrix #(.matrixcols(8), .matrixrows(1), .dotshape("circle")) dotmatrix_13 (
    .col0(n16_byte_sram_13_s8), .col1(n16_byte_sram_13_s7), .col2(n16_byte_sram_13_s6),
    .col3(n16_byte_sram_13_s5), .col4(n16_byte_sram_13_s4), .col5(n16_byte_sram_13_s3),
    .col6(n16_byte_sram_13_s2), .col7(n16_byte_sram_13_s1));
  _16_Byte_SRAM u_16_byte_sram_14 (
    .Read(n4_bit_binary_decoder_1_da), .Write(and_14_out), .Clear(Clear), .A1_2(A1_2), .A2_2(A2_2),
    .A3_2(A3_2), .A4_2(A4_2), .S8(n16_byte_sram_14_s8), .S7(n16_byte_sram_14_s7), .S6(n16_byte_sram_14_s6),
    .S5(n16_byte_sram_14_s5), .S4(n16_byte_sram_14_s4), .S3(n16_byte_sram_14_s3), .S2(n16_byte_sram_14_s2),
    .S1(n16_byte_sram_14_s1), .Q8(S8), .Q7(S7), .Q6(S6), .Q5(S5), .Q4(S4), .Q3(S3), .Q2(S2), .Q1(S1),
    .A8(controlled_buffer_12_out), .A7(controlled_buffer_11_out), .A6(controlled_buffer_9_out),
    .A5(controlled_buffer_10_out), .A4(controlled_buffer_16_out), .A3(controlled_buffer_15_out),
    .A2(controlled_buffer_13_out), .A1(controlled_buffer_14_out), .Clock(Clock));
  DotMatrix #(.matrixcols(8), .matrixrows(1), .dotshape("circle")) dotmatrix_14 (
    .col0(n16_byte_sram_14_s8), .col1(n16_byte_sram_14_s7), .col2(n16_byte_sram_14_s6),
    .col3(n16_byte_sram_14_s5), .col4(n16_byte_sram_14_s4), .col5(n16_byte_sram_14_s3),
    .col6(n16_byte_sram_14_s2), .col7(n16_byte_sram_14_s1));
  _16_Byte_SRAM u_16_byte_sram_15 (
    .Read(n4_bit_binary_decoder_1_d9), .Write(and_15_out), .Clear(Clear), .A1_2(A1_2), .A2_2(A2_2),
    .A3_2(A3_2), .A4_2(A4_2), .S8(n16_byte_sram_15_s8), .S7(n16_byte_sram_15_s7), .S6(n16_byte_sram_15_s6),
    .S5(n16_byte_sram_15_s5), .S4(n16_byte_sram_15_s4), .S3(n16_byte_sram_15_s3), .S2(n16_byte_sram_15_s2),
    .S1(n16_byte_sram_15_s1), .Q8(S8), .Q7(S7), .Q6(S6), .Q5(S5), .Q4(S4), .Q3(S3), .Q2(S2), .Q1(S1),
    .A8(controlled_buffer_12_out), .A7(controlled_buffer_11_out), .A6(controlled_buffer_9_out),
    .A5(controlled_buffer_10_out), .A4(controlled_buffer_16_out), .A3(controlled_buffer_15_out),
    .A2(controlled_buffer_13_out), .A1(controlled_buffer_14_out), .Clock(Clock));
  DotMatrix #(.matrixcols(8), .matrixrows(1), .dotshape("circle")) dotmatrix_15 (
    .col0(n16_byte_sram_15_s8), .col1(n16_byte_sram_15_s7), .col2(n16_byte_sram_15_s6),
    .col3(n16_byte_sram_15_s5), .col4(n16_byte_sram_15_s4), .col5(n16_byte_sram_15_s3),
    .col6(n16_byte_sram_15_s2), .col7(n16_byte_sram_15_s1));
  _16_Byte_SRAM u_16_byte_sram_16 (
    .Read(n4_bit_binary_decoder_1_d8), .Write(and_16_out), .Clear(Clear), .A1_2(A1_2), .A2_2(A2_2),
    .A3_2(A3_2), .A4_2(A4_2), .S8(n16_byte_sram_16_s8), .S7(n16_byte_sram_16_s7), .S6(n16_byte_sram_16_s6),
    .S5(n16_byte_sram_16_s5), .S4(n16_byte_sram_16_s4), .S3(n16_byte_sram_16_s3), .S2(n16_byte_sram_16_s2),
    .S1(n16_byte_sram_16_s1), .Q8(S8), .Q7(S7), .Q6(S6), .Q5(S5), .Q4(S4), .Q3(S3), .Q2(S2), .Q1(S1),
    .A8(controlled_buffer_12_out), .A7(controlled_buffer_11_out), .A6(controlled_buffer_9_out),
    .A5(controlled_buffer_10_out), .A4(controlled_buffer_16_out), .A3(controlled_buffer_15_out),
    .A2(controlled_buffer_13_out), .A1(controlled_buffer_14_out), .Clock(Clock));
  DotMatrix #(.matrixcols(8), .matrixrows(1), .dotshape("circle")) dotmatrix_16 (
    .col0(n16_byte_sram_16_s8), .col1(n16_byte_sram_16_s7), .col2(n16_byte_sram_16_s6),
    .col3(n16_byte_sram_16_s5), .col4(n16_byte_sram_16_s4), .col5(n16_byte_sram_16_s3),
    .col6(n16_byte_sram_16_s2), .col7(n16_byte_sram_16_s1));
endmodule

module Program_Loader (
  input  Enable,
  input  Reset,
  input  [7:0] ROM_Data,
  input  Clock,
  output Q1,
  output [7:0] ROM_Address,
  output Q2,
  output Q3,
  output Q4,
  output Q5,
  output Q6,
  output Q7,
  output Q8,
  output Programming,
  output Address_Write,
  output Data_Write
);

  wire j_k_ff_1_q, j_k_ff_1_qn;
  wire [7:0] controlled_buffer_1_out;

  _8_Bit_Counter u_8_bit_counter_1 (
    .Enable_Out(Enable), .Enable(Enable), .Reset(Reset), .Write(1'b0), .Clock(j_k_ff_1_qn),
    .Q8(ROM_Address[7]), .Q7(ROM_Address[6]), .Q6(ROM_Address[5]), .Q5(ROM_Address[4]), .Q4(ROM_Address[3]),
    .Q3(ROM_Address[2]), .Q2(ROM_Address[1]), .Q1(ROM_Address[0]));  // open: D8, S7, S6, S5, S4, S3, S2, S1, A8, A7, A6, A5, A4, A3, A2, A1
  assign controlled_buffer_1_out = j_k_ff_1_qn ? ROM_Address : 8'bz;  // Controlled_Buffer controlled_buffer_1
  assign controlled_buffer_1_out = j_k_ff_1_q ? ROM_Data : 8'bz;  // Controlled_Buffer controlled_buffer_2
  J_K_Flip_Flop j_k_ff_1 (
    .J(Clock), .clk(Clock), .K(Clock), .Q(j_k_ff_1_q), .Qn(j_k_ff_1_qn), .preset(1'b0), .en(Clock),
    .reset(1'b0));
  and and_1 (Address_Write, j_k_ff_1_qn, Enable);
  and and_2 (Data_Write, Enable, j_k_ff_1_q);
  assign Q1 = Enable ? controlled_buffer_1_out[0] : 1'bz;  // Controlled_Buffer controlled_buffer_3
  assign Q2 = Enable ? controlled_buffer_1_out[1] : 1'bz;  // Controlled_Buffer controlled_buffer_4
  assign Q3 = Enable ? controlled_buffer_1_out[2] : 1'bz;  // Controlled_Buffer controlled_buffer_5
  assign Q4 = Enable ? controlled_buffer_1_out[3] : 1'bz;  // Controlled_Buffer controlled_buffer_6
  assign Q5 = Enable ? controlled_buffer_1_out[4] : 1'bz;  // Controlled_Buffer controlled_buffer_7
  assign Q6 = Enable ? controlled_buffer_1_out[5] : 1'bz;  // Controlled_Buffer controlled_buffer_8
  assign Q7 = Enable ? controlled_buffer_1_out[6] : 1'bz;  // Controlled_Buffer controlled_buffer_9
  assign Q8 = Enable ? controlled_buffer_1_out[7] : 1'bz;  // Controlled_Buffer controlled_buffer_10

  assign Programming = Enable;
endmodule

module Instruction_Decoder (
  input  NF,
  input  VF,
  input  PM,
  input  ZF,
  input  CF,
  input  OP_0,
  input  OP_1,
  input  OP_2,
  input  OP_3,
  input  OP_4,
  input  Reset,
  input  Clock,
  output out_13,
  output out_14,
  output OI,
  output JP,
  output CO,
  output CE,
  output IR,
  output II,
  output RR,
  output RW,
  output MI,
  output BO,
  output BI,
  output CI,
  output EO,
  output ALU_SEL_1,
  output S8,
  output S7,
  output S6,
  output S5,
  output S4,
  output S3,
  output S2,
  output S1,
  output ALU_SEL_2,
  output ALU_SEL_3,
  output AO,
  output AI,
  output HLT,
  output FI
);

  wire n4_bit_binary_decoder_1_d8, n8_bit_counter_1_q4, not_1_out, not_2_out, not_3_out, or_1_out;
  wire [2:0] n8_bit_counter_1_q1;
  wire [20:0] rom_1_data;

  not not_1 (not_1_out, Clock);
  not not_2 (not_2_out, 1'b1);
  or or_1 (or_1_out, Reset, rom_1_data[4], n4_bit_binary_decoder_1_d8);
  _8_Bit_Counter u_8_bit_counter_1 (
    .Enable_Out(1'b1), .Enable(1'b1), .Reset(or_1_out), .Write(not_2_out), .Clock(not_1_out),
    .Q4(n8_bit_counter_1_q4), .Q3(n8_bit_counter_1_q1[2]), .Q2(n8_bit_counter_1_q1[1]),
    .Q1(n8_bit_counter_1_q1[0]));  // open: Q8, Q7, Q6, Q5, D8, S7, S6, S5, S4, S3, S2, S1, A8, A7, A6, A5, A4, A3, A2, A1
  _4_bit_binary_decoder u_4_bit_binary_decoder_1 (
    .D0(S1), .D1(S2), .D2(S3), .D3(S4), .D4(S5), .D5(S6), .D6(S7), .D7(S8), .D8(n4_bit_binary_decoder_1_d8),
    .Enable(1'b1), .A0(n8_bit_counter_1_q1[0]), .A1(n8_bit_counter_1_q1[1]), .A2(n8_bit_counter_1_q1[2]),
    .A3(n8_bit_counter_1_q4));  // open: D9, DA, DB, DC, DD, DE, DF
  ROM #(.addrWidth(10), .dataWidth(21)) rom_1 (
    .addr({OP_4, OP_3, OP_2, OP_1, OP_0, CF, ZF, n8_bit_counter_1_q1}), .data(rom_1_data));  // open: sel
  not not_3 (not_3_out, PM);
  and and_1 (OI, rom_1_data[0], not_3_out);
  and and_2 (JP, rom_1_data[1], not_3_out);
  and and_3 (CO, rom_1_data[2], not_3_out);
  and and_4 (CE, rom_1_data[3], not_3_out);
  and and_5 (IR, rom_1_data[4], not_3_out);
  and and_6 (II, rom_1_data[5], not_3_out);
  and and_7 (RR, rom_1_data[6], not_3_out);
  and and_8 (RW, rom_1_data[7], not_3_out);
  and and_9 (MI, rom_1_data[8], not_3_out);
  and and_10 (BO, rom_1_data[9], not_3_out);
  and and_11 (BI, rom_1_data[10], not_3_out);
  and and_12 (CI, rom_1_data[11], not_3_out);
  and and_13 (EO, rom_1_data[12], not_3_out);
  and and_14 (ALU_SEL_1, rom_1_data[13], not_3_out);
  and and_15 (ALU_SEL_2, rom_1_data[14], not_3_out);
  and and_16 (ALU_SEL_3, rom_1_data[15], not_3_out);
  and and_17 (AO, rom_1_data[16], not_3_out);
  and and_18 (AI, rom_1_data[17], not_3_out);
  and and_19 (HLT, rom_1_data[18], not_3_out);
  and and_20 (FI, rom_1_data[19], not_3_out);

  assign out_13 = NF;
  assign out_14 = VF;

  // Notes on the sheet:
  //   contents of rom_1 (hex, n*v repeats v):
  //   104 68 10 5*0 104 68 10 5*0 104 68 10 5*0 104 68 10 5*0 104 68 40000 10 4*0 104 68 40000 10 4*0 104
  //   68 40000 10 4*0 104 68 40000 10 4*0 104 68 104 20040 10 0 0 0 104 68 104 20040 10 0 0 0 104 68 104
  //   20040 10 0 0 0 104 68 104 20040 10 0 0 0 104 68 10c 140 20040 10 0 0 104 68 10c 140 20040 10 0 0 104
  //   68 10c 140 20040 10 0 0 104 68 10c 140 20040 10 0 0 104 68 10c 140 10080 10 0 0 104 68 10c 140 10080
  //   10 0 0 104 68 10c 140 10080 10 0 0 104 68 10c 140 10080 10 0 0 104 68 10c 440 10 0 0 0 104 68 10c
  //   440 10 0 0 0 104 68 10c 440 10 0 0 0 104 68 10c 440 10 0 0 0 104 68 10c 140 440 10 0 0 104 68 10c
  //   140 440 10 0 0 104 68 10c 140 440 10 0 0 104 68 10c 140 440 10 0 0 104 68 10c 140 280 10 0 0 104 68
  //   10c 140 280 10 0 0 104 68 10c 140 280 10 0 0 104 68 10c 140 280 10 0 0 104 68 10c 440 a1000 10 0 0
  //   104 68 10c 440 a1000 10 0 0 104 68 10c 440 a1000 10 0 0 104 68 10c 440 a1000 10 0 0 104 68 10c 140
  //   440 10 0 0 104 68 10c 140 440 10 0 0 104 68 10c 140 440 10 0 0 104 68 10c 140 440 10 0 0 104 68 10c
  //   c40 a1800 10 0 0 104 68 10c c40 a1800 10 0 0 104 68 10c c40 a1800 10 0 0 104 68 10c c40 a1800 10 0 0
  //   104 68 10c 140 c40 a1800 10 0 104 68 10c 140 c40 a1800 10 0 104 68 10c 140 c40 a1800 10 0 104 68 10c
  //   140 c40 a1800 10 0 104 68 10 10 4*0 104 68 10 10 4*0 104 68 10 10 4*0 104 68 10 10 4*0 104 68 10 10
  //   4*0 104 68 10 10 4*0 104 68 10 10 4*0 104 68 10 10 4*0 104 68 10 10 4*0 104 68 10 10 4*0 104 68 10
  //   10 4*0 104 68 10 10 4*0 104 68 10 10 4*0 104 68 10 10 4*0 104 68 10 10 4*0 104 68 10 10 4*0 104 68
  //   10 10 4*0 104 68 10 10 4*0 104 68 10 10 4*0 104 68 10 10 4*0 104 68 10 10 4*0 104 68 10 10 4*0 104
  //   68 10 10 4*0 104 68 10 10 4*0 104 68 10 10 4*0 104 68 10 10 4*0 104 68 10 10 4*0 104 68 10 10 4*0
  //   104 68 10 10 4*0 104 68 10 10 4*0 104 68 10 10 4*0 104 68 10 10 4*0 104 68 10001 10 4*0 104 68 10001
  //   10 4*0 104 68 10001 10 4*0 104 68 10001 10 4*0 104 68 201 10 4*0 104 68 201 10 4*0 104 68 201 10 4*0
  //   104 68 201 10 4*0 104 68 10c 41 10 0 0 0 104 68 10c 41 10 0 0 0 104 68 10c 41 10 0 0 0 104 68 10c 41
  //   10 0 0 0 104 68 10c 140 41 10 0 0 104 68 10c 140 41 10 0 0 104 68 10c 140 41 10 0 0 104 68 10c 140
  //   41 10 0 0 104 68 10c 42 10 0 0 0 104 68 10c 42 10 0 0 0 104 68 10c 42 10 0 0 0 104 68 10c 42 10 0 0
  //   0 104 68 8 10 4*0 104 68 8 10 4*0 104 68 8 10 4*0 104 68 8 10 4*0 104 68 10c 42 10 0 0 0 104 68 10c
  //   42 10 0 0 0 104 68 10c 42 10 0 0 0 104 68 10c 42 10 0 0 0 104 68 10 10 4*0 104 68 10 10 4*0 104 68
  //   10 10 4*0 104 68 10 10
endmodule

module _8_Bit_Processor_old (
  input  Reset,
  input  Reset_RAM,
  input  in_3,
  input  in_4,
  input  in_5,
  output Programming
);

  wire and_1_out, clock_1_out, instruction_decoder_1_ai, instruction_decoder_1_alu_sel_1,
       instruction_decoder_1_alu_sel_2, instruction_decoder_1_alu_sel_3, instruction_decoder_1_ao,
       instruction_decoder_1_bi, instruction_decoder_1_bo, instruction_decoder_1_ce,
       instruction_decoder_1_ci, instruction_decoder_1_co, instruction_decoder_1_eo,
       instruction_decoder_1_fi, instruction_decoder_1_hlt, instruction_decoder_1_ii,
       instruction_decoder_1_ir, instruction_decoder_1_jp, instruction_decoder_1_mi,
       instruction_decoder_1_oi, instruction_decoder_1_rr, instruction_decoder_1_rw,
       instruction_decoder_1_s1, instruction_decoder_1_s2, instruction_decoder_1_s3,
       instruction_decoder_1_s4, instruction_decoder_1_s5, instruction_decoder_1_s6,
       instruction_decoder_1_s7, instruction_decoder_1_s8, n4_bit_register_1_s0, n4_bit_register_1_s1,
       n4_bit_register_1_s2, n4_bit_register_1_s3, n8_bit_7_segment_decoder_1_a1,
       n8_bit_7_segment_decoder_1_a2, n8_bit_7_segment_decoder_1_a3, n8_bit_7_segment_decoder_1_b1,
       n8_bit_7_segment_decoder_1_b2, n8_bit_7_segment_decoder_1_b3, n8_bit_7_segment_decoder_1_c1,
       n8_bit_7_segment_decoder_1_c2, n8_bit_7_segment_decoder_1_c3, n8_bit_7_segment_decoder_1_d1,
       n8_bit_7_segment_decoder_1_d2, n8_bit_7_segment_decoder_1_d3, n8_bit_7_segment_decoder_1_e1,
       n8_bit_7_segment_decoder_1_e2, n8_bit_7_segment_decoder_1_e3, n8_bit_7_segment_decoder_1_f1,
       n8_bit_7_segment_decoder_1_f2, n8_bit_7_segment_decoder_1_f3, n8_bit_7_segment_decoder_1_g1,
       n8_bit_7_segment_decoder_1_g2, n8_bit_7_segment_decoder_1_g3, n8_bit_alu_1_carry,
       n8_bit_alu_1_negative, n8_bit_alu_1_overflow, n8_bit_alu_1_s0, n8_bit_alu_1_s1_2, n8_bit_alu_1_s2_2,
       n8_bit_alu_1_s3_2, n8_bit_alu_1_s4, n8_bit_alu_1_s5, n8_bit_alu_1_s6, n8_bit_alu_1_s7,
       n8_bit_alu_1_zero, n8_bit_counter_1_d8, n8_bit_counter_1_s1, n8_bit_counter_1_s2, n8_bit_counter_1_s3,
       n8_bit_counter_1_s4, n8_bit_counter_1_s5, n8_bit_counter_1_s6, n8_bit_counter_1_s7,
       n8_bit_register_1_q0, n8_bit_register_1_q1, n8_bit_register_1_q2, n8_bit_register_1_q3,
       n8_bit_register_1_q4, n8_bit_register_1_q5, n8_bit_register_1_q6, n8_bit_register_1_q7,
       n8_bit_register_1_s0, n8_bit_register_1_s1, n8_bit_register_1_s2, n8_bit_register_1_s3,
       n8_bit_register_1_s4, n8_bit_register_1_s5, n8_bit_register_1_s6, n8_bit_register_1_s7,
       n8_bit_register_2_q0, n8_bit_register_2_q1, n8_bit_register_2_q2, n8_bit_register_2_q3,
       n8_bit_register_2_q4, n8_bit_register_2_s0, n8_bit_register_2_s1, n8_bit_register_2_s2,
       n8_bit_register_2_s3, n8_bit_register_2_s4, n8_bit_register_2_s5, n8_bit_register_2_s6,
       n8_bit_register_2_s7, n8_bit_register_3_s0, n8_bit_register_3_s1, n8_bit_register_3_s2,
       n8_bit_register_3_s3, n8_bit_register_3_s4, n8_bit_register_3_s5, n8_bit_register_3_s6,
       n8_bit_register_3_s7, n8_bit_register_4_q0, n8_bit_register_4_q1, n8_bit_register_4_q2,
       n8_bit_register_4_q3, n8_bit_register_4_q4, n8_bit_register_4_q5, n8_bit_register_4_q6,
       n8_bit_register_4_q7, n8_bit_register_5_s0, n8_bit_register_5_s1, n8_bit_register_5_s2,
       n8_bit_register_5_s3, n8_bit_register_5_s4, n8_bit_register_5_s5, n8_bit_register_5_s6,
       n8_bit_register_5_s7, n8_bit_reverser_1_q1, n8_bit_reverser_1_q2, n8_bit_reverser_1_q3,
       n8_bit_reverser_1_q4, n8_bit_reverser_1_q5, n8_bit_reverser_1_q6, n8_bit_reverser_1_q7,
       n8_bit_reverser_1_q8, or_1_out, or_2_out, program_loader_1_address_write, program_loader_1_data_write;
  wire [3:0] n4_bit_register_1_q0, n8_bit_register_4_s0, n8_bit_register_4_s4, n256_byte_sram_1_s1,
       n256_byte_sram_1_s5;
  wire [7:0] program_loader_1_rom_address, rom_1_data;

  _8_Bit_Register u_8_bit_register_1 (
    .Clock(and_1_out), .Load(instruction_decoder_1_ai), .Reset(Reset), .Enable(instruction_decoder_1_ao),
    .A0(n8_bit_register_1_q0), .A1(n8_bit_register_1_q1), .A2(n8_bit_register_1_q2),
    .A3(n8_bit_register_1_q3), .A4(n8_bit_register_1_q4), .A5(n8_bit_register_1_q5),
    .A6(n8_bit_register_1_q6), .A8(n8_bit_register_1_q7), .Q0(n8_bit_register_1_q0),
    .Q1(n8_bit_register_1_q1), .Q2(n8_bit_register_1_q2), .Q3(n8_bit_register_1_q3),
    .Q4(n8_bit_register_1_q4), .Q5(n8_bit_register_1_q5), .Q6(n8_bit_register_1_q6),
    .Q7(n8_bit_register_1_q7), .S7(n8_bit_register_1_s7), .S6(n8_bit_register_1_s6),
    .S5(n8_bit_register_1_s5), .S4(n8_bit_register_1_s4), .S3(n8_bit_register_1_s3),
    .S2(n8_bit_register_1_s2), .S1(n8_bit_register_1_s1), .S0(n8_bit_register_1_s0));
  DotMatrix #(.matrixcols(8), .matrixrows(1), .dotshape("circle")) dotmatrix_1 (
    .col0(n8_bit_register_1_s7), .col1(n8_bit_register_1_s6), .col2(n8_bit_register_1_s5),
    .col3(n8_bit_register_1_s4), .col4(n8_bit_register_1_s3), .col5(n8_bit_register_1_s2),
    .col6(n8_bit_register_1_s1), .col7(n8_bit_register_1_s0));
  LED led_1 (.in(instruction_decoder_1_ir));
  DotMatrix #(.matrixcols(8), .matrixrows(1), .dotshape("circle")) dotmatrix_2 (
    .col0(instruction_decoder_1_s8), .col1(instruction_decoder_1_s7), .col2(instruction_decoder_1_s6),
    .col3(instruction_decoder_1_s5), .col4(instruction_decoder_1_s4), .col5(instruction_decoder_1_s3),
    .col6(instruction_decoder_1_s2), .col7(instruction_decoder_1_s1));
  Instruction_Decoder instruction_decoder_1 (
    .NF(in_5), .VF(in_4), .ZF(n4_bit_register_1_q0[3]), .CF(n4_bit_register_1_q0[0]),
    .OP_0(n8_bit_register_2_q0), .OP_1(n8_bit_register_2_q1), .OP_2(n8_bit_register_2_q2),
    .OP_3(n8_bit_register_2_q3), .OP_4(n8_bit_register_2_q4), .Reset(Reset), .Clock(and_1_out),
    .FI(instruction_decoder_1_fi), .HLT(instruction_decoder_1_hlt), .AI(instruction_decoder_1_ai),
    .AO(instruction_decoder_1_ao), .ALU_SEL_3(instruction_decoder_1_alu_sel_3),
    .ALU_SEL_2(instruction_decoder_1_alu_sel_2), .ALU_SEL_1(instruction_decoder_1_alu_sel_1),
    .EO(instruction_decoder_1_eo), .CI(instruction_decoder_1_ci), .BI(instruction_decoder_1_bi),
    .BO(instruction_decoder_1_bo), .MI(instruction_decoder_1_mi), .RW(instruction_decoder_1_rw),
    .RR(instruction_decoder_1_rr), .II(instruction_decoder_1_ii), .IR(instruction_decoder_1_ir),
    .CE(instruction_decoder_1_ce), .CO(instruction_decoder_1_co), .JP(instruction_decoder_1_jp),
    .OI(instruction_decoder_1_oi), .S8(instruction_decoder_1_s8), .S7(instruction_decoder_1_s7),
    .S6(instruction_decoder_1_s6), .S5(instruction_decoder_1_s5), .S4(instruction_decoder_1_s4),
    .S3(instruction_decoder_1_s3), .S2(instruction_decoder_1_s2), .S1(instruction_decoder_1_s1), .PM(in_3));  // open: out_13, out_14
  DotMatrix #(.matrixcols(8), .matrixrows(1), .dotshape("circle")) dotmatrix_3 (
    .col0(n8_bit_reverser_1_q1), .col1(n8_bit_reverser_1_q2), .col2(n8_bit_reverser_1_q3),
    .col3(n8_bit_reverser_1_q4), .col4(n8_bit_reverser_1_q5), .col5(n8_bit_reverser_1_q6),
    .col6(n8_bit_reverser_1_q7), .col7(n8_bit_reverser_1_q8));
  DotMatrix #(.inputtype("row"), .matrixcols(1), .matrixrows(5), .dotshape("circle")) dotmatrix_4 (
    .row0(n8_bit_register_2_q4), .row1(n8_bit_register_2_q3), .row2(n8_bit_register_2_q2),
    .row3(n8_bit_register_2_q1), .row4(n8_bit_register_2_q0));
  _8_Bit_Reverser u_8_bit_reverser_1 (
    .A8(n8_bit_register_2_s7), .A7(n8_bit_register_2_s6), .A6(n8_bit_register_2_s5),
    .A5(n8_bit_register_2_s4), .A4(n8_bit_register_2_s3), .A3(n8_bit_register_2_s2),
    .A2(n8_bit_register_2_s1), .A1(n8_bit_register_2_s0), .Q8(n8_bit_reverser_1_q8),
    .Q7(n8_bit_reverser_1_q7), .Q6(n8_bit_reverser_1_q6), .Q5(n8_bit_reverser_1_q5),
    .Q4(n8_bit_reverser_1_q4), .Q3(n8_bit_reverser_1_q3), .Q2(n8_bit_reverser_1_q2), .Q1(n8_bit_reverser_1_q1));
  _8_Bit_Register u_8_bit_register_2 (
    .Clock(and_1_out), .Load(instruction_decoder_1_ii), .Reset(Reset), .Enable(1'b1),
    .A0(n8_bit_register_1_q0), .A1(n8_bit_register_1_q1), .A2(n8_bit_register_1_q2),
    .A3(n8_bit_register_1_q3), .A4(n8_bit_register_1_q4), .A5(n8_bit_register_1_q5),
    .A6(n8_bit_register_1_q6), .A8(n8_bit_register_1_q7), .Q0(n8_bit_register_2_q0),
    .Q1(n8_bit_register_2_q1), .Q2(n8_bit_register_2_q2), .Q3(n8_bit_register_2_q3),
    .Q4(n8_bit_register_2_q4), .S7(n8_bit_register_2_s7), .S6(n8_bit_register_2_s6),
    .S5(n8_bit_register_2_s5), .S4(n8_bit_register_2_s4), .S3(n8_bit_register_2_s3),
    .S2(n8_bit_register_2_s2), .S1(n8_bit_register_2_s1), .S0(n8_bit_register_2_s0));  // open: Q5, Q6, Q7
  _4_Bit_Register u_4_bit_register_1 (
    .A0(n8_bit_alu_1_carry), .A1(n8_bit_alu_1_overflow), .A2(n8_bit_alu_1_negative), .A3(n8_bit_alu_1_zero),
    .Clock(and_1_out), .Load(instruction_decoder_1_fi), .Reset(Reset), .S3(n4_bit_register_1_s3),
    .S2(n4_bit_register_1_s2), .S1(n4_bit_register_1_s1), .S0(n4_bit_register_1_s0), .Enable(1'b1),
    .Q0(n4_bit_register_1_q0[0]));  // open: Q1, Q2, Q3
  DotMatrix #(.matrixcols(4), .matrixrows(1), .dotshape("circle")) dotmatrix_5 (
    .col0(n4_bit_register_1_s3), .col1(n4_bit_register_1_s2), .col2(n4_bit_register_1_s1),
    .col3(n4_bit_register_1_s0));
  DotMatrix #(.matrixcols(8), .matrixrows(1), .dotshape("circle")) dotmatrix_6 (
    .col0(n8_bit_alu_1_s7), .col1(n8_bit_alu_1_s6), .col2(n8_bit_alu_1_s5), .col3(n8_bit_alu_1_s4),
    .col4(n8_bit_alu_1_s3_2), .col5(n8_bit_alu_1_s2_2), .col6(n8_bit_alu_1_s1_2), .col7(n8_bit_alu_1_s0));
  _8_Bit_ALU u_8_bit_alu_1 (
    .Alu_En(instruction_decoder_1_eo), .A0(n8_bit_register_1_s0), .A1(n8_bit_register_1_s1),
    .A2(n8_bit_register_1_s2), .A3(n8_bit_register_1_s3), .A4(n8_bit_register_1_s4),
    .A5(n8_bit_register_1_s5), .A6(n8_bit_register_1_s6), .A7(n8_bit_register_1_s7),
    .B0(n8_bit_register_3_s0), .Ci(instruction_decoder_1_ci), .B1(n8_bit_register_3_s1),
    .B2(n8_bit_register_3_s2), .B3(n8_bit_register_3_s3), .B4(n8_bit_register_3_s4),
    .B5(n8_bit_register_3_s5), .B6(n8_bit_register_3_s6), .B7(n8_bit_register_3_s7),
    .Q0(n8_bit_register_1_q0), .Q1(n8_bit_register_1_q1), .Q3(n8_bit_register_1_q3),
    .Q4(n8_bit_register_1_q4), .Q5(n8_bit_register_1_q5), .Q6(n8_bit_register_1_q6),
    .Q7(n8_bit_register_1_q7), .Carry(n8_bit_alu_1_carry), .Overflow(n8_bit_alu_1_overflow),
    .Negative(n8_bit_alu_1_negative), .Zero(n8_bit_alu_1_zero), .S3(instruction_decoder_1_alu_sel_1),
    .S2(instruction_decoder_1_alu_sel_2), .S1(instruction_decoder_1_alu_sel_3), .S7(n8_bit_alu_1_s7),
    .S6(n8_bit_alu_1_s6), .S5(n8_bit_alu_1_s5), .S4(n8_bit_alu_1_s4), .S3_2(n8_bit_alu_1_s3_2),
    .S2_2(n8_bit_alu_1_s2_2), .S1_2(n8_bit_alu_1_s1_2), .S0(n8_bit_alu_1_s0), .Q2(n8_bit_register_1_q2));
  _8_Bit_Register u_8_bit_register_3 (
    .Clock(and_1_out), .Load(instruction_decoder_1_bi), .Reset(Reset), .Enable(instruction_decoder_1_bo),
    .A0(n8_bit_register_1_q0), .A1(n8_bit_register_1_q1), .A2(n8_bit_register_1_q2),
    .A3(n8_bit_register_1_q3), .A4(n8_bit_register_1_q4), .A5(n8_bit_register_1_q5),
    .A6(n8_bit_register_1_q6), .A8(n8_bit_register_1_q7), .Q0(n8_bit_register_1_q0),
    .Q1(n8_bit_register_1_q1), .Q2(n8_bit_register_1_q2), .Q3(n8_bit_register_1_q3),
    .Q4(n8_bit_register_1_q4), .Q5(n8_bit_register_1_q5), .Q6(n8_bit_register_1_q6),
    .Q7(n8_bit_register_1_q7), .S7(n8_bit_register_3_s7), .S6(n8_bit_register_3_s6),
    .S5(n8_bit_register_3_s5), .S4(n8_bit_register_3_s4), .S3(n8_bit_register_3_s3),
    .S2(n8_bit_register_3_s2), .S1(n8_bit_register_3_s1), .S0(n8_bit_register_3_s0));
  DotMatrix #(.matrixcols(8), .matrixrows(1), .dotshape("circle")) dotmatrix_7 (
    .col0(n8_bit_register_3_s7), .col1(n8_bit_register_3_s6), .col2(n8_bit_register_3_s5),
    .col3(n8_bit_register_3_s4), .col4(n8_bit_register_3_s3), .col5(n8_bit_register_3_s2),
    .col6(n8_bit_register_3_s1), .col7(n8_bit_register_3_s0));
  DotMatrix #(.matrixcols(8), .matrixrows(1), .dotshape("circle")) dotmatrix_8 (
    .col0(n8_bit_counter_1_d8), .col1(n8_bit_counter_1_s7), .col2(n8_bit_counter_1_s6),
    .col3(n8_bit_counter_1_s5), .col4(n8_bit_counter_1_s4), .col5(n8_bit_counter_1_s3),
    .col6(n8_bit_counter_1_s2), .col7(n8_bit_counter_1_s1));
  _8_Bit_Counter u_8_bit_counter_1 (
    .Enable_Out(instruction_decoder_1_co), .Enable(instruction_decoder_1_ce), .Reset(Reset),
    .Write(instruction_decoder_1_jp), .Clock(and_1_out), .Q8(n8_bit_register_1_q7),
    .Q7(n8_bit_register_1_q6), .Q6(n8_bit_register_1_q5), .Q5(n8_bit_register_1_q4),
    .Q4(n8_bit_register_1_q3), .Q3(n8_bit_register_1_q2), .Q2(n8_bit_register_1_q1),
    .Q1(n8_bit_register_1_q0), .D8(n8_bit_counter_1_d8), .S7(n8_bit_counter_1_s7), .S6(n8_bit_counter_1_s6),
    .S5(n8_bit_counter_1_s5), .S4(n8_bit_counter_1_s4), .S3(n8_bit_counter_1_s3), .S2(n8_bit_counter_1_s2),
    .S1(n8_bit_counter_1_s1), .A8(n8_bit_register_1_q7), .A7(n8_bit_register_1_q6),
    .A6(n8_bit_register_1_q5), .A5(n8_bit_register_1_q4), .A4(n8_bit_register_1_q3),
    .A3(n8_bit_register_1_q2), .A2(n8_bit_register_1_q1), .A1(n8_bit_register_1_q0));
  _8_Bit_Register u_8_bit_register_4 (
    .Clock(and_1_out), .Load(or_1_out), .Reset(Reset), .Enable(1'b1), .A0(n8_bit_register_1_q0),
    .A1(n8_bit_register_1_q1), .A2(n8_bit_register_1_q2), .A3(n8_bit_register_1_q3),
    .A4(n8_bit_register_1_q4), .A5(n8_bit_register_1_q5), .A6(n8_bit_register_1_q6),
    .A8(n8_bit_register_1_q7), .Q0(n8_bit_register_4_q0), .Q1(n8_bit_register_4_q1),
    .Q2(n8_bit_register_4_q2), .Q3(n8_bit_register_4_q3), .Q4(n8_bit_register_4_q4),
    .Q5(n8_bit_register_4_q5), .Q6(n8_bit_register_4_q6), .Q7(n8_bit_register_4_q7),
    .S7(n8_bit_register_4_s4[3]), .S6(n8_bit_register_4_s4[2]), .S5(n8_bit_register_4_s4[1]),
    .S4(n8_bit_register_4_s4[0]), .S3(n8_bit_register_4_s0[3]), .S2(n8_bit_register_4_s0[2]),
    .S1(n8_bit_register_4_s0[1]), .S0(n8_bit_register_4_s0[0]));
  DotMatrix #(.matrixcols(8), .matrixrows(1), .dotshape("circle")) dotmatrix_9 (
    .col0(n8_bit_register_4_s4[3]), .col1(n8_bit_register_4_s4[2]), .col2(n8_bit_register_4_s4[1]),
    .col3(n8_bit_register_4_s4[0]), .col4(n8_bit_register_4_s0[3]), .col5(n8_bit_register_4_s0[2]),
    .col6(n8_bit_register_4_s0[1]), .col7(n8_bit_register_4_s0[0]));
  Hex_Digit_Display hex_digit_display_1 (.value(n8_bit_register_4_s4));  // open: dp
  or or_1 (or_1_out, instruction_decoder_1_mi, program_loader_1_address_write);
  Hex_Digit_Display hex_digit_display_2 (.value(n8_bit_register_4_s0));  // open: dp
  _8_Bit_Register u_8_bit_register_5 (
    .Clock(and_1_out), .Load(instruction_decoder_1_oi), .Reset(Reset), .Enable(1'b1),
    .A0(n8_bit_register_1_q0), .A1(n8_bit_register_1_q1), .A2(n8_bit_register_1_q2),
    .A3(n8_bit_register_1_q3), .A4(n8_bit_register_1_q4), .A5(n8_bit_register_1_q5),
    .A6(n8_bit_register_1_q6), .A8(n8_bit_register_1_q7), .S7(n8_bit_register_5_s7),
    .S6(n8_bit_register_5_s6), .S5(n8_bit_register_5_s5), .S4(n8_bit_register_5_s4),
    .S3(n8_bit_register_5_s3), .S2(n8_bit_register_5_s2), .S1(n8_bit_register_5_s1), .S0(n8_bit_register_5_s0));  // open: Q0, Q1, Q2, Q3, Q4, Q5, Q6, Q7
  _7_Segment_Display u_7_segment_display_1 (
    .g(n8_bit_7_segment_decoder_1_g3), .f(n8_bit_7_segment_decoder_1_f3), .a(n8_bit_7_segment_decoder_1_a3),
    .b(n8_bit_7_segment_decoder_1_b3), .e(n8_bit_7_segment_decoder_1_e3), .d(n8_bit_7_segment_decoder_1_d3),
    .c(n8_bit_7_segment_decoder_1_c3));  // open: dp
  Hex_Digit_Display hex_digit_display_3 (.value(n256_byte_sram_1_s5));  // open: dp
  DotMatrix #(.matrixcols(8), .matrixrows(1), .dotshape("circle")) dotmatrix_10 (
    .col0(n256_byte_sram_1_s5[3]), .col1(n256_byte_sram_1_s5[2]), .col2(n256_byte_sram_1_s5[1]),
    .col3(n256_byte_sram_1_s5[0]), .col4(n256_byte_sram_1_s1[3]), .col5(n256_byte_sram_1_s1[2]),
    .col6(n256_byte_sram_1_s1[1]), .col7(n256_byte_sram_1_s1[0]));
  _256_Byte_SRAM u_256_byte_sram_1 (
    .Read(instruction_decoder_1_rr), .Write(or_2_out), .Clear(Reset_RAM), .Clock(and_1_out),
    .A1_2(n8_bit_register_4_q0), .A2_2(n8_bit_register_4_q1), .A3_2(n8_bit_register_4_q2),
    .A4_2(n8_bit_register_4_q3), .A5_2(n8_bit_register_4_q4), .A6_2(n8_bit_register_4_q5),
    .A7_2(n8_bit_register_4_q6), .A8_2(n8_bit_register_4_q7), .S8(n256_byte_sram_1_s5[3]),
    .S7(n256_byte_sram_1_s5[2]), .S6(n256_byte_sram_1_s5[1]), .S5(n256_byte_sram_1_s5[0]),
    .S4(n256_byte_sram_1_s1[3]), .S3(n256_byte_sram_1_s1[2]), .S2(n256_byte_sram_1_s1[1]),
    .S1(n256_byte_sram_1_s1[0]), .Q8(n8_bit_register_1_q7), .Q7(n8_bit_register_1_q6),
    .Q6(n8_bit_register_1_q5), .Q5(n8_bit_register_1_q4), .Q4(n8_bit_register_1_q3),
    .Q3(n8_bit_register_1_q2), .Q2(n8_bit_register_1_q1), .Q1(n8_bit_register_1_q0),
    .A8(n8_bit_register_1_q7), .A7(n8_bit_register_1_q6), .A6(n8_bit_register_1_q5),
    .A5(n8_bit_register_1_q4), .A4(n8_bit_register_1_q3), .A3(n8_bit_register_1_q2),
    .A2(n8_bit_register_1_q1), .A1(n8_bit_register_1_q0));
  _8_Bit_7_segment_decoder u_8_bit_7_segment_decoder_1 (
    .in_1(n8_bit_register_5_s0), .in_2(n8_bit_register_5_s1), .in_3(n8_bit_register_5_s2),
    .in_4(n8_bit_register_5_s3), .in_5(n8_bit_register_5_s4), .in_6(n8_bit_register_5_s5),
    .in_7(n8_bit_register_5_s6), .in_8(n8_bit_register_5_s7), .A1(n8_bit_7_segment_decoder_1_a1),
    .B1(n8_bit_7_segment_decoder_1_b1), .C1(n8_bit_7_segment_decoder_1_c1),
    .D1(n8_bit_7_segment_decoder_1_d1), .E1(n8_bit_7_segment_decoder_1_e1),
    .F1(n8_bit_7_segment_decoder_1_f1), .G1(n8_bit_7_segment_decoder_1_g1),
    .A2(n8_bit_7_segment_decoder_1_a2), .B2(n8_bit_7_segment_decoder_1_b2),
    .C2(n8_bit_7_segment_decoder_1_c2), .D2(n8_bit_7_segment_decoder_1_d2),
    .E2(n8_bit_7_segment_decoder_1_e2), .F2(n8_bit_7_segment_decoder_1_f2),
    .G2(n8_bit_7_segment_decoder_1_g2), .A3(n8_bit_7_segment_decoder_1_a3),
    .B3(n8_bit_7_segment_decoder_1_b3), .C3(n8_bit_7_segment_decoder_1_c3),
    .D3(n8_bit_7_segment_decoder_1_d3), .E3(n8_bit_7_segment_decoder_1_e3),
    .F3(n8_bit_7_segment_decoder_1_f3), .G3(n8_bit_7_segment_decoder_1_g3));
  _7_Segment_Display u_7_segment_display_2 (
    .g(n8_bit_7_segment_decoder_1_g2), .f(n8_bit_7_segment_decoder_1_f2), .a(n8_bit_7_segment_decoder_1_a2),
    .b(n8_bit_7_segment_decoder_1_b2), .e(n8_bit_7_segment_decoder_1_e2), .d(n8_bit_7_segment_decoder_1_d2),
    .c(n8_bit_7_segment_decoder_1_c2));  // open: dp
  _7_Segment_Display u_7_segment_display_3 (
    .g(n8_bit_7_segment_decoder_1_g1), .f(n8_bit_7_segment_decoder_1_f1), .a(n8_bit_7_segment_decoder_1_a1),
    .b(n8_bit_7_segment_decoder_1_b1), .e(n8_bit_7_segment_decoder_1_e1), .d(n8_bit_7_segment_decoder_1_d1),
    .c(n8_bit_7_segment_decoder_1_c1));  // open: dp
  Hex_Digit_Display hex_digit_display_4 (.value(n256_byte_sram_1_s1));  // open: dp
  or or_2 (or_2_out, instruction_decoder_1_rw, program_loader_1_data_write);
  DotMatrix #(.inputtype("row"), .matrixcols(1), .matrixrows(8), .dotshape("circle")) dotmatrix_11 (
    .row0(n8_bit_register_1_q0), .row1(n8_bit_register_1_q1), .row2(n8_bit_register_1_q2),
    .row3(n8_bit_register_1_q3), .row4(n8_bit_register_1_q4), .row5(n8_bit_register_1_q5),
    .row6(n8_bit_register_1_q6), .row7(n8_bit_register_1_q7));
  Program_Loader program_loader_1 (
    .Q1(n8_bit_register_1_q0), .Q2(n8_bit_register_1_q1), .Q3(n8_bit_register_1_q2),
    .Q4(n8_bit_register_1_q3), .Q5(n8_bit_register_1_q4), .Q6(n8_bit_register_1_q5),
    .Q7(n8_bit_register_1_q6), .Q8(n8_bit_register_1_q7), .Programming(Programming),
    .Address_Write(program_loader_1_address_write), .Data_Write(program_loader_1_data_write), .Enable(in_3),
    .Reset(Reset), .ROM_Address(program_loader_1_rom_address), .ROM_Data(rom_1_data), .Clock(and_1_out));
  ROM rom_1 (.addr(program_loader_1_rom_address), .data(rom_1_data));  // open: sel
  Clock clock_1 (.out(clock_1_out));
  and and_1 (and_1_out, ~Reset, clock_1_out, ~instruction_decoder_1_hlt);  // AND_Gate
  // Pins of 1 and 4 bits meet at n4_bit_register_1_q0

  // Notes on the sheet:
  //   Register A
  //   Instruction
  //   Register
  //   Flags
  //   Register
  //   Register B
  //   PC
  //   Register
  //   Memory
  //   Register
  //   Out
  //   Register
  //   Ram
  //   program rom
  //   contents of rom_1 (hex, n*v repeats v):
  //   2 55 4 23 17 23
endmodule
